// Digital circuit 6502.dig as structural Verilog
module _6502 (
  input  clk
);

  wire clk_t, clock_1_c0, clock_1_c1, clock_1_c2, clock_1_c3, Decode, DecodeFlag, DecodeHigh, Execute,
       ExecuteFlag, Fetch, FetchFlag, HighFlag, Itterate, MRead, MWrite, or_1_out, or_2_out, PCWrite;
  wire [7:0] driver_2_out, driver_3_out, driver_4_out, ramsingleport_1_d, register_1_q, register_2_q,
       register_3_q;
  wire [15:0] driver_1_out, PCInstOut, program_counter_1_output;

  assign driver_1_out = PCWrite ? PCInstOut : 16'bz;  // Driver driver_1
  clock clock_1 (.ClockIn(clk), .C3(clock_1_c3), .C2(clock_1_c2), .C1(clock_1_c1), .C0(clock_1_c0), .Clock(clk_t));
  Program_Counter program_counter_1 (
    .Input(driver_1_out), .ClockIn(clk_t), .OverWriteIn(PCWrite), .ItterateIn(Itterate),
    .Output(program_counter_1_output));
  Register #(.Bits(8)) register_1 (.D(driver_2_out), .C(clk_t), .en(Fetch), .Q(register_1_q));
  assign driver_1_out = ~PCWrite ? program_counter_1_output : 16'bz;  // DriverInvSel driverinvsel_1
  assign driver_2_out[0] = Fetch ? ramsingleport_1_d[0] : 1'bz;  // Driver driver_2
  Register #(.Bits(8)) register_2 (.D(driver_3_out), .C(clk_t), .en(Decode), .Q(register_2_q));
  assign driver_3_out[0] = Decode ? ramsingleport_1_d[0] : 1'bz;  // Driver driver_3
  and and_1 (Execute, clock_1_c3, ExecuteFlag);
  and and_2 (DecodeHigh, clock_1_c2, HighFlag);
  and and_3 (Decode, clock_1_c1, DecodeFlag);
  and and_4 (Fetch, clock_1_c0, FetchFlag);
  or or_1 (or_1_out, Itterate, MRead);
  or or_2 (or_2_out, MWrite, or_1_out);
  Register #(.Bits(8)) register_3 (.D(driver_4_out), .C(clk_t), .en(DecodeHigh), .Q(register_3_q));
  RAMSinglePort #(.AddrBits(16), .Bits(8)) ramsingleport_1 (
    .A(program_counter_1_output), .str(MWrite), .C(or_2_out), .ld(or_1_out), .D(ramsingleport_1_d));
  assign driver_4_out[0] = DecodeHigh ? ramsingleport_1_d[0] : 1'bz;  // Driver driver_4
  or or_3 (Itterate, DecodeHigh, Decode, Fetch);
  // Pins of 1 and 8 bits meet at ramsingleport_1_d
  // Pins of 1 and 8 bits meet at driver_2_out
  // Pins of 1 and 8 bits meet at driver_3_out
  // Pins of 1 and 8 bits meet at driver_4_out
endmodule
