// Digital circuit Program Counter.dig as structural Verilog
module Program_Counter (
  input  [15:0] Input,
  input  ClockIn,
  input  OverWriteIn,
  input  ItterateIn,
  output [15:0] Output
);

  wire or_1_out;
  wire [15:0] add_1_s, driver_1_out;

  Add #(.Bits(16)) add_1 (.a(Output), .b(16'h1), .c_i(1'b0), .s(add_1_s));  // open: c_o
  assign driver_1_out = ItterateIn ? add_1_s : 16'bz;  // Driver driver_1
  assign driver_1_out = OverWriteIn ? Input : 16'bz;  // Driver driver_2
  or or_1 (or_1_out, OverWriteIn, ItterateIn);
  Register #(.Bits(16)) register_1 (.D(driver_1_out), .C(~ClockIn), .en(or_1_out), .Q(Output));
endmodule
