// Digital circuit Retreive.dig as structural Verilog
module Retreive (
  input  [7:0] LowByte,
  input  [7:0] X,
  input  [7:0] Y,
  input  [7:0] HighByte,
  input  Clock,
  input  Reset,
  input  [11:0] AddressInput,
  input  DecodeHigh,
  output ExecuteFlag,
  output DecodeFlag,
  output HighByteFlag,
  output PCOFFflag,
  output [15:0] NextAddress
);

  wire and_1_out, and_2_out, and_4_out, and_5_out, d_ff_as_1_q, d_ff_as_3_q, d_ff_as_4_q, Itter1, not_1_out,
       not_3_out, not_4_out, not_5_out, notconnected_1_out, notconnected_2_out, notconnected_3_out,
       notconnected_4_out, notconnected_5_out, notconnected_6_out, or_1_out, or_3_out, or_4_out, or_5_out,
       or_6_out, or_7_out, or_8_out, or_9_out, or_10_out, or_11_out, or_12_out, or_13_out, or_14_out,
       or_15_out, or_16_out, or_17_out, or_18_out, or_19_out, or_20_out, or_21_out, or_22_out;
  wire [7:0] add_1_s, add_2_s, add_3_s, add_4_s, add_5_s, add_6_s, driverinvsel_1_out, driverinvsel_2_out,
       driverinvsel_3_out, driverinvsel_4_out;

  or or_1 (or_1_out, AddressInput[11], AddressInput[10], AddressInput[9], AddressInput[8], AddressInput[7], AddressInput[6], AddressInput[5], AddressInput[4], AddressInput[2], AddressInput[1], AddressInput[0]);
  not not_1 (not_1_out, or_1_out);
  or or_2 (ExecuteFlag, not_1_out, d_ff_as_1_q);
  not not_2 (DecodeFlag, ExecuteFlag);
  or or_3 (or_3_out, AddressInput[11], AddressInput[10]);
  assign NextAddress[7:0] = AddressInput[7] ? LowByte : 8'bz;  // Driver driver_1
  assign NextAddress[15:8] = AddressInput[7] ? {8{1'b0}} : 8'bz;  // Driver driver_2
  or or_4 (or_4_out, or_3_out, Itter1);
  Add #(.Bits(8)) add_1 (.a(LowByte), .b(X), .c_i(notconnected_1_out), .s(add_1_s));  // open: c_o
  // NotConnected on notconnected_1_out
  D_FF_AS d_ff_as_1 (.Set(1'b0), .D(or_4_out), .C(~Clock), .Clr(Reset), .Q(d_ff_as_1_q));  // open: nQ
  assign NextAddress[7:0] = AddressInput[6] ? add_1_s : 8'bz;  // Driver driver_3
  Add #(.Bits(8)) add_2 (.a(LowByte), .b(Y), .c_i(notconnected_2_out), .s(add_2_s));  // open: c_o
  // NotConnected on notconnected_2_out
  assign NextAddress[15:8] = AddressInput[6] ? {8{1'b0}} : 8'bz;  // Driver driver_4
  or or_5 (or_5_out, AddressInput[7], AddressInput[6]);
  assign NextAddress[7:0] = AddressInput[5] ? add_2_s : 8'bz;  // Driver driver_5
  assign NextAddress[15:8] = AddressInput[5] ? {8{1'b0}} : 8'bz;  // Driver driver_6
  or or_6 (or_6_out, or_5_out, AddressInput[5]);
  assign NextAddress[7:0] = AddressInput[1] ? LowByte : 8'bz;  // Driver driver_7
  assign NextAddress[15:8] = AddressInput[1] ? HighByte : 8'bz;  // Driver driver_8
  or or_7 (or_7_out, or_6_out, AddressInput[1]);
  Add #(.Bits(8)) add_3 (.a(LowByte), .b(X), .c_i(notconnected_3_out), .s(add_3_s));  // open: c_o
  // NotConnected on notconnected_3_out
  assign NextAddress[7:0] = AddressInput[0] ? add_3_s : 8'bz;  // Driver driver_9
  assign NextAddress[15:8] = AddressInput[0] ? HighByte : 8'bz;  // Driver driver_10
  Add #(.Bits(8)) add_4 (.a(LowByte), .b(Y), .c_i(notconnected_4_out), .s(add_4_s));  // open: c_o
  // NotConnected on notconnected_4_out
  or or_8 (or_8_out, AddressInput[1], AddressInput[0]);
  or or_9 (or_9_out, AddressInput[1], AddressInput[0]);
  or or_10 (or_10_out, or_7_out, AddressInput[0]);
  assign NextAddress[7:0] = AddressInput[4] ? add_4_s : 8'bz;  // Driver driver_11
  assign NextAddress[15:8] = AddressInput[4] ? HighByte : 8'bz;  // Driver driver_12
  or or_11 (or_11_out, or_8_out, AddressInput[4]);
  or or_12 (or_12_out, or_9_out, AddressInput[4]);
  or or_13 (or_13_out, or_10_out, AddressInput[4]);
  or or_14 (or_14_out, or_13_out, d_ff_as_3_q);
  assign NextAddress[7:0] = AddressInput[2] ? LowByte : 8'bz;  // Driver driver_13
  assign NextAddress[15:8] = AddressInput[2] ? HighByte : 8'bz;  // Driver driver_14
  or or_15 (or_15_out, or_11_out, AddressInput[2]);
  or or_16 (or_16_out, or_12_out, AddressInput[2]);
  D_FF_AS d_ff_as_2 (.Set(1'b0), .D(or_14_out), .C(~Clock), .Clr(Reset), .Q(Itter1));  // open: nQ
  not not_3 (not_3_out, Itter1);
  assign driverinvsel_1_out = ~not_3_out ? {8{1'b0}} : 8'bz;  // DriverInvSel driverinvsel_1
  assign driverinvsel_2_out = ~Itter1 ? {8{1'b0}} : 8'bz;  // DriverInvSel driverinvsel_2
  assign driverinvsel_1_out = not_3_out ? X : 8'bz;  // Driver driver_15
  and and_1 (and_1_out, AddressInput[9], Itter1);
  assign driverinvsel_2_out = Itter1 ? HighByte : 8'bz;  // Driver driver_16
  Add #(.Bits(8)) add_5 (.a(LowByte), .b(driverinvsel_1_out), .c_i(notconnected_5_out), .s(add_5_s));  // open: c_o
  // NotConnected on notconnected_5_out
  or or_17 (or_17_out, and_1_out, or_16_out);
  assign NextAddress[7:0] = AddressInput[9] ? add_5_s : 8'bz;  // Driver driver_17
  assign NextAddress[15:8] = AddressInput[9] ? driverinvsel_2_out : 8'bz;  // Driver driver_18
  or or_18 (or_18_out, AddressInput[2], AddressInput[9]);
  assign driverinvsel_3_out = ~Itter1 ? {8{1'b0}} : 8'bz;  // DriverInvSel driverinvsel_3
  assign driverinvsel_4_out = ~Itter1 ? {8{1'b0}} : 8'bz;  // DriverInvSel driverinvsel_4
  assign driverinvsel_3_out = Itter1 ? Y : 8'bz;  // Driver driver_19
  and and_2 (and_2_out, AddressInput[8], Itter1);
  assign driverinvsel_4_out = Itter1 ? HighByte : 8'bz;  // Driver driver_20
  Add #(.Bits(8)) add_6 (.a(LowByte), .b(driverinvsel_3_out), .c_i(notconnected_6_out), .s(add_6_s));  // open: c_o
  // NotConnected on notconnected_6_out
  or or_19 (or_19_out, and_2_out, or_17_out);
  and and_3 (HighByteFlag, DecodeFlag, or_19_out);
  assign NextAddress[7:0] = AddressInput[8] ? add_6_s : 8'bz;  // Driver driver_21
  assign NextAddress[15:8] = AddressInput[8] ? driverinvsel_4_out : 8'bz;  // Driver driver_22
  or or_20 (or_20_out, or_18_out, AddressInput[8]);
  D_FF_AS d_ff_as_3 (.Set(1'b0), .D(or_20_out), .C(~Clock), .Clr(Reset), .Q(d_ff_as_3_q));  // open: nQ
  or or_21 (or_21_out, Itter1, d_ff_as_3_q);
  not not_4 (not_4_out, ExecuteFlag);
  not not_5 (not_5_out, or_15_out);
  and and_4 (and_4_out, or_21_out, not_5_out);
  and and_5 (and_5_out, d_ff_as_4_q, or_15_out);
  D_FF_AS d_ff_as_4 (.Set(1'b0), .D(or_15_out), .C(~DecodeHigh), .Clr(Clock), .Q(d_ff_as_4_q));  // open: nQ
  or or_22 (or_22_out, and_4_out, and_5_out);
  and and_6 (PCOFFflag, not_4_out, or_22_out);
endmodule
