// Digital circuit clock.dig as structural Verilog
module clock (
  input  ClockIn,
  output C3,
  output C2,
  output C1,
  output C0,
  output Clock
);

  wire d_ff_1_q, d_ff_2_q, d_ff_3_q, d_ff_4_q, nor_1_out;

  nor nor_1 (nor_1_out, d_ff_4_q, d_ff_3_q, d_ff_2_q, d_ff_1_q);
  D_FF d_ff_1 (.D(d_ff_2_q), .C(~ClockIn), .Q(d_ff_1_q));  // open: nQ
  D_FF d_ff_2 (.D(d_ff_3_q), .C(~ClockIn), .Q(d_ff_2_q));  // open: nQ
  D_FF d_ff_3 (.D(d_ff_4_q), .C(~ClockIn), .Q(d_ff_3_q));  // open: nQ
  D_FF d_ff_4 (.D(nor_1_out), .C(~ClockIn), .Q(d_ff_4_q));  // open: nQ
  and and_1 (C3, ClockIn, d_ff_1_q);
  and and_2 (C2, ClockIn, d_ff_2_q);
  and and_3 (C1, ClockIn, d_ff_3_q);
  and and_4 (C0, ClockIn, d_ff_4_q);

  assign Clock = ClockIn;
endmodule
