// Digital circuit decoder.dig as structural Verilog
module decoder (
  input  [7:0] INPUT,
  output BRK,
  output BPL,
  output JSR,
  output BMI,
  output RTI,
  output BVC,
  output RTS,
  output BVS,
  output BCC,
  output BCS,
  output BNE,
  output BEQ,
  output rel,
  output Xind,
  output IndY,
  output hash,
  output zpg,
  output zpgX,
  output PHP,
  output CLC,
  output PLP,
  output SEC,
  output PHA,
  output CLI,
  output PLA,
  output SEI,
  output DEY,
  output TYA,
  output TAY,
  output CLV,
  output INY,
  output CLD,
  output INX,
  output SED,
  output zpgY,
  output DEX,
  output TSX,
  output TAX,
  output TXS,
  output TXA,
  output JMP,
  output ind,
  output CPX,
  output SBC,
  output INC,
  output CPY,
  output CMP,
  output DEC,
  output LDY,
  output LDA,
  output LDX,
  output STY,
  output STA,
  output STX,
  output ADC,
  output ROR,
  output EOR,
  output LSR,
  output AND,
  output ROL,
  output ORA,
  output ASL,
  output absX,
  output abs,
  output A,
  output absY
);

  wire and_10_out, and_12_out, and_14_out, and_16_out, and_17_out, and_18_out, and_19_out, and_20_out,
       and_21_out, and_22_out, and_23_out, and_24_out, and_25_out, and_26_out, and_27_out, and_28_out,
       and_29_out, and_30_out, and_31_out, and_32_out, and_33_out, and_34_out, and_35_out, and_36_out,
       and_37_out, and_38_out, and_39_out, and_40_out, and_41_out, and_42_out, and_43_out, and_44_out,
       and_45_out, and_46_out, and_47_out, and_48_out, and_49_out, and_50_out, and_51_out, and_52_out,
       and_53_out, and_54_out, and_55_out, and_56_out, and_57_out, and_58_out, and_59_out, and_60_out,
       and_61_out, and_62_out, and_63_out, and_64_out, and_65_out, and_66_out, and_67_out, and_68_out,
       and_69_out, and_70_out, and_87_out, and_88_out, and_89_out, and_90_out, and_91_out, and_92_out,
       and_93_out, and_94_out, and_95_out, and_96_out, and_97_out, and_98_out, and_99_out, and_100_out,
       and_101_out, and_102_out, and_103_out, and_104_out, and_105_out, and_111_out, and_113_out,
       and_114_out, and_116_out, and_117_out, and_118_out, and_119_out, and_120_out, and_121_out,
       and_122_out, and_123_out, and_124_out, and_125_out, and_126_out, and_127_out, and_128_out,
       and_129_out, and_130_out, and_131_out, and_132_out, and_133_out, and_134_out, and_135_out,
       and_136_out, and_137_out, and_138_out, and_139_out, and_140_out, and_141_out, and_142_out,
       and_143_out, and_145_out, and_146_out, and_147_out, and_148_out, decoder_1_out_0, decoder_1_out_1,
       decoder_1_out_2, decoder_1_out_3, decoder_1_out_4, decoder_1_out_5, decoder_1_out_6, decoder_1_out_7,
       decoder_1_out_8, decoder_1_out_9, decoder_1_out_10, decoder_1_out_11, decoder_1_out_12,
       decoder_1_out_13, decoder_1_out_14, decoder_1_out_15, decoder_2_out_1, decoder_2_out_2,
       decoder_2_out_3, decoder_2_out_5, decoder_2_out_6, decoder_2_out_7, decoder_2_out_9, decoder_2_out_10,
       decoder_2_out_11, decoder_2_out_13, decoder_2_out_14, decoder_2_out_15, LDXABSY, LDYABSX, or_1_out,
       or_2_out, or_3_out, or_4_out, or_5_out, or_7_out, or_8_out, or_9_out, or_10_out, or_12_out, or_13_out,
       or_14_out, or_15_out, or_16_out, or_17_out, or_19_out, or_20_out, or_21_out, or_22_out, or_23_out,
       or_24_out, or_25_out, or_26_out, or_27_out, or_28_out, or_29_out, or_30_out, or_31_out, or_32_out,
       or_34_out, or_35_out, or_36_out, or_38_out, or_39_out, or_40_out, or_41_out, or_42_out, or_44_out,
       or_45_out, or_46_out, or_47_out, or_48_out, or_49_out, or_50_out, or_51_out, or_52_out, or_53_out,
       or_54_out, or_55_out, or_56_out, or_57_out, or_58_out, or_59_out, or_60_out, or_61_out, or_62_out,
       or_63_out, or_64_out, or_65_out, or_66_out, or_67_out, or_68_out, or_69_out, or_70_out, or_71_out,
       or_72_out, or_73_out, or_74_out, or_75_out, or_76_out, or_77_out, or_78_out, or_79_out, or_80_out,
       or_81_out, or_82_out, or_83_out, or_84_out, or_85_out, or_86_out, or_88_out, or_89_out, or_90_out,
       or_91_out, or_92_out, or_93_out, or_94_out, or_95_out, or_96_out, or_97_out, or_98_out, or_99_out,
       or_100_out, or_101_out, or_102_out, or_103_out, or_104_out, or_105_out, or_106_out, or_107_out,
       or_108_out, or_109_out, or_110_out, or_111_out, or_112_out, or_113_out, or_114_out, or_115_out,
       or_116_out, or_117_out, or_118_out, or_119_out, or_121_out, or_122_out, or_123_out, or_124_out,
       or_125_out, or_126_out, or_127_out, or_128_out, or_129_out, or_130_out, or_131_out, or_132_out,
       or_134_out, or_136_out, or_137_out, or_138_out, or_139_out, or_140_out, or_141_out, or_147_out,
       or_148_out, or_149_out, or_150_out, or_151_out, or_152_out, or_153_out, or_154_out, or_155_out,
       or_156_out, or_157_out, or_158_out, or_159_out, or_160_out, or_161_out, or_162_out, or_163_out,
       or_164_out, or_165_out, or_166_out, or_167_out, or_168_out, or_169_out, or_178_out, or_180_out,
       or_181_out, or_182_out, or_183_out, or_184_out, or_185_out, or_186_out, or_187_out, or_188_out,
       or_189_out, or_190_out, or_191_out, or_192_out, or_193_out, or_195_out, or_196_out, or_197_out,
       or_198_out, or_199_out;

  Decoder #(.Selector_Bits(4)) decoder_1 (
    .sel(INPUT[7:4]), .out_0(decoder_1_out_0), .out_1(decoder_1_out_1), .out_2(decoder_1_out_2),
    .out_3(decoder_1_out_3), .out_4(decoder_1_out_4), .out_5(decoder_1_out_5), .out_6(decoder_1_out_6),
    .out_7(decoder_1_out_7), .out_8(decoder_1_out_8), .out_9(decoder_1_out_9), .out_10(decoder_1_out_10),
    .out_11(decoder_1_out_11), .out_12(decoder_1_out_12), .out_13(decoder_1_out_13),
    .out_14(decoder_1_out_14), .out_15(decoder_1_out_15));
  and and_1 (BRK, decoder_2_out_15, decoder_1_out_0);
  and and_2 (BPL, decoder_2_out_15, decoder_1_out_1);
  and and_3 (JSR, decoder_2_out_15, decoder_1_out_2);
  and and_4 (BMI, decoder_2_out_15, decoder_1_out_3);
  and and_5 (RTI, decoder_2_out_15, decoder_1_out_4);
  and and_6 (BVC, decoder_2_out_15, decoder_1_out_5);
  and and_7 (RTS, decoder_2_out_15, decoder_1_out_6);
  and and_8 (BVS, decoder_2_out_15, decoder_1_out_7);
  and and_9 (BCC, decoder_2_out_15, decoder_1_out_9);
  and and_10 (and_10_out, decoder_2_out_15, decoder_1_out_10);
  and and_11 (BCS, decoder_2_out_15, decoder_1_out_11);
  and and_12 (and_12_out, decoder_2_out_15, decoder_1_out_12);
  and and_13 (BNE, decoder_2_out_15, decoder_1_out_13);
  and and_14 (and_14_out, decoder_2_out_15, decoder_1_out_14);
  and and_15 (BEQ, decoder_2_out_15, decoder_1_out_15);
  or or_1 (or_1_out, or_7_out, BVC);
  or or_2 (or_2_out, or_1_out, BVS);
  or or_3 (or_3_out, or_2_out, BCC);
  or or_4 (or_4_out, or_3_out, BCS);
  or or_5 (or_5_out, or_4_out, BNE);
  or or_6 (rel, or_5_out, BEQ);
  or or_7 (or_7_out, BPL, BMI);
  or or_8 (or_8_out, and_10_out, and_12_out);
  or or_9 (or_9_out, or_8_out, and_14_out);
  or or_10 (or_10_out, and_32_out, or_9_out);
  and and_16 (and_16_out, decoder_2_out_14, decoder_1_out_0);
  and and_17 (and_17_out, decoder_2_out_14, decoder_1_out_1);
  and and_18 (and_18_out, decoder_2_out_14, decoder_1_out_2);
  and and_19 (and_19_out, decoder_2_out_14, decoder_1_out_3);
  and and_20 (and_20_out, decoder_2_out_14, decoder_1_out_4);
  and and_21 (and_21_out, decoder_2_out_14, decoder_1_out_5);
  and and_22 (and_22_out, decoder_2_out_14, decoder_1_out_6);
  and and_23 (and_23_out, decoder_2_out_14, decoder_1_out_7);
  and and_24 (and_24_out, decoder_2_out_14, decoder_1_out_8);
  and and_25 (and_25_out, decoder_2_out_14, decoder_1_out_9);
  and and_26 (and_26_out, decoder_2_out_14, decoder_1_out_10);
  and and_27 (and_27_out, decoder_2_out_14, decoder_1_out_11);
  and and_28 (and_28_out, decoder_2_out_14, decoder_1_out_12);
  and and_29 (and_29_out, decoder_2_out_14, decoder_1_out_13);
  and and_30 (and_30_out, decoder_2_out_14, decoder_1_out_14);
  and and_31 (and_31_out, decoder_2_out_14, decoder_1_out_15);
  or or_11 (hash, or_104_out, or_10_out);
  or or_12 (or_12_out, and_16_out, and_18_out);
  or or_13 (or_13_out, or_12_out, and_20_out);
  or or_14 (or_14_out, or_13_out, and_22_out);
  or or_15 (or_15_out, or_14_out, and_24_out);
  or or_16 (or_16_out, or_15_out, and_26_out);
  or or_17 (or_17_out, or_16_out, and_28_out);
  or or_18 (Xind, or_17_out, and_30_out);
  or or_19 (or_19_out, and_16_out, and_17_out);
  or or_20 (or_20_out, and_19_out, and_18_out);
  or or_21 (or_21_out, and_17_out, and_19_out);
  or or_22 (or_22_out, and_21_out, and_20_out);
  or or_23 (or_23_out, or_21_out, and_21_out);
  or or_24 (or_24_out, and_23_out, and_22_out);
  or or_25 (or_25_out, or_23_out, and_23_out);
  or or_26 (or_26_out, and_25_out, and_24_out);
  or or_27 (or_27_out, or_25_out, and_25_out);
  or or_28 (or_28_out, and_27_out, and_26_out);
  or or_29 (or_29_out, or_27_out, and_27_out);
  or or_30 (or_30_out, and_29_out, and_28_out);
  or or_31 (or_31_out, or_29_out, and_29_out);
  or or_32 (or_32_out, and_31_out, and_30_out);
  or or_33 (IndY, or_31_out, and_31_out);
  and and_32 (and_32_out, decoder_2_out_13, decoder_1_out_10);
  and and_33 (and_33_out, decoder_2_out_11, decoder_1_out_8);
  and and_34 (and_34_out, decoder_2_out_11, decoder_1_out_9);
  and and_35 (and_35_out, decoder_2_out_11, decoder_1_out_10);
  and and_36 (and_36_out, decoder_2_out_11, decoder_1_out_11);
  and and_37 (and_37_out, decoder_2_out_11, decoder_1_out_12);
  and and_38 (and_38_out, decoder_2_out_11, decoder_1_out_14);
  or or_34 (or_34_out, and_33_out, and_35_out);
  or or_35 (or_35_out, or_34_out, and_37_out);
  or or_36 (or_36_out, or_35_out, and_38_out);
  or or_37 (zpg, or_45_out, or_36_out);
  or or_38 (or_38_out, and_33_out, and_34_out);
  or or_39 (or_39_out, and_36_out, and_35_out);
  or or_40 (or_40_out, and_34_out, and_36_out);
  or or_41 (or_41_out, and_37_out, and_12_out);
  or or_42 (or_42_out, and_38_out, and_14_out);
  or or_43 (zpgX, or_60_out, or_40_out);
  or or_44 (or_44_out, and_10_out, or_39_out);
  and and_39 (and_39_out, decoder_2_out_10, decoder_1_out_0);
  and and_40 (and_40_out, decoder_2_out_10, decoder_1_out_1);
  and and_41 (and_41_out, decoder_2_out_10, decoder_1_out_2);
  and and_42 (and_42_out, decoder_2_out_10, decoder_1_out_3);
  and and_43 (and_43_out, decoder_2_out_10, decoder_1_out_4);
  and and_44 (and_44_out, decoder_2_out_10, decoder_1_out_5);
  and and_45 (and_45_out, decoder_2_out_10, decoder_1_out_6);
  and and_46 (and_46_out, decoder_2_out_10, decoder_1_out_7);
  and and_47 (and_47_out, decoder_2_out_10, decoder_1_out_8);
  and and_48 (and_48_out, decoder_2_out_10, decoder_1_out_9);
  and and_49 (and_49_out, decoder_2_out_10, decoder_1_out_10);
  and and_50 (and_50_out, decoder_2_out_10, decoder_1_out_11);
  and and_51 (and_51_out, decoder_2_out_10, decoder_1_out_12);
  and and_52 (and_52_out, decoder_2_out_10, decoder_1_out_13);
  and and_53 (and_53_out, decoder_2_out_10, decoder_1_out_14);
  and and_54 (and_54_out, decoder_2_out_10, decoder_1_out_15);
  or or_45 (or_45_out, or_58_out, or_83_out);
  or or_46 (or_46_out, and_39_out, and_41_out);
  or or_47 (or_47_out, and_40_out, and_42_out);
  or or_48 (or_48_out, or_46_out, and_43_out);
  or or_49 (or_49_out, or_47_out, and_44_out);
  or or_50 (or_50_out, or_48_out, and_45_out);
  or or_51 (or_51_out, or_49_out, and_46_out);
  or or_52 (or_52_out, or_50_out, and_47_out);
  or or_53 (or_53_out, or_51_out, and_48_out);
  or or_54 (or_54_out, or_52_out, and_49_out);
  or or_55 (or_55_out, or_53_out, and_50_out);
  or or_56 (or_56_out, or_54_out, and_51_out);
  or or_57 (or_57_out, or_55_out, and_52_out);
  or or_58 (or_58_out, or_56_out, and_53_out);
  or or_59 (or_59_out, or_57_out, and_54_out);
  or or_60 (or_60_out, or_59_out, or_89_out);
  or or_61 (or_61_out, and_39_out, and_40_out);
  or or_62 (or_62_out, and_42_out, and_41_out);
  or or_63 (or_63_out, and_44_out, and_43_out);
  or or_64 (or_64_out, and_46_out, and_45_out);
  or or_65 (or_65_out, and_48_out, and_47_out);
  or or_66 (or_66_out, and_50_out, and_49_out);
  or or_67 (or_67_out, and_52_out, and_51_out);
  or or_68 (or_68_out, and_54_out, and_53_out);
  or or_69 (or_69_out, or_19_out, or_61_out);
  or or_70 (or_70_out, or_20_out, or_62_out);
  or or_71 (or_71_out, or_22_out, or_63_out);
  or or_72 (or_72_out, or_24_out, or_64_out);
  or or_73 (or_73_out, or_26_out, or_65_out);
  or or_74 (or_74_out, or_28_out, or_66_out);
  or or_75 (or_75_out, or_30_out, or_67_out);
  or or_76 (or_76_out, or_32_out, or_68_out);
  and and_55 (and_55_out, decoder_2_out_9, decoder_1_out_0);
  and and_56 (and_56_out, decoder_2_out_9, decoder_1_out_1);
  and and_57 (and_57_out, decoder_2_out_9, decoder_1_out_2);
  and and_58 (and_58_out, decoder_2_out_9, decoder_1_out_3);
  and and_59 (and_59_out, decoder_2_out_9, decoder_1_out_4);
  and and_60 (and_60_out, decoder_2_out_9, decoder_1_out_5);
  and and_61 (and_61_out, decoder_2_out_9, decoder_1_out_6);
  and and_62 (and_62_out, decoder_2_out_9, decoder_1_out_7);
  and and_63 (and_63_out, decoder_2_out_9, decoder_1_out_8);
  and and_64 (and_64_out, decoder_2_out_9, decoder_1_out_9);
  and and_65 (and_65_out, decoder_2_out_9, decoder_1_out_10);
  and and_66 (and_66_out, decoder_2_out_9, decoder_1_out_11);
  and and_67 (and_67_out, decoder_2_out_9, decoder_1_out_12);
  and and_68 (and_68_out, decoder_2_out_9, decoder_1_out_13);
  and and_69 (and_69_out, decoder_2_out_9, decoder_1_out_14);
  and and_70 (and_70_out, decoder_2_out_9, decoder_1_out_15);
  or or_77 (or_77_out, and_55_out, and_57_out);
  or or_78 (or_78_out, or_77_out, and_59_out);
  or or_79 (or_79_out, or_78_out, and_61_out);
  or or_80 (or_80_out, or_79_out, and_63_out);
  or or_81 (or_81_out, or_80_out, and_65_out);
  or or_82 (or_82_out, or_81_out, and_67_out);
  or or_83 (or_83_out, or_82_out, and_69_out);
  or or_84 (or_84_out, and_56_out, and_58_out);
  or or_85 (or_85_out, or_84_out, and_60_out);
  or or_86 (or_86_out, or_85_out, and_62_out);
  or or_87 (zpgY, and_64_out, and_66_out);
  or or_88 (or_88_out, or_86_out, and_68_out);
  or or_89 (or_89_out, or_88_out, and_70_out);
  or or_90 (or_90_out, and_55_out, and_56_out);
  or or_91 (or_91_out, and_58_out, and_57_out);
  or or_92 (or_92_out, and_60_out, and_59_out);
  or or_93 (or_93_out, and_62_out, and_61_out);
  or or_94 (or_94_out, and_64_out, and_63_out);
  or or_95 (or_95_out, and_66_out, and_65_out);
  or or_96 (or_96_out, and_68_out, and_67_out);
  or or_97 (or_97_out, and_70_out, and_69_out);
  or or_98 (or_98_out, and_32_out, or_95_out);
  and and_71 (PHP, decoder_2_out_7, decoder_1_out_0);
  and and_72 (CLC, decoder_2_out_7, decoder_1_out_1);
  and and_73 (PLP, decoder_2_out_7, decoder_1_out_2);
  and and_74 (SEC, decoder_2_out_7, decoder_1_out_3);
  and and_75 (PHA, decoder_2_out_7, decoder_1_out_4);
  and and_76 (CLI, decoder_2_out_7, decoder_1_out_5);
  and and_77 (PLA, decoder_2_out_7, decoder_1_out_6);
  and and_78 (SEI, decoder_2_out_7, decoder_1_out_7);
  and and_79 (DEY, decoder_2_out_7, decoder_1_out_8);
  and and_80 (TYA, decoder_2_out_7, decoder_1_out_9);
  and and_81 (TAY, decoder_2_out_7, decoder_1_out_10);
  and and_82 (CLV, decoder_2_out_7, decoder_1_out_11);
  and and_83 (INY, decoder_2_out_7, decoder_1_out_12);
  and and_84 (CLD, decoder_2_out_7, decoder_1_out_13);
  and and_85 (INX, decoder_2_out_7, decoder_1_out_14);
  and and_86 (SED, decoder_2_out_7, decoder_1_out_15);
  Decoder #(.Selector_Bits(4)) decoder_2 (
    .sel(INPUT[3:0]), .out_1(decoder_2_out_1), .out_2(decoder_2_out_2), .out_3(decoder_2_out_3),
    .out_5(decoder_2_out_5), .out_6(decoder_2_out_6), .out_7(decoder_2_out_7), .out_9(decoder_2_out_9),
    .out_10(decoder_2_out_10), .out_11(decoder_2_out_11), .out_13(decoder_2_out_13),
    .out_14(decoder_2_out_14), .out_15(decoder_2_out_15));  // open: out_0, out_4, out_8, out_12
  and and_87 (and_87_out, decoder_2_out_6, decoder_1_out_0);
  and and_88 (and_88_out, decoder_2_out_6, decoder_1_out_1);
  and and_89 (and_89_out, decoder_2_out_6, decoder_1_out_2);
  and and_90 (and_90_out, decoder_2_out_6, decoder_1_out_3);
  and and_91 (and_91_out, decoder_2_out_6, decoder_1_out_4);
  and and_92 (and_92_out, decoder_2_out_6, decoder_1_out_5);
  and and_93 (and_93_out, decoder_2_out_6, decoder_1_out_6);
  and and_94 (and_94_out, decoder_2_out_6, decoder_1_out_7);
  and and_95 (and_95_out, decoder_2_out_6, decoder_1_out_9);
  and and_96 (and_96_out, decoder_2_out_6, decoder_1_out_10);
  and and_97 (and_97_out, decoder_2_out_6, decoder_1_out_11);
  and and_98 (and_98_out, decoder_2_out_6, decoder_1_out_12);
  and and_99 (and_99_out, decoder_2_out_6, decoder_1_out_13);
  and and_100 (and_100_out, decoder_2_out_6, decoder_1_out_14);
  and and_101 (and_101_out, decoder_2_out_6, decoder_1_out_15);
  or or_99 (or_99_out, and_87_out, and_89_out);
  or or_100 (or_100_out, or_99_out, and_91_out);
  or or_101 (or_101_out, or_100_out, and_93_out);
  or or_102 (or_102_out, or_101_out, and_96_out);
  or or_103 (or_103_out, or_102_out, and_98_out);
  or or_104 (or_104_out, or_103_out, and_100_out);
  or or_105 (or_105_out, and_87_out, and_88_out);
  or or_106 (or_106_out, and_90_out, and_89_out);
  or or_107 (or_107_out, and_88_out, and_90_out);
  or or_108 (or_108_out, and_92_out, and_91_out);
  or or_109 (or_109_out, or_107_out, and_92_out);
  or or_110 (or_110_out, and_94_out, and_93_out);
  or or_111 (or_111_out, or_109_out, and_94_out);
  or or_112 (or_112_out, and_95_out, or_73_out);
  or or_113 (or_113_out, or_111_out, and_95_out);
  or or_114 (or_114_out, and_97_out, and_96_out);
  or or_115 (or_115_out, or_113_out, and_97_out);
  or or_116 (or_116_out, and_99_out, and_98_out);
  or or_117 (or_117_out, or_115_out, and_99_out);
  or or_118 (or_118_out, and_101_out, and_100_out);
  or or_119 (or_119_out, or_117_out, and_101_out);
  or or_120 (absY, LDXABSY, or_119_out);
  or or_121 (or_121_out, or_69_out, or_105_out);
  or or_122 (or_122_out, or_70_out, or_106_out);
  or or_123 (or_123_out, or_71_out, or_108_out);
  or or_124 (or_124_out, or_72_out, or_110_out);
  or or_125 (or_125_out, or_74_out, or_114_out);
  or or_126 (or_126_out, or_75_out, or_116_out);
  or or_127 (or_127_out, or_76_out, or_118_out);
  and and_102 (and_102_out, decoder_2_out_5, decoder_1_out_0);
  and and_103 (and_103_out, decoder_2_out_5, decoder_1_out_2);
  and and_104 (and_104_out, decoder_2_out_5, decoder_1_out_4);
  and and_105 (and_105_out, decoder_2_out_5, decoder_1_out_6);
  and and_106 (TXA, decoder_2_out_5, decoder_1_out_8);
  and and_107 (TXS, decoder_2_out_5, decoder_1_out_9);
  and and_108 (TAX, decoder_2_out_5, decoder_1_out_10);
  and and_109 (TSX, decoder_2_out_5, decoder_1_out_11);
  and and_110 (DEX, decoder_2_out_5, decoder_1_out_12);
  or or_128 (or_128_out, or_90_out, and_102_out);
  or or_129 (or_129_out, and_102_out, and_103_out);
  or or_130 (or_130_out, or_91_out, and_103_out);
  or or_131 (or_131_out, or_129_out, and_104_out);
  or or_132 (or_132_out, or_92_out, and_104_out);
  or or_133 (A, or_131_out, and_105_out);
  or or_134 (or_134_out, or_93_out, and_105_out);
  and and_111 (and_111_out, decoder_2_out_3, decoder_1_out_4);
  and and_112 (ind, decoder_2_out_3, decoder_1_out_6);
  and and_113 (and_113_out, decoder_2_out_3, decoder_1_out_8);
  and and_114 (and_114_out, decoder_2_out_3, decoder_1_out_10);
  and and_115 (LDYABSX, decoder_2_out_3, decoder_1_out_11);
  and and_116 (and_116_out, decoder_2_out_3, decoder_1_out_12);
  and and_117 (and_117_out, decoder_2_out_3, decoder_1_out_14);
  or or_135 (JMP, and_111_out, ind);
  or or_136 (or_136_out, and_111_out, and_113_out);
  or or_137 (or_137_out, or_136_out, and_114_out);
  or or_138 (or_138_out, LDYABSX, and_114_out);
  or or_139 (or_139_out, or_137_out, and_116_out);
  or or_140 (or_140_out, or_139_out, and_117_out);
  or or_141 (or_141_out, JSR, or_140_out);
  or or_142 (abs, or_147_out, or_141_out);
  or or_143 (STA, or_38_out, and_113_out);
  or or_144 (LDY, or_44_out, or_138_out);
  or or_145 (CPY, or_41_out, and_116_out);
  or or_146 (CPX, or_42_out, and_117_out);
  and and_118 (and_118_out, decoder_2_out_2, decoder_1_out_0);
  and and_119 (and_119_out, decoder_2_out_2, decoder_1_out_1);
  and and_120 (and_120_out, decoder_2_out_2, decoder_1_out_2);
  and and_121 (and_121_out, decoder_2_out_2, decoder_1_out_3);
  and and_122 (and_122_out, decoder_2_out_2, decoder_1_out_4);
  and and_123 (and_123_out, decoder_2_out_2, decoder_1_out_5);
  and and_124 (and_124_out, decoder_2_out_2, decoder_1_out_6);
  and and_125 (and_125_out, decoder_2_out_2, decoder_1_out_7);
  and and_126 (and_126_out, decoder_2_out_2, decoder_1_out_8);
  and and_127 (and_127_out, decoder_2_out_2, decoder_1_out_9);
  and and_128 (and_128_out, decoder_2_out_2, decoder_1_out_10);
  and and_129 (and_129_out, decoder_2_out_2, decoder_1_out_11);
  and and_130 (and_130_out, decoder_2_out_2, decoder_1_out_12);
  and and_131 (and_131_out, decoder_2_out_2, decoder_1_out_13);
  and and_132 (and_132_out, decoder_2_out_2, decoder_1_out_14);
  and and_133 (and_133_out, decoder_2_out_2, decoder_1_out_15);
  or or_147 (or_147_out, or_186_out, or_154_out);
  or or_148 (or_148_out, and_118_out, and_120_out);
  or or_149 (or_149_out, or_148_out, and_122_out);
  or or_150 (or_150_out, or_149_out, and_124_out);
  or or_151 (or_151_out, or_150_out, and_126_out);
  or or_152 (or_152_out, or_151_out, and_128_out);
  or or_153 (or_153_out, or_152_out, and_130_out);
  or or_154 (or_154_out, or_153_out, and_132_out);
  or or_155 (or_155_out, and_118_out, and_119_out);
  or or_156 (or_156_out, and_121_out, and_120_out);
  or or_157 (or_157_out, and_119_out, and_121_out);
  or or_158 (or_158_out, and_123_out, and_122_out);
  or or_159 (or_159_out, or_157_out, and_123_out);
  or or_160 (or_160_out, and_125_out, and_124_out);
  or or_161 (or_161_out, or_159_out, and_125_out);
  or or_162 (or_162_out, and_127_out, and_126_out);
  or or_163 (or_163_out, or_161_out, and_127_out);
  or or_164 (or_164_out, and_129_out, and_128_out);
  or or_165 (or_165_out, or_163_out, and_129_out);
  or or_166 (or_166_out, and_131_out, and_130_out);
  or or_167 (or_167_out, or_165_out, and_131_out);
  or or_168 (or_168_out, and_133_out, and_132_out);
  or or_169 (or_169_out, or_167_out, and_133_out);
  or or_170 (ORA, or_121_out, or_155_out);
  or or_171 (AND, or_122_out, or_156_out);
  or or_172 (EOR, or_123_out, or_158_out);
  or or_173 (ADC, or_124_out, or_160_out);
  or or_174 (LDA, or_125_out, or_164_out);
  or or_175 (CMP, or_126_out, or_166_out);
  or or_176 (SBC, or_127_out, or_168_out);
  or or_177 (STY, or_112_out, or_162_out);
  and and_134 (and_134_out, decoder_2_out_1, decoder_1_out_0);
  and and_135 (and_135_out, decoder_2_out_1, decoder_1_out_1);
  and and_136 (and_136_out, decoder_2_out_1, decoder_1_out_2);
  and and_137 (and_137_out, decoder_2_out_1, decoder_1_out_3);
  and and_138 (and_138_out, decoder_2_out_1, decoder_1_out_4);
  and and_139 (and_139_out, decoder_2_out_1, decoder_1_out_5);
  and and_140 (and_140_out, decoder_2_out_1, decoder_1_out_6);
  and and_141 (and_141_out, decoder_2_out_1, decoder_1_out_7);
  and and_142 (and_142_out, decoder_2_out_1, decoder_1_out_8);
  and and_143 (and_143_out, decoder_2_out_1, decoder_1_out_10);
  and and_144 (LDXABSY, decoder_2_out_1, decoder_1_out_11);
  and and_145 (and_145_out, decoder_2_out_1, decoder_1_out_12);
  and and_146 (and_146_out, decoder_2_out_1, decoder_1_out_13);
  and and_147 (and_147_out, decoder_2_out_1, decoder_1_out_14);
  and and_148 (and_148_out, decoder_2_out_1, decoder_1_out_15);
  or or_178 (or_178_out, or_199_out, or_169_out);
  or or_179 (absX, LDYABSX, or_178_out);
  or or_180 (or_180_out, and_134_out, and_136_out);
  or or_181 (or_181_out, or_180_out, and_138_out);
  or or_182 (or_182_out, or_181_out, and_140_out);
  or or_183 (or_183_out, or_182_out, and_142_out);
  or or_184 (or_184_out, or_183_out, and_143_out);
  or or_185 (or_185_out, or_184_out, and_145_out);
  or or_186 (or_186_out, or_185_out, and_147_out);
  or or_187 (or_187_out, and_134_out, and_135_out);
  or or_188 (or_188_out, and_137_out, and_136_out);
  or or_189 (or_189_out, and_135_out, and_137_out);
  or or_190 (or_190_out, and_139_out, and_138_out);
  or or_191 (or_191_out, or_189_out, and_139_out);
  or or_192 (or_192_out, and_141_out, and_140_out);
  or or_193 (or_193_out, or_191_out, and_141_out);
  or or_194 (STX, or_94_out, and_142_out);
  or or_195 (or_195_out, LDXABSY, and_143_out);
  or or_196 (or_196_out, and_146_out, and_145_out);
  or or_197 (or_197_out, or_193_out, and_146_out);
  or or_198 (or_198_out, and_148_out, and_147_out);
  or or_199 (or_199_out, or_197_out, and_148_out);
  or or_200 (ASL, or_128_out, or_187_out);
  or or_201 (ROL, or_130_out, or_188_out);
  or or_202 (LSR, or_132_out, or_190_out);
  or or_203 (ROR, or_134_out, or_192_out);
  or or_204 (LDX, or_98_out, or_195_out);
  or or_205 (DEC, or_96_out, or_196_out);
  or or_206 (INC, or_97_out, or_198_out);

  // Other names for the same wires on the sheet: JSRABS = JSR
endmodule
