// Digital circuit ABH.dig as structural Verilog
module ABH (
  input  PHI1,
  input  PHI2,
  input  ADH_ABH,
  input  ADH0,
  input  ADH1,
  input  ADH2,
  input  ADH3,
  input  ADH4,
  input  ADH5,
  input  ADH6,
  input  ADH7,
  output A8,
  output A9,
  output A10,
  output A11,
  output A12,
  output A13,
  output A14,
  output A15
);

  wire notconnected_1_out, notconnected_2_out, notconnected_3_out, notconnected_4_out, notconnected_5_out,
       notconnected_6_out, notconnected_7_out, notconnected_8_out;

  ABH_BIT abh_bit_1 (.PHI1(PHI1), .PHI2(PHI2), .in_6(notconnected_1_out), .ADH_ABH(ADH_ABH), .ADHx(ADH0), .Ax(A8));
  // NotConnected on notconnected_1_out
  ABH_BIT abh_bit_2 (.PHI1(PHI1), .PHI2(PHI2), .in_6(notconnected_2_out), .ADH_ABH(ADH_ABH), .ADHx(ADH1), .Ax(A9));
  // NotConnected on notconnected_2_out
  ABH_BIT abh_bit_3 (.PHI1(PHI1), .PHI2(PHI2), .in_6(notconnected_3_out), .ADH_ABH(ADH_ABH), .ADHx(ADH2), .Ax(A10));
  // NotConnected on notconnected_3_out
  ABH_BIT abh_bit_4 (.PHI1(PHI1), .PHI2(PHI2), .in_6(notconnected_4_out), .ADH_ABH(ADH_ABH), .ADHx(ADH3), .Ax(A11));
  // NotConnected on notconnected_4_out
  ABH_BIT abh_bit_5 (.PHI1(PHI1), .PHI2(PHI2), .in_6(notconnected_5_out), .ADH_ABH(ADH_ABH), .ADHx(ADH4), .Ax(A12));
  // NotConnected on notconnected_5_out
  ABH_BIT abh_bit_6 (.PHI1(PHI1), .PHI2(PHI2), .in_6(notconnected_6_out), .ADH_ABH(ADH_ABH), .ADHx(ADH5), .Ax(A13));
  // NotConnected on notconnected_6_out
  ABH_BIT abh_bit_7 (.PHI1(PHI1), .PHI2(PHI2), .in_6(notconnected_7_out), .ADH_ABH(ADH_ABH), .ADHx(ADH6), .Ax(A14));
  // NotConnected on notconnected_7_out
  ABH_BIT abh_bit_8 (.PHI1(PHI1), .PHI2(PHI2), .in_6(notconnected_8_out), .ADH_ABH(ADH_ABH), .ADHx(ADH7), .Ax(A15));
  // NotConnected on notconnected_8_out

  // Notes on the sheet:
  //   0
  //   1
  //   2
  //   3
  //   4
  //   5
  //   6
  //   7
endmodule
