// Digital circuit ALU_AC.dig as structural Verilog
module ALU_AC (
  input  in_1,
  input  SB_AC,
  input  AC_SB,
  input  AC_DB,
  input  SB_DB,
  input  SB_ADH,
  input  [7:0] ins,
  input  SB_Dirty,
  input  DB_Dirty,
  input  ADH_Dirty,
  input  [7:0] SB_In,
  input  [7:0] DB_In,
  input  [7:0] ADH_In,
  output [7:0] SB_out,
  output [7:0] DB_out,
  output [7:0] ADH_out,
  output [7:0] AC_Debug
);

  wire and_1_out, and_2_out, and_3_out, and_4_out, driver_1_out, driver_2_out, driver_3_out, driver_4_out,
       driver_5_out, driver_6_out, driver_7_out, driver_8_out;

  assign driver_1_out = SB_AC ? ins[0] : 1'bz;  // Driver driver_1
  assign driver_2_out = SB_AC ? ins[1] : 1'bz;  // Driver driver_2
  assign driver_3_out = SB_AC ? ins[2] : 1'bz;  // Driver driver_3
  assign driver_4_out = SB_AC ? ins[3] : 1'bz;  // Driver driver_4
  assign driver_5_out = SB_AC ? ins[4] : 1'bz;  // Driver driver_5
  assign driver_6_out = SB_AC ? ins[5] : 1'bz;  // Driver driver_6
  assign driver_7_out = SB_AC ? ins[6] : 1'bz;  // Driver driver_7
  assign driver_8_out = SB_AC ? ins[7] : 1'bz;  // Driver driver_8
  DLATCH dlatch_1 (.C(in_1), .D(driver_1_out), .Q(AC_Debug[0]));  // open: nQ
  DLATCH dlatch_2 (.C(in_1), .D(driver_2_out), .Q(AC_Debug[1]));  // open: nQ
  DLATCH dlatch_3 (.C(in_1), .D(driver_3_out), .Q(AC_Debug[2]));  // open: nQ
  DLATCH dlatch_4 (.C(in_1), .D(driver_4_out), .Q(AC_Debug[3]));  // open: nQ
  DLATCH dlatch_5 (.C(in_1), .D(driver_5_out), .Q(AC_Debug[4]));  // open: nQ
  DLATCH dlatch_6 (.C(in_1), .D(driver_6_out), .Q(AC_Debug[5]));  // open: nQ
  DLATCH dlatch_7 (.C(in_1), .D(driver_7_out), .Q(AC_Debug[6]));  // open: nQ
  DLATCH dlatch_8 (.C(in_1), .D(driver_8_out), .Q(AC_Debug[7]));  // open: nQ
  assign SB_out = AC_SB ? AC_Debug : 8'bz;  // Driver driver_9
  assign DB_out = AC_DB ? AC_Debug : 8'bz;  // Driver driver_10
  and and_1 (and_1_out, SB_DB, DB_Dirty);
  and and_2 (and_2_out, SB_ADH, SB_Dirty);
  assign SB_out = and_1_out ? DB_In : 8'bz;  // Driver driver_11
  assign ADH_out = and_2_out ? SB_In : 8'bz;  // Driver driver_12
  and and_3 (and_3_out, SB_DB, SB_Dirty);
  and and_4 (and_4_out, SB_ADH, ADH_Dirty);
  assign DB_out = and_3_out ? SB_In : 8'bz;  // Driver driver_13
  assign SB_out = and_4_out ? ADH_In : 8'bz;  // Driver driver_14
endmodule
