// Digital circuit ALU_BCD.dig as structural Verilog
module ALU_BCD (
  input  [7:0] \ÃDDx ,
  input  SB0,
  input  SB1,
  input  SB2,
  input  SB3,
  input  SB4,
  input  SB5,
  input  SB6,
  input  SB7,
  input  PHI2,
  input  ncarry3,
  input  ACR,
  input  nDAA,
  input  nDSA,
  output out0,
  output out1,
  output out2,
  output out3,
  output out4,
  output out5,
  output out6,
  output out7
);

  wire and_1_out, and_2_out, and_3_out, and_4_out, dlatch_1_nq, dlatch_2_nq, dlatch_3_q, dlatch_4_nq,
       nand_1_out, nand_2_out, nand_3_out, nand_4_out, nand_5_out, nand_6_out, nand_7_out, nand_8_out,
       nand_9_out, nand_10_out, nand_11_out, nor_1_out, nor_2_out, nor_3_out, nor_4_out, nor_5_out,
       nor_6_out, nor_7_out, not_1_out, not_2_out, not_3_out, not_4_out, not_5_out, not_6_out, not_7_out,
       not_8_out, not_9_out;

  not not_1 (not_1_out, nDAA);
  nor nor_1 (nor_1_out, \ÃDDx [1], \ÃDDx [2]);
  nand nand_1 (nand_1_out, \ÃDDx [1], \ÃDDx [2]);
  nor nor_2 (nor_2_out, \ÃDDx [5], \ÃDDx [6]);
  nand nand_2 (nand_2_out, \ÃDDx [5], \ÃDDx [6]);
  nand nand_3 (nand_3_out, not_1_out, ncarry3);
  nor nor_3 (nor_3_out, ncarry3, nDSA);
  not not_2 (not_2_out, nDSA);
  DLATCH dlatch_1 (.C(PHI2), .D(nand_3_out), .nQ(dlatch_1_nq));  // open: Q
  DLATCH dlatch_2 (.C(PHI2), .D(not_1_out), .nQ(dlatch_2_nq));  // open: Q
  DLATCH dlatch_3 (.C(PHI2), .D(nor_3_out), .Q(dlatch_3_q));  // open: nQ
  DLATCH dlatch_4 (.C(PHI2), .D(not_2_out), .nQ(dlatch_4_nq));  // open: Q
  nand nand_4 (nand_4_out, \ÃDDx [1], dlatch_1_nq);
  nand nand_5 (nand_5_out, ~\ÃDDx [1], dlatch_3_q);  // NAnd
  nand nand_6 (nand_6_out, ~nor_1_out, dlatch_3_q);  // NAnd
  nand nand_7 (nand_7_out, nand_1_out, dlatch_1_nq);
  nand nand_8 (nand_8_out, \ÃDDx [5], nor_4_out);
  nand nand_9 (nand_9_out, ~\ÃDDx [5], nor_5_out);  // NAnd
  nand nand_10 (nand_10_out, ~nor_2_out, nor_5_out);  // NAnd
  nand nand_11 (nand_11_out, nand_2_out, nor_4_out);
  not not_3 (not_3_out, ACR);
  and and_1 (and_1_out, nand_4_out, nand_5_out);
  and and_2 (and_2_out, nand_6_out, nand_7_out);
  and and_3 (and_3_out, nand_8_out, nand_9_out);
  and and_4 (and_4_out, nand_10_out, nand_11_out);
  nor nor_4 (nor_4_out, not_3_out, dlatch_2_nq);
  nor nor_5 (nor_5_out, ACR, dlatch_4_nq);
  nor nor_6 (nor_6_out, dlatch_1_nq, dlatch_3_q);
  nor nor_7 (nor_7_out, nor_4_out, nor_5_out);
  not not_4 (not_4_out, SB1);
  not not_5 (not_5_out, SB2);
  not not_6 (not_6_out, SB3);
  not not_7 (not_7_out, SB5);
  not not_8 (not_8_out, SB6);
  not not_9 (not_9_out, SB7);
  xor xor_1 (out1, nor_6_out, not_4_out);
  xor xor_2 (out2, and_1_out, not_5_out);
  xor xor_3 (out3, and_2_out, not_6_out);
  xor xor_4 (out5, nor_7_out, not_7_out);
  xor xor_5 (out6, and_3_out, not_8_out);
  xor xor_6 (out7, and_4_out, not_9_out);

  assign out0 = SB0;
  assign out4 = SB4;
endmodule
