// Digital circuit ALU_EVEN_BIT.dig as structural Verilog
module ALU_EVEN_BIT (
  input  NDB_ADD,
  input  DB_ADD,
  input  Z_ADD,
  input  SB_ADD,
  input  ADL_ADD,
  input  ANDS,
  input  EORS,
  input  ORS,
  input  SRS,
  input  SUMS,
  input  ncin,
  input  prev_res,
  input  SBx,
  input  DBx,
  input  ADLx,
  input  in_23,
  input  in_24,
  input  in_25,
  input  in_26,
  output AI_Debug,
  output BI_Debig,
  output r_xor,
  output r_nand,
  output r_nor,
  output cout,
  output nres
);

  wire and_1_out, driver_1_out, driver_3_out, nand_2_out, nand_3_out, nand_4_out, nor_2_out, not_1_out,
       not_2_out, not_3_out, not_4_out, not_5_out;

  assign driver_1_out = Z_ADD ? 1'b0 : 1'bz;  // Driver driver_1
  assign driver_1_out = SB_ADD ? SBx : 1'bz;  // Driver driver_2
  not not_1 (not_1_out, DBx);
  assign driver_3_out = DB_ADD ? DBx : 1'bz;  // Driver driver_3
  assign driver_3_out = NDB_ADD ? not_1_out : 1'bz;  // Driver driver_4
  assign driver_3_out = ADL_ADD ? ADLx : 1'bz;  // Driver driver_5
  not not_2 (not_2_out, ncin);
  DLATCH dlatch_1 (.C(1'b1), .D(driver_1_out), .Q(AI_Debug));  // open: nQ
  DLATCH dlatch_2 (.C(1'b1), .D(driver_3_out), .Q(BI_Debig));  // open: nQ
  not not_3 (not_3_out, r_nor);
  nand nand_1 (r_nand, AI_Debug, BI_Debig);
  nor nor_1 (r_nor, AI_Debug, BI_Debig);
  nand nand_2 (nand_2_out, not_3_out, r_nand);
  nand nand_3 (nand_3_out, not_2_out, nand_2_out);
  nor nor_2 (nor_2_out, not_2_out, nand_2_out);
  nand nand_4 (nand_4_out, ncin, r_nand);
  not not_4 (not_4_out, nor_2_out);
  not not_5 (not_5_out, r_nor);
  and and_1 (and_1_out, nand_3_out, not_4_out);
  and and_2 (cout, nand_4_out, not_5_out);
  assign nres = ANDS ? r_nand : 1'bz;  // Driver driver_6
  assign nres = ORS ? r_nor : 1'bz;  // Driver driver_7
  assign nres = EORS ? nand_2_out : 1'bz;  // Driver driver_8
  assign nres = SRS ? prev_res : 1'bz;  // Driver driver_9
  assign nres = SUMS ? and_1_out : 1'bz;  // Driver driver_10
  not not_6 (r_xor, nand_2_out);

  // Other names for the same wires on the sheet: AI = AI_Debug; BI = BI_Debig
endmodule
