// Digital circuit ALU_OPS.dig as structural Verilog
module ALU_OPS (
  input  SB0,
  input  SB1,
  input  SB2,
  input  SB3,
  input  SB4,
  input  SB5,
  input  SB6,
  input  SB7,
  input  DB0,
  input  DB1,
  input  DB2,
  input  DB3,
  input  DB4,
  input  DB5,
  input  DB6,
  input  DB7,
  input  ADL0,
  input  ADL1,
  input  ADL2,
  input  ADL3,
  input  ADL4,
  input  ADL5,
  input  ADL6,
  input  ADL7,
  input  DC3,
  input  ncin,
  input  SUMS,
  input  SRS,
  input  ORS,
  input  EORS,
  input  ANDS,
  input  ADL_ADD,
  input  SB_ADD,
  input  Z_ADD,
  input  DB_ADD,
  input  NDB_ADD,
  output res0,
  output res1,
  output res2,
  output res3,
  output res4,
  output res5,
  output res6,
  output res7,
  output nor0,
  output nor1,
  output nor2,
  output nor3,
  output nor4,
  output nor5,
  output nor6,
  output nor7,
  output nand0,
  output nand1,
  output nand2,
  output nand3,
  output nand4,
  output nand5,
  output nand6,
  output nand7,
  output xor0,
  output xor1,
  output xor2,
  output xor3,
  output xor4,
  output xor5,
  output xor6,
  output xor7,
  output ncarry3,
  output carry4,
  output carry6,
  output ncarry7,
  output [7:0] BI_Debug,
  output [7:0] AI_Debug
);

  wire alu_even_bit_1_cout, alu_even_bit_2_cout, alu_odd_bit_1_cout, alu_odd_bit_3_cout, and_1_out,
       not_1_out, notconnected_1_out, notconnected_2_out, notconnected_3_out, notconnected_4_out,
       notconnected_5_out, notconnected_6_out, notconnected_7_out, notconnected_8_out, notconnected_9_out,
       notconnected_10_out, notconnected_11_out, notconnected_12_out, notconnected_13_out,
       notconnected_14_out, notconnected_15_out, notconnected_16_out, notconnected_17_out,
       notconnected_18_out, notconnected_19_out, notconnected_20_out, notconnected_21_out,
       notconnected_22_out, notconnected_23_out, notconnected_24_out, notconnected_25_out,
       notconnected_26_out, notconnected_27_out, notconnected_28_out, notconnected_29_out,
       notconnected_30_out, notconnected_31_out, notconnected_32_out;

  ALU_EVEN_BIT alu_even_bit_1 (
    .NDB_ADD(NDB_ADD), .DB_ADD(DB_ADD), .Z_ADD(Z_ADD), .SB_ADD(SB_ADD), .ADL_ADD(ADL_ADD), .ANDS(ANDS),
    .EORS(EORS), .ORS(ORS), .SRS(SRS), .SUMS(SUMS), .in_23(notconnected_1_out), .in_24(notconnected_2_out),
    .ncin(ncin), .in_25(notconnected_3_out), .prev_res(nand1), .in_26(notconnected_4_out), .SBx(SB0),
    .DBx(DB0), .ADLx(ADL0), .AI_Debug(AI_Debug[0]), .BI_Debig(BI_Debug[0]), .nres(res0),
    .cout(alu_even_bit_1_cout), .r_nor(nor0), .r_nand(nand0), .r_xor(xor0));
  // NotConnected on notconnected_1_out
  // NotConnected on notconnected_2_out
  // NotConnected on notconnected_3_out
  // NotConnected on notconnected_4_out
  ALU_ODD_BIT alu_odd_bit_1 (
    .NDB_ADD(NDB_ADD), .DB_ADD(DB_ADD), .Z_ADD(Z_ADD), .SB_ADD(SB_ADD), .ADL_ADD(ADL_ADD), .ANDS(ANDS),
    .EORS(EORS), .ORS(ORS), .SRS(SRS), .SUMS(SUMS), .in_23(notconnected_5_out), .in_24(notconnected_6_out),
    .ncin(alu_even_bit_1_cout), .in_25(notconnected_7_out), .prev_res(nand2), .in_26(notconnected_8_out),
    .SBx(SB1), .DBx(DB1), .ADLx(ADL1), .AI_Debug(AI_Debug[1]), .BI_Debig(BI_Debug[1]), .nres(res1),
    .cout(alu_odd_bit_1_cout), .r_nor(nor1), .r_nand(nand1), .r_xor(xor1));
  // NotConnected on notconnected_5_out
  // NotConnected on notconnected_6_out
  // NotConnected on notconnected_7_out
  // NotConnected on notconnected_8_out
  ALU_EVEN_BIT alu_even_bit_2 (
    .NDB_ADD(NDB_ADD), .DB_ADD(DB_ADD), .Z_ADD(Z_ADD), .SB_ADD(SB_ADD), .ADL_ADD(ADL_ADD), .ANDS(ANDS),
    .EORS(EORS), .ORS(ORS), .SRS(SRS), .SUMS(SUMS), .in_23(notconnected_9_out), .in_24(notconnected_10_out),
    .ncin(alu_odd_bit_1_cout), .in_25(notconnected_11_out), .prev_res(nand3), .in_26(notconnected_12_out),
    .SBx(SB2), .DBx(DB2), .ADLx(ADL2), .AI_Debug(AI_Debug[2]), .BI_Debig(BI_Debug[2]), .nres(res2),
    .cout(alu_even_bit_2_cout), .r_nor(nor2), .r_nand(nand2), .r_xor(xor2));
  // NotConnected on notconnected_9_out
  // NotConnected on notconnected_10_out
  // NotConnected on notconnected_11_out
  // NotConnected on notconnected_12_out
  ALU_ODD_BIT alu_odd_bit_2 (
    .NDB_ADD(NDB_ADD), .DB_ADD(DB_ADD), .Z_ADD(Z_ADD), .SB_ADD(SB_ADD), .ADL_ADD(ADL_ADD), .ANDS(ANDS),
    .EORS(EORS), .ORS(ORS), .SRS(SRS), .SUMS(SUMS), .in_23(notconnected_13_out), .in_24(notconnected_14_out),
    .ncin(alu_even_bit_2_cout), .in_25(notconnected_15_out), .prev_res(nand4), .in_26(notconnected_16_out),
    .SBx(SB3), .DBx(DB3), .ADLx(ADL3), .AI_Debug(AI_Debug[3]), .BI_Debig(BI_Debug[3]), .nres(res3),
    .cout(ncarry3), .r_nor(nor3), .r_nand(nand3), .r_xor(xor3));
  // NotConnected on notconnected_13_out
  // NotConnected on notconnected_14_out
  // NotConnected on notconnected_15_out
  // NotConnected on notconnected_16_out
  not not_1 (not_1_out, DC3);
  and and_1 (and_1_out, ncarry3, not_1_out);
  ALU_EVEN_BIT alu_even_bit_3 (
    .NDB_ADD(NDB_ADD), .DB_ADD(DB_ADD), .Z_ADD(Z_ADD), .SB_ADD(SB_ADD), .ADL_ADD(ADL_ADD), .ANDS(ANDS),
    .EORS(EORS), .ORS(ORS), .SRS(SRS), .SUMS(SUMS), .in_23(notconnected_17_out), .in_24(notconnected_18_out),
    .ncin(and_1_out), .in_25(notconnected_19_out), .prev_res(nand5), .in_26(notconnected_20_out), .SBx(SB4),
    .DBx(DB4), .ADLx(ADL4), .AI_Debug(AI_Debug[4]), .BI_Debig(BI_Debug[4]), .nres(res4), .cout(carry4),
    .r_nor(nor4), .r_nand(nand4), .r_xor(xor4));
  // NotConnected on notconnected_17_out
  // NotConnected on notconnected_18_out
  // NotConnected on notconnected_19_out
  // NotConnected on notconnected_20_out
  ALU_ODD_BIT alu_odd_bit_3 (
    .NDB_ADD(NDB_ADD), .DB_ADD(DB_ADD), .Z_ADD(Z_ADD), .SB_ADD(SB_ADD), .ADL_ADD(ADL_ADD), .ANDS(ANDS),
    .EORS(EORS), .ORS(ORS), .SRS(SRS), .SUMS(SUMS), .in_23(notconnected_21_out), .in_24(notconnected_22_out),
    .ncin(carry4), .in_25(notconnected_23_out), .prev_res(nand6), .in_26(notconnected_24_out), .SBx(SB5),
    .DBx(DB5), .ADLx(ADL5), .AI_Debug(AI_Debug[5]), .BI_Debig(BI_Debug[5]), .nres(res5),
    .cout(alu_odd_bit_3_cout), .r_nor(nor5), .r_nand(nand5), .r_xor(xor5));
  // NotConnected on notconnected_21_out
  // NotConnected on notconnected_22_out
  // NotConnected on notconnected_23_out
  // NotConnected on notconnected_24_out
  ALU_EVEN_BIT alu_even_bit_4 (
    .NDB_ADD(NDB_ADD), .DB_ADD(DB_ADD), .Z_ADD(Z_ADD), .SB_ADD(SB_ADD), .ADL_ADD(ADL_ADD), .ANDS(ANDS),
    .EORS(EORS), .ORS(ORS), .SRS(SRS), .SUMS(SUMS), .in_23(notconnected_25_out), .in_24(notconnected_26_out),
    .ncin(alu_odd_bit_3_cout), .in_25(notconnected_27_out), .prev_res(nand7), .in_26(notconnected_28_out),
    .SBx(SB6), .DBx(DB6), .ADLx(ADL6), .AI_Debug(AI_Debug[6]), .BI_Debig(BI_Debug[6]), .nres(res6),
    .cout(carry6), .r_nor(nor6), .r_nand(nand6), .r_xor(xor6));
  // NotConnected on notconnected_25_out
  // NotConnected on notconnected_26_out
  // NotConnected on notconnected_27_out
  // NotConnected on notconnected_28_out
  ALU_ODD_BIT alu_odd_bit_4 (
    .NDB_ADD(NDB_ADD), .DB_ADD(DB_ADD), .Z_ADD(Z_ADD), .SB_ADD(SB_ADD), .ADL_ADD(ADL_ADD), .ANDS(ANDS),
    .EORS(EORS), .ORS(ORS), .SRS(SRS), .SUMS(SUMS), .in_23(notconnected_29_out), .in_24(notconnected_30_out),
    .ncin(carry6), .in_25(notconnected_31_out), .prev_res(1'b1), .in_26(notconnected_32_out), .SBx(SB7),
    .DBx(DB7), .ADLx(ADL7), .AI_Debug(AI_Debug[7]), .BI_Debig(BI_Debug[7]), .nres(res7), .cout(ncarry7),
    .r_nor(nor7), .r_nand(nand7), .r_xor(xor7));
  // NotConnected on notconnected_29_out
  // NotConnected on notconnected_30_out
  // NotConnected on notconnected_31_out
  // NotConnected on notconnected_32_out
endmodule
