// Digital circuit BCD_CARRY.dig as structural Verilog
module BCD_CARRY (
  input  nACIN,
  input  carry4,
  input  nDAA,
  input  [7:0] nors,
  input  [7:0] nands,
  input  [7:0] xors,
  output DC7,
  output DC3
);

  wire and_1_out, nand_1_out, nand_2_out, nor_1_out, nor_2_out, nor_3_out, nor_4_out, nor_5_out, nor_6_out,
       nor_7_out, nor_8_out, nor_9_out, nor_10_out, not_1_out, not_2_out, not_3_out, not_4_out, not_5_out,
       not_6_out, not_7_out, not_8_out, or_1_out, or_2_out;

  not not_1 (not_1_out, nands[5]);
  and and_1 (and_1_out, nACIN, nands[0]);
  nor nor_1 (nor_1_out, and_1_out, nors[0]);
  not not_2 (not_2_out, nands[2]);
  not not_3 (not_3_out, nands[1]);
  nor nor_2 (nor_2_out, not_2_out, nors[2]);
  not not_4 (not_4_out, nands[6]);
  nor nor_3 (nor_3_out, carry4, not_1_out, xors[5], xors[6]);
  nor nor_4 (nor_4_out, nor_1_out, nor_2_out, not_3_out, xors[1]);
  nor nor_5 (nor_5_out, xors[7], not_4_out);
  not not_5 (not_5_out, xors[6]);
  nand nand_1 (nand_1_out, not_1_out, carry4);
  nor nor_6 (nor_6_out, not_2_out, xors[3]);
  nand nand_2 (nand_2_out, not_6_out, nor_1_out);
  not not_6 (not_6_out, nands[1]);
  nor nor_7 (nor_7_out, nor_5_out, nor_3_out);
  nor nor_8 (nor_8_out, not_5_out, nand_1_out);
  nor nor_9 (nor_9_out, nor_6_out, nor_4_out);
  nor nor_10 (nor_10_out, nors[2], nand_2_out);
  or or_1 (or_1_out, nor_7_out, nor_8_out);
  or or_2 (or_2_out, nor_9_out, nor_10_out);
  not not_7 (not_7_out, nDAA);
  not not_8 (not_8_out, nDAA);
  and and_2 (DC3, or_2_out, not_7_out);
  and and_3 (DC7, or_1_out, not_8_out);
endmodule
