// Digital circuit BRANCH_LOGIC.dig as structural Verilog
module BRANCH_LOGIC (
  input  BR2,
  input  DB7_in,
  input  PHI2,
  input  PHI1,
  input  nZ_OUT,
  input  nN_OUT,
  input  nV_OUT,
  input  nC_OUT,
  input  D126,
  input  D121,
  input  nIR5,
  output nBRTAKEN,
  output BRFW
);

  wire br2_latch_q, brfw_latch2_2_q, brfw_latch2_q, multiplexer_1_out, nor_1_out, nor_2_out, nor_3_out,
       nor_4_out, nor_5_out, not_1_out, not_2_out, not_3_out, not_4_out, not_5_out, not_6_out;

  not not_1 (not_1_out, D121);
  not not_2 (not_2_out, D126);
  not not_3 (not_3_out, D126);
  not not_4 (not_4_out, D121);
  nor nor_1 (nor_1_out, nC_OUT, D126, not_1_out);
  nor nor_2 (nor_2_out, nV_OUT, D121, not_2_out);
  nor nor_3 (nor_3_out, nN_OUT, not_3_out, not_4_out);
  nor nor_4 (nor_4_out, D126, D121, nZ_OUT);
  not not_5 (not_5_out, DB7_in);
  DLATCH br2_latch (.C(PHI2), .D(BR2), .Q(br2_latch_q));  // open: nQ
  DLATCH brfw_latch2 (.C(PHI2), .D(brfw_latch2_2_q), .Q(brfw_latch2_q));  // open: nQ
  nor nor_5 (nor_5_out, nor_1_out, nor_2_out, nor_3_out, nor_4_out);
  Multiplexer multiplexer_1 (.sel(br2_latch_q), .in_0(brfw_latch2_q), .in_1(not_5_out), .out(multiplexer_1_out));
  not not_6 (not_6_out, multiplexer_1_out);
  xor xor_1 (nBRTAKEN, nIR5, nor_5_out);
  DLATCH brfw_latch2_2 (.C(PHI1), .D(not_6_out), .Q(brfw_latch2_2_q));  // open: nQ
  not not_7 (BRFW, brfw_latch2_2_q);
endmodule
