// Digital circuit BUS_CONTROL.dig as structural Verilog
module BUS_CONTROL (
  input  PHI1,
  input  PHI2,
  input  BR2,
  input  BR3,
  input  T0,
  input  T1,
  input  T2,
  input  T6,
  input  T7,
  input  nready,
  input  AND,
  input  Z_ADL0,
  input  nSBXY,
  input  STXY,
  input  INC_SB,
  input  BRK6E,
  input  DL_PCH,
  input  nPCH_PCH,
  input  ACRL2,
  input  STOR,
  input  D45,
  input  D47,
  input  D48,
  input  D49,
  input  D55,
  input  D56,
  input  D57,
  input  D58,
  input  D59,
  input  D60,
  input  D61,
  input  D62,
  input  D63,
  input  D64,
  input  D65,
  input  D66,
  input  D67,
  input  D68,
  input  D71,
  input  D72,
  input  D73,
  input  D74,
  input  D79,
  input  D81,
  input  D82,
  input  D83,
  input  D84,
  input  D89,
  input  D90,
  input  D91,
  input  D101,
  input  D128,
  input  D129,
  output DL_ADL,
  output DL_DB,
  output DL_ADH,
  output ADH_ABH,
  output ADL_ABL,
  output SB_AC,
  output AC_SB,
  output Z_ADH0,
  output Z_ADH17,
  output AC_DB,
  output SB_DB,
  output SB_ADH,
  output ZTST,
  output PGX
);

  wire ac_db_latch_q, ac_sb_latch_q, adh_abh_latch_nq, adl_abl_latch_nq, and_1_out, and_2_out, and_3_out,
       and_4_out, and_5_out, and_6_out, dl_adh_latch_nq, dl_adl_latch_nq, dl_db_latch_nq, nand_2_out,
       nand_3_out, nand_4_out, nand_5_out, nor_1_out, nor_2_out, nor_3_out, nor_4_out, nor_5_out, nor_6_out,
       nor_7_out, nor_8_out, nor_9_out, nor_10_out, nor_11_out, nor_12_out, nor_13_out, nor_14_out,
       nor_15_out, nor_16_out, nor_17_out, nor_18_out, nor_19_out, nor_20_out, nor_21_out, nor_22_out,
       nor_23_out, nor_24_out, nor_25_out, not_1_out, not_2_out, not_3_out, not_4_out, not_5_out, not_6_out,
       not_7_out, not_8_out, not_9_out, nready_latch_nq, or_1_out, sb_ac_latch_q, sb_adh_latch_nq,
       sb_db_latch_nq, z_adh17_latch_nq;

  nor nor_1 (nor_1_out, D71, D72);
  not not_1 (not_1_out, D73);
  and and_1 (and_1_out, D79, STOR);
  nor nor_2 (nor_2_out, D81, D82);
  and and_2 (and_2_out, D90, ~D129);  // And
  and and_3 (and_3_out, D83, ~D129);  // And
  and and_4 (and_4_out, D128, ~D129);  // And
  nor nor_3 (nor_3_out, D58, D59, D60, D61, D62, D63, D64);
  not not_2 (not_2_out, D64);
  nor nor_4 (nor_4_out, INC_SB, D45, BRK6E, D49, D47, D48);
  not not_3 (not_3_out, D48);
  and and_5 (and_5_out, not_2_out, D65);
  nand nand_1 (PGX, nor_1_out, not_1_out);
  nor nor_5 (nor_5_out, D74, and_1_out);
  nor nor_6 (nor_6_out, D89, and_2_out, D91, D84);
  nor nor_7 (nor_7_out, and_3_out, T0);
  DLATCH nready_latch (.C(PHI1), .D(nready), .nQ(nready_latch_nq));  // open: Q
  not not_4 (not_4_out, nor_1_out);
  nand nand_2 (nand_2_out, not_3_out, STXY);
  not not_5 (not_5_out, nor_3_out);
  nor nor_8 (nor_8_out, and_5_out, D66, D67, D68, AND);
  not not_6 (not_6_out, nor_6_out);
  nor nor_9 (nor_9_out, nor_7_out, and_4_out);
  nand nand_3 (nand_3_out, ACRL2, nready_latch_nq);
  not not_7 (not_7_out, nor_4_out);
  nor nor_10 (nor_10_out, nSBXY, not_5_out, T7, AND);
  nor nor_11 (nor_11_out, not_4_out, nready);
  nor nor_12 (nor_12_out, PGX, BR3);
  nor nor_13 (nor_13_out, not_6_out, T2, nPCH_PCH, D56);
  nand nand_4 (nand_4_out, T6, D55);
  nor nor_14 (nor_14_out, nor_12_out, nand_3_out);
  nor nor_15 (nor_15_out, nready, nor_13_out);
  not not_8 (not_8_out, nand_4_out);
  not not_9 (not_9_out, nor_2_out);
  nor nor_16 (nor_16_out, nor_10_out, AND);
  nor nor_17 (nor_17_out, D57, not_9_out);
  or or_1 (or_1_out, nor_14_out, nor_15_out);
  nor nor_18 (nor_18_out, T7, T6);
  nor nor_19 (nor_19_out, not_8_out, nor_16_out, D67, T1, BR2, nand_2_out);
  and and_6 (and_6_out, or_1_out, ~BR3);  // And
  nand nand_5 (nand_5_out, nor_18_out, nor_11_out);
  nor nor_20 (nor_20_out, DL_PCH, not_6_out);
  nor nor_21 (nor_21_out, Z_ADL0, and_6_out);
  nor nor_22 (nor_22_out, BR2, nor_9_out, not_7_out, D101, T6);
  DLATCH z_adh0_latch (.C(PHI2), .D(nor_2_out), .nQ(Z_ADH0));  // open: Q
  DLATCH z_adh17_latch (.C(PHI2), .D(nor_17_out), .nQ(z_adh17_latch_nq));  // open: Q
  DLATCH sb_ac_latch (.C(PHI2), .D(nor_3_out), .Q(sb_ac_latch_q));  // open: nQ
  DLATCH adl_abl_latch (.C(PHI2), .D(nand_5_out), .nQ(adl_abl_latch_nq));  // open: Q
  DLATCH ac_sb_latch (.C(PHI2), .D(nor_8_out), .Q(ac_sb_latch_q));  // open: nQ
  DLATCH sb_db_latch (.C(PHI2), .D(nor_19_out), .nQ(sb_db_latch_nq));  // open: Q
  DLATCH ac_db_latch (.C(PHI2), .D(nor_5_out), .Q(ac_db_latch_q));  // open: nQ
  DLATCH sb_adh_latch (.C(PHI2), .D(nor_12_out), .nQ(sb_adh_latch_nq));  // open: Q
  DLATCH dl_adh_latch (.C(PHI2), .D(nor_20_out), .nQ(dl_adh_latch_nq));  // open: Q
  DLATCH dl_adl_latch (.C(PHI2), .D(nor_2_out), .nQ(dl_adl_latch_nq));  // open: Q
  DLATCH adh_abh_latch (.C(PHI2), .D(nor_21_out), .nQ(adh_abh_latch_nq));  // open: Q
  DLATCH dl_db_latch (.C(PHI2), .D(nor_22_out), .nQ(dl_db_latch_nq));  // open: Q
  nor nor_23 (nor_23_out, sb_ac_latch_q, PHI2);
  nor nor_24 (nor_24_out, ac_sb_latch_q, PHI2);
  nor nor_25 (nor_25_out, ac_db_latch_q, PHI2);
  assign Z_ADH17 = 1'b1 ? z_adh17_latch_nq : 1'bz;  // Driver driver_1
  assign SB_AC = 1'b1 ? nor_23_out : 1'bz;  // Driver driver_2
  not not_10 (ZTST, nor_10_out);
  assign ADL_ABL = 1'b1 ? adl_abl_latch_nq : 1'bz;  // Driver driver_3
  assign AC_SB = 1'b1 ? nor_24_out : 1'bz;  // Driver driver_4
  assign SB_DB = 1'b1 ? sb_db_latch_nq : 1'bz;  // Driver driver_5
  assign AC_DB = 1'b1 ? nor_25_out : 1'bz;  // Driver driver_6
  assign SB_ADH = 1'b1 ? sb_adh_latch_nq : 1'bz;  // Driver driver_7
  assign DL_ADH = 1'b1 ? dl_adh_latch_nq : 1'bz;  // Driver driver_8
  assign DL_ADL = 1'b1 ? dl_adl_latch_nq : 1'bz;  // Driver driver_9
  assign ADH_ABH = 1'b1 ? adh_abh_latch_nq : 1'bz;  // Driver driver_10
  assign DL_DB = 1'b1 ? dl_db_latch_nq : 1'bz;  // Driver driver_11

  // Other names for the same wires on the sheet: RTS_5 = D84
endmodule
