// Digital circuit DECODER_TRANS.dig as structural Verilog
module DECODER_TRANS (
  input  IR0,
  input  IR01,
  input  IR1,
  input  IR2,
  input  IR3,
  input  IR4,
  input  IR5,
  input  IR6,
  input  IR7,
  input  T0,
  input  T1X,
  input  T2,
  input  T3,
  input  T4,
  input  T5,
  output x0,
  output x1,
  output x2,
  output x3,
  output x4,
  output x5,
  output x6,
  output x7,
  output x8,
  output x9,
  output x10,
  output x11,
  output x12,
  output x13,
  output x14,
  output x15,
  output x16,
  output x17,
  output x18,
  output x19,
  output x20,
  output x21,
  output x22,
  output x23,
  output x24,
  output x25,
  output x26,
  output x27,
  output x28,
  output x29,
  output x30,
  output x31,
  output x31_2,
  output x32,
  output x33,
  output x34,
  output x35,
  output x36,
  output x37,
  output x38,
  output x39,
  output x40,
  output x41,
  output x42,
  output x43,
  output x44,
  output x45,
  output x46,
  output x47,
  output x48,
  output x49,
  output x50,
  output x51,
  output x52,
  output x53,
  output x54,
  output x55,
  output x56,
  output x57,
  output x58,
  output x59,
  output x60,
  output x61,
  output x62,
  output x63,
  output x64,
  output x65,
  output x66,
  output x67,
  output x68,
  output x69,
  output x70,
  output x71,
  output x72,
  output x73,
  output x74,
  output x75,
  output x76,
  output x77,
  output x78,
  output x79,
  output x80,
  output x81,
  output x82,
  output x83,
  output x84,
  output x85,
  output x86,
  output x87,
  output x88,
  output x89,
  output x90,
  output x91,
  output x92,
  output x93,
  output x94,
  output x95,
  output x96,
  output x97,
  output x98,
  output x99,
  output x100,
  output x101,
  output x102,
  output x103,
  output x104,
  output x105,
  output x106,
  output x107,
  output x108,
  output x109,
  output x110,
  output x111,
  output x112,
  output x113,
  output x114,
  output x115,
  output x116,
  output x117,
  output x118,
  output x119,
  output x120,
  output x121,
  output x122,
  output x123,
  output x124,
  output x125,
  output x126,
  output x127,
  output x128,
  output x129
);

  wire not_1_out, not_2_out, not_3_out, not_4_out, not_5_out, not_6_out, not_7_out, not_8_out, not_10_out,
       not_14_out;

  not not_1 (not_1_out, IR0);
  not not_2 (not_2_out, IR1);
  not not_3 (not_3_out, IR2);
  not not_4 (not_4_out, IR3);
  not not_5 (not_5_out, IR4);
  not not_6 (not_6_out, IR5);
  not not_7 (not_7_out, IR6);
  not not_8 (not_8_out, IR7);
  not not_9 (x33, T0);
  not not_10 (not_10_out, T1X);
  not not_11 (x28, T2);
  not not_12 (x85, T3);
  not not_13 (x84, T4);
  not not_14 (not_14_out, T5);
  and and_1 (x0, IR01, not_3_out, IR5, IR6, not_8_out);
  and and_2 (x1, not_1_out, IR2, IR3, not_5_out, x85);
  and and_3 (x2, not_1_out, IR2, not_4_out, not_5_out, x28);
  and and_4 (x3, IR01, IR2, not_4_out, IR4, IR5, not_8_out, x33);
  and and_5 (x4, IR01, IR2, not_4_out, not_5_out, IR5, IR6, not_8_out, x33);
  and and_6 (x5, IR01, IR4, IR5, not_7_out, not_8_out, x33);
  and and_7 (x6, not_3_out, not_5_out, x28);
  and and_8 (x7, not_2_out, IR6, not_8_out);
  and and_9 (x8, not_1_out, IR2, IR3, IR4, x28);
  and and_10 (x9, not_2_out, IR2, not_4_out, IR4, IR5, IR6, not_8_out, x33);
  and and_11 (x10, not_2_out, IR2, not_4_out, IR4, IR5, not_7_out, not_8_out, x33);
  and and_12 (x11, IR01, IR4, not_6_out, not_7_out, not_8_out, x33);
  and and_13 (x12, not_2_out, IR5, IR6, not_8_out);
  and and_14 (x13, not_2_out, IR2, not_4_out, not_5_out, IR5, IR6, not_8_out, x33);
  and and_15 (x14, not_2_out, not_6_out, IR6, not_8_out, x33);
  and and_16 (x15, not_2_out, IR2, not_4_out, IR4, IR5, not_7_out, not_8_out, not_10_out);
  and and_17 (x16, IR01, IR2, not_4_out, IR4, not_6_out, not_7_out, not_8_out, not_10_out);
  and and_18 (x17, not_2_out, IR2, not_4_out, not_5_out, not_6_out, IR6, not_8_out, x33);
  and and_19 (x18, IR01, IR2, not_4_out, IR4, IR5, not_8_out, not_10_out);
  and and_20 (x19, IR01, not_3_out, not_6_out, IR6, not_8_out, x33);
  and and_21 (x20, IR01, IR4, not_6_out, IR6, not_8_out, x33);
  and and_22 (x21, IR01, IR2, IR3, IR4, not_6_out, IR6, IR7, x33);
  and and_23 (x22, IR01, IR2, IR3, IR4, IR5, IR6, IR7, not_14_out);
  and and_24 (x23, IR01, IR2, not_4_out, IR4, IR5, IR7, x33);
  and and_25 (x24, IR01, IR2, IR3, IR4, not_6_out, not_7_out, IR7, x84);
  and and_26 (x25, IR01, IR2, not_4_out, IR4, not_6_out, IR7, x85);
  and and_27 (x26, IR01, IR2, IR3, IR4, IR5, not_7_out, IR7, not_14_out);
  and and_28 (x27, not_2_out, not_6_out, not_7_out, IR7, x33);
  and and_29 (x29, not_1_out, IR5, not_7_out, IR7, x33);
  and and_30 (x30, IR01, not_3_out, not_4_out, IR4, not_7_out, IR7);
  and and_31 (x31, not_3_out, not_4_out, IR4, x28);
  and and_32 (x31_2, not_1_out, IR5, IR6, IR7, x33);
  and and_33 (x32, IR3, x28);
  and and_34 (x34, IR01, IR2, IR4, IR7, x28);
  and and_35 (x35, IR01, IR4, IR7, x85);
  and and_36 (x36, IR01, IR2, IR3, IR4, IR6, IR7, x84);
  and and_37 (x37, IR01, IR2, IR3, IR4, IR5, not_7_out, IR7, x84);
  and and_38 (x38, not_1_out, IR2, IR3, IR4, x85);
  and and_39 (x39, not_1_out, IR2, IR3, not_5_out, x84);
  and and_40 (x40, not_1_out, IR2, IR3, not_5_out, x28);
  and and_41 (x41, not_4_out, not_5_out, x85);
  and and_42 (x42, IR01, IR2, not_4_out, IR4, not_6_out, IR7);
  and and_43 (x43, not_2_out, not_6_out, not_7_out, not_8_out);
  and and_44 (x44, not_1_out, IR2, IR3, IR4, x84);
  and and_45 (x45, not_1_out, IR2, IR3, not_5_out, x85);
  and and_46 (x46, IR01, IR2, IR3, IR4, not_7_out, IR7);
  and and_47 (x47, IR01, IR2, IR3, IR4, not_6_out, IR6, IR7, x28);
  and and_48 (x48, IR01, IR4, not_7_out, not_8_out, x33);
  and and_49 (x49, not_1_out, IR5, not_7_out, not_8_out, x33);
  and and_50 (x50, not_1_out, not_6_out, not_7_out, not_8_out, x33);
  and and_51 (x51, not_1_out, not_6_out, not_7_out, x33);
  and and_52 (x52, not_2_out, not_6_out, IR6, IR7);
  and and_53 (x53, IR01, not_3_out, not_4_out, IR4, not_7_out, IR7, x85);
  and and_54 (x54, not_2_out, IR6, IR7);
  and and_55 (x55, IR01, IR2, IR3, IR4, not_6_out, IR6, IR7, not_14_out);
  and and_56 (x56, IR01, IR2, IR4, IR7, x28);
  and and_57 (x57, IR01, IR2, not_4_out, not_5_out, IR5, IR6, not_8_out, x33);
  and and_58 (x58, not_1_out, IR7, not_10_out);
  and and_59 (x59, not_1_out, not_6_out, not_7_out, not_10_out);
  and and_60 (x60, not_2_out, IR2, not_4_out, IR4, IR7, not_10_out);
  and and_61 (x61, not_2_out, IR2, not_4_out, IR4, IR5, IR6, not_8_out, x33);
  and and_62 (x62, IR01, IR2, not_4_out, IR4, not_6_out, not_7_out, IR7, x33);
  and and_63 (x63, not_1_out, not_6_out, IR6, not_8_out, x33);
  and and_64 (x64, not_1_out, x33);
  and and_65 (x65, IR01, IR2, not_4_out, IR4, not_6_out, IR6, not_8_out, x33);
  and and_66 (x66, not_2_out, IR2, not_4_out, IR4, IR7, x33);
  and and_67 (x67, not_2_out, IR2, not_4_out, IR4, not_6_out, IR6, not_8_out, x33);
  and and_68 (x68, IR01, not_3_out, IR4, not_6_out, IR6, IR7, x33);
  and and_69 (x69, not_1_out, not_6_out, IR6, IR7, x33);
  and and_70 (x70, not_4_out, not_5_out, x84);
  and and_71 (x71, not_1_out, IR2, IR3, not_5_out, not_14_out);
  and and_72 (x72, IR01, IR2, IR3, not_5_out, x33);
  and and_73 (x73, IR01, IR2, not_4_out, IR4, IR5, not_7_out, IR7, x28);
  and and_74 (x74, not_2_out, IR2, not_4_out, IR4, not_7_out, IR7, x33);
  and and_75 (x75, not_2_out, not_7_out, IR7);
  and and_76 (x76, IR01, IR2, IR3, IR4, IR5, IR6, IR7, x28);
  and and_77 (x77, IR01, IR2, IR3, IR4, not_6_out, IR6, IR7, x85);
  and and_78 (x78, not_1_out, IR5, IR6, not_8_out);
  and and_79 (x79, IR01, IR2, IR3, not_5_out, x28);
  and and_80 (x80, not_3_out, IR3, x28);
  and and_81 (x81, not_1_out, IR2, IR3, x28);
  and and_82 (x82, not_4_out, x28);
  and and_83 (x83, IR01, IR2, IR3, IR4, not_6_out, not_7_out, IR7, not_14_out);
  and and_84 (x86, IR01, IR2, IR3, IR4, IR5, IR7, x33);
  and and_85 (x87, IR01, not_3_out, not_4_out, IR4, not_7_out, IR7, x33);
  and and_86 (x88, not_1_out, IR2, IR3, IR4, not_14_out);
  and and_87 (x89, not_4_out, x85);
  and and_88 (x90, not_1_out, IR2, IR3, not_5_out, x84);
  and and_89 (x91, not_4_out, not_5_out, x85);
  and and_90 (x92, IR01, IR2, IR3, not_5_out, x85);
  and and_91 (x93, IR01, IR2, IR3, IR4, IR5, IR7);
  and and_92 (x94, IR01, IR2, IR3, IR4, not_6_out, IR6, IR7);
  and and_93 (x95, IR01, not_3_out, not_4_out, IR4, not_7_out, IR7);
  and and_94 (x96, IR01, IR2, not_4_out, IR4, IR7);
  and and_95 (x97, IR5, IR6, not_8_out);
  and and_96 (x98, IR01, IR2, IR3, IR4, IR5, IR6, IR7, x84);
  and and_97 (x99, IR01, IR2, not_4_out, IR4, IR5, IR6, IR7, x28);
  and and_98 (x100, IR01, IR2, not_4_out, IR4, IR5, IR7, x28);
  and and_99 (x101, IR01, not_3_out, not_4_out, IR4, not_7_out, IR7, x84);
  and and_100 (x102, IR01, IR2, IR3, IR4, not_7_out, IR7, not_14_out);
  and and_101 (x103, IR01, IR2, IR3, IR4, not_6_out, IR6, IR7, not_14_out);
  and and_102 (x104, IR01, not_3_out, not_4_out, IR4, IR5, not_7_out, IR7, x28);
  and and_103 (x105, IR01, IR2, not_4_out, IR4, not_6_out, IR7, x85);
  and and_104 (x106, not_2_out, not_7_out);
  and and_105 (x107, not_2_out, IR6, IR7);
  and and_106 (x108, IR01, IR2, not_4_out, not_5_out, not_7_out, IR7, x33);
  and and_107 (x109, IR01, not_3_out, IR4, not_6_out, IR6, IR7, not_10_out);
  and and_108 (x110, IR01, IR2, not_4_out, not_5_out, IR6, IR7, x33);
  and and_109 (x111, not_3_out, IR3, not_5_out, x85);
  and and_110 (x112, not_1_out, not_6_out, not_7_out, not_10_out);
  and and_111 (x113, IR01, not_3_out, IR4, not_6_out, IR6, IR7, x33);
  and and_112 (x114, IR01, IR2, not_4_out, IR4, not_6_out, IR6, IR7, x33);
  and and_113 (x115, IR01, IR2, IR3, IR4, IR5, not_7_out, IR7, x84);
  and and_114 (x116, not_1_out, IR5, not_7_out, not_8_out, not_10_out);
  and and_115 (x117, IR01, not_3_out, not_4_out, IR4, not_7_out, not_8_out, not_10_out);
  and and_116 (x118, not_2_out, IR2, not_4_out, IR4, IR6, IR7, not_10_out);
  and and_117 (x119, IR01, IR3, IR4, not_7_out, not_8_out, not_10_out, x28);
  and and_118 (x120, IR01, IR2, not_4_out, IR4, IR7);
  and and_119 (x121, IR01, IR2, not_4_out, not_5_out, not_7_out, not_8_out, x33);
  and and_120 (x123, not_3_out, not_4_out, IR4, x85);
  and and_121 (x124, not_3_out, IR3, IR4, x28);
  and and_122 (x125, not_1_out, IR2, IR3, not_14_out);
  and and_123 (x126, not_4_out, not_5_out, x84);
  and and_124 (x128, IR01, IR2, not_4_out, not_5_out, not_6_out, IR6, not_8_out);
  and and_125 (x129, IR2, not_4_out);

  assign x122 = IR6;
  assign x127 = IR7;
endmodule
