// Digital circuit DL.dig as structural Verilog
module DL (
  input  PHI2,
  input  PHI1,
  input  WR,
  input  DL_ADL,
  input  DL_ADH,
  input  DL_DB,
  input  DB0,
  input  DB1,
  input  DB2,
  input  DB3,
  input  DB4,
  input  DB5,
  input  DB6,
  input  DB7,
  input  D0,
  input  D1,
  input  D2,
  input  D3,
  input  D4,
  input  D5,
  input  D6,
  input  D7,
  output D_out0,
  output D_out1,
  output D_out2,
  output D_out3,
  output D_out4,
  output D_out5,
  output D_out6,
  output D_out7,
  output ADH0,
  output ADH1,
  output ADH2,
  output ADH3,
  output ADH4,
  output ADH5,
  output ADH6,
  output ADH7,
  output ADL0,
  output ADL1,
  output ADL2,
  output ADL3,
  output ADL4,
  output ADL5,
  output ADL6,
  output ADL7,
  output DB_out0,
  output DB_out1,
  output DB_out2,
  output DB_out3,
  output DB_out4,
  output DB_out5,
  output DB_out6,
  output DB_out7,
  output [7:0] DL,
  output [7:0] DOR
);

  wire dlatch_1_nq, notconnected_1_out, notconnected_2_out, notconnected_3_out, notconnected_4_out,
       notconnected_5_out, notconnected_6_out, notconnected_7_out, notconnected_8_out, notconnected_9_out,
       notconnected_10_out, notconnected_11_out, notconnected_12_out, notconnected_13_out,
       notconnected_14_out, notconnected_15_out, notconnected_16_out, notconnected_17_out,
       notconnected_18_out, notconnected_19_out, notconnected_20_out, notconnected_21_out,
       notconnected_22_out, notconnected_23_out, notconnected_24_out, notconnected_25_out,
       notconnected_26_out, notconnected_27_out, notconnected_28_out, notconnected_29_out,
       notconnected_30_out, notconnected_31_out, notconnected_32_out, RD;

  DLATCH dlatch_1 (.C(PHI1), .D(WR), .nQ(dlatch_1_nq));  // open: Q
  Multiplexer multiplexer_1 (.sel(PHI2), .in_0(dlatch_1_nq), .in_1(1'b1), .out(RD));
  DL_BIT dl_bit_1 (
    .PHI1(PHI1), .PHI2(PHI2), .in_15(notconnected_1_out), .DL_ADL(DL_ADL), .DL_ADH(DL_ADH), .DL_DB(DL_DB),
    .in_16(notconnected_2_out), .RD(RD), .in_17(notconnected_3_out), .DBx_in(DB0),
    .in_18(notconnected_4_out), .Dx_in(D0), .DBx(DB_out0), .ADLx(ADL0), .ADHx(ADH0), .Dx(D_out0),
    .Debug(DOR[0]), .DL(DL[0]));
  // NotConnected on notconnected_1_out
  // NotConnected on notconnected_2_out
  // NotConnected on notconnected_3_out
  // NotConnected on notconnected_4_out
  DL_BIT dl_bit_2 (
    .PHI1(PHI1), .PHI2(PHI2), .in_15(notconnected_5_out), .DL_ADL(DL_ADL), .DL_ADH(DL_ADH), .DL_DB(DL_DB),
    .in_16(notconnected_6_out), .RD(RD), .in_17(notconnected_7_out), .DBx_in(DB1),
    .in_18(notconnected_8_out), .Dx_in(D1), .DBx(DB_out1), .ADLx(ADL1), .ADHx(ADH1), .Dx(D_out1),
    .Debug(DOR[1]), .DL(DL[1]));
  // NotConnected on notconnected_5_out
  // NotConnected on notconnected_6_out
  // NotConnected on notconnected_7_out
  // NotConnected on notconnected_8_out
  DL_BIT dl_bit_3 (
    .PHI1(PHI1), .PHI2(PHI2), .in_15(notconnected_9_out), .DL_ADL(DL_ADL), .DL_ADH(DL_ADH), .DL_DB(DL_DB),
    .in_16(notconnected_10_out), .RD(RD), .in_17(notconnected_11_out), .DBx_in(DB2),
    .in_18(notconnected_12_out), .Dx_in(D2), .DBx(DB_out2), .ADLx(ADL2), .ADHx(ADH2), .Dx(D_out2),
    .Debug(DOR[2]), .DL(DL[2]));
  // NotConnected on notconnected_9_out
  // NotConnected on notconnected_10_out
  // NotConnected on notconnected_11_out
  // NotConnected on notconnected_12_out
  DL_BIT dl_bit_4 (
    .PHI1(PHI1), .PHI2(PHI2), .in_15(notconnected_13_out), .DL_ADL(DL_ADL), .DL_ADH(DL_ADH), .DL_DB(DL_DB),
    .in_16(notconnected_14_out), .RD(RD), .in_17(notconnected_15_out), .DBx_in(DB3),
    .in_18(notconnected_16_out), .Dx_in(D3), .DBx(DB_out3), .ADLx(ADL3), .ADHx(ADH3), .Dx(D_out3),
    .Debug(DOR[3]), .DL(DL[3]));
  // NotConnected on notconnected_13_out
  // NotConnected on notconnected_14_out
  // NotConnected on notconnected_15_out
  // NotConnected on notconnected_16_out
  DL_BIT dl_bit_5 (
    .PHI1(PHI1), .PHI2(PHI2), .in_15(notconnected_17_out), .DL_ADL(DL_ADL), .DL_ADH(DL_ADH), .DL_DB(DL_DB),
    .in_16(notconnected_18_out), .RD(RD), .in_17(notconnected_19_out), .DBx_in(DB4),
    .in_18(notconnected_20_out), .Dx_in(D4), .DBx(DB_out4), .ADLx(ADL4), .ADHx(ADH4), .Dx(D_out4),
    .Debug(DOR[4]), .DL(DL[4]));
  // NotConnected on notconnected_17_out
  // NotConnected on notconnected_18_out
  // NotConnected on notconnected_19_out
  // NotConnected on notconnected_20_out
  DL_BIT dl_bit_6 (
    .PHI1(PHI1), .PHI2(PHI2), .in_15(notconnected_21_out), .DL_ADL(DL_ADL), .DL_ADH(DL_ADH), .DL_DB(DL_DB),
    .in_16(notconnected_22_out), .RD(RD), .in_17(notconnected_23_out), .DBx_in(DB5),
    .in_18(notconnected_24_out), .Dx_in(D5), .DBx(DB_out5), .ADLx(ADL5), .ADHx(ADH5), .Dx(D_out5),
    .Debug(DOR[5]), .DL(DL[5]));
  // NotConnected on notconnected_21_out
  // NotConnected on notconnected_22_out
  // NotConnected on notconnected_23_out
  // NotConnected on notconnected_24_out
  DL_BIT dl_bit_7 (
    .PHI1(PHI1), .PHI2(PHI2), .in_15(notconnected_25_out), .DL_ADL(DL_ADL), .DL_ADH(DL_ADH), .DL_DB(DL_DB),
    .in_16(notconnected_26_out), .RD(RD), .in_17(notconnected_27_out), .DBx_in(DB6),
    .in_18(notconnected_28_out), .Dx_in(D6), .DBx(DB_out6), .ADLx(ADL6), .ADHx(ADH6), .Dx(D_out6),
    .Debug(DOR[6]), .DL(DL[6]));
  // NotConnected on notconnected_25_out
  // NotConnected on notconnected_26_out
  // NotConnected on notconnected_27_out
  // NotConnected on notconnected_28_out
  DL_BIT dl_bit_8 (
    .PHI1(PHI1), .PHI2(PHI2), .in_15(notconnected_29_out), .DL_ADL(DL_ADL), .DL_ADH(DL_ADH), .DL_DB(DL_DB),
    .in_16(notconnected_30_out), .RD(RD), .in_17(notconnected_31_out), .DBx_in(DB7),
    .in_18(notconnected_32_out), .Dx_in(D7), .DBx(DB_out7), .ADLx(ADL7), .ADHx(ADH7), .Dx(D_out7),
    .Debug(DOR[7]), .DL(DL[7]));
  // NotConnected on notconnected_29_out
  // NotConnected on notconnected_30_out
  // NotConnected on notconnected_31_out
  // NotConnected on notconnected_32_out
endmodule
