// Digital circuit DL_BIT.dig as structural Verilog
module DL_BIT (
  input  PHI1,
  input  PHI2,
  input  DL_ADL,
  input  DL_ADH,
  input  DL_DB,
  input  RD,
  input  DBx_in,
  input  Dx_in,
  input  in_15,
  input  in_16,
  input  in_17,
  input  in_18,
  output ADLx,
  output ADHx,
  output DBx,
  output Dx,
  output Debug,
  output DL
);

  wire and_1_out, and_2_out, and_3_out, not_1_out, not_2_out, not_3_out;

  not not_1 (not_1_out, Dx_in);
  not not_2 (not_2_out, DBx_in);
  DLATCH dlatch_1 (.C(PHI2), .D(not_1_out), .nQ(DL));  // open: Q
  DLATCH dlatch_2 (.C(PHI1), .D(not_2_out), .nQ(Debug));  // open: Q
  and and_1 (and_1_out, DL_ADL, PHI1);
  and and_2 (and_2_out, DL_ADH, PHI1);
  and and_3 (and_3_out, DL_DB, PHI1);
  not not_3 (not_3_out, RD);
  assign ADLx = and_1_out ? DL : 1'bz;  // Driver driver_1
  assign ADHx = and_2_out ? DL : 1'bz;  // Driver driver_2
  assign DBx = and_3_out ? DL : 1'bz;  // Driver driver_3
  assign Dx = not_3_out ? Debug : 1'bz;  // Driver driver_4
endmodule
