// Digital circuit DispCompletionUnit.dig as structural Verilog
module DispCompletionUnit (
  input  PHI1,
  input  PHI2,
  input  nready,
  input  ACRL1,
  input  D91,
  input  D92,
  input  REST,
  input  BRK6E,
  input  RESP,
  input  nSHIFT,
  input  nMemOP,
  input  T7,
  input  D96,
  input  D100,
  input  D101,
  input  D102,
  input  D103,
  input  D104,
  input  D105,
  input  T0,
  input  nBRTAKEN,
  input  T1,
  input  BR2,
  input  BR3,
  output TRES2,
  output nTRESX,
  output ENDS
);

  wire and_1_out, dlatch_1_q, dlatch_2_q, dlatch_3_q, dlatch_4_nq, multiplexer_1_out, nor_1_out, nor_2_out,
       nor_3_out, nor_4_out, nor_6_out, nor_7_out, nor_8_out, nor_9_out, not_1_out, not_2_out, not_3_out;

  nor nor_1 (nor_1_out, D91, D92);
  nor nor_2 (nor_2_out, D100, D101, D102, D103, D104, D105);
  not not_1 (not_1_out, nor_2_out);
  and and_1 (and_1_out, nBRTAKEN, BR2);
  nor nor_3 (nor_3_out, T0, and_1_out);
  not not_2 (not_2_out, T1);
  Multiplexer multiplexer_1 (.sel(nready), .in_0(nor_3_out), .in_1(not_2_out), .out(multiplexer_1_out));
  not not_3 (not_3_out, nSHIFT);
  DLATCH dlatch_1 (.C(PHI2), .D(nor_1_out), .Q(dlatch_1_q));  // open: nQ
  nor nor_4 (nor_4_out, D96, not_3_out, nMemOP);
  DLATCH dlatch_2 (.C(PHI2), .D(multiplexer_1_out), .Q(dlatch_2_q));  // open: nQ
  DLATCH dlatch_3 (.C(PHI2), .D(RESP), .Q(dlatch_3_q));  // open: nQ
  nor nor_5 (ENDS, dlatch_2_q, dlatch_3_q);
  nor nor_6 (nor_6_out, nor_4_out, T7, not_1_out, BR3);
  nor nor_7 (nor_7_out, ACRL1, dlatch_1_q, nready, REST);
  nor nor_8 (nor_8_out, nready, nor_6_out);
  nor nor_9 (nor_9_out, RESP, ENDS, nor_8_out);
  nor nor_10 (nTRESX, nor_7_out, BRK6E, dlatch_4_nq);
  DLATCH dlatch_4 (.C(PHI2), .D(nor_9_out), .nQ(dlatch_4_nq));  // open: Q
  DLATCH dlatch_5 (.C(PHI1), .D(nTRESX), .nQ(TRES2));  // open: Q
endmodule
