// Digital circuit DispIncrementPC.dig as structural Verilog
module DispIncrementPC (
  input  PHI1,
  input  PHI2,
  input  B_OUT,
  input  NotReadyPhi1,
  input  BRFW,
  input  ACR,
  input  nready,
  input  nBRTAKEN,
  input  nADL_PCL,
  input  nIMPLIED,
  input  BR2,
  input  BR3,
  output BRA,
  output nIPC
);

  wire and_1_out, dlatch_1_nq, dlatch_2_q, dlatch_3_q, dlatch_4_q, dlatch_5_q, nor_1_out, nor_2_out,
       nor_3_out, nor_4_out, nor_5_out, not_1_out, not_2_out, not_3_out, not_4_out, or_1_out, xor_1_out;

  nor nor_1 (nor_1_out, BR2, BR3);
  not not_1 (not_1_out, nIMPLIED);
  not not_2 (not_2_out, nor_1_out);
  and and_1 (and_1_out, nBRTAKEN, BR2);
  nor nor_2 (nor_2_out, nADL_PCL, not_2_out);
  not not_3 (not_3_out, BR3);
  nor nor_3 (nor_3_out, not_3_out, NotReadyPhi1);
  nor nor_4 (nor_4_out, and_1_out, nor_2_out);
  not not_4 (not_4_out, ACR);
  DLATCH dlatch_1 (.C(PHI2), .D(nor_3_out), .nQ(dlatch_1_nq));  // open: Q
  xor xor_1 (xor_1_out, BRFW, not_4_out);
  DLATCH dlatch_2 (.C(PHI2), .D(nor_4_out), .Q(dlatch_2_q));  // open: nQ
  and and_2 (BRA, ~dlatch_1_nq, xor_1_out);  // And
  nor nor_5 (nor_5_out, nready, dlatch_2_q, not_1_out);
  DLATCH dlatch_3 (.C(PHI1), .D(B_OUT), .Q(dlatch_3_q));  // open: nQ
  DLATCH dlatch_4 (.C(PHI1), .D(BRA), .Q(dlatch_4_q));  // open: nQ
  DLATCH dlatch_5 (.C(PHI1), .D(nor_5_out), .Q(dlatch_5_q));  // open: nQ
  or or_1 (or_1_out, dlatch_4_q, dlatch_5_q);
  nand nand_1 (nIPC, dlatch_3_q, or_1_out);
endmodule
