// Digital circuit DispReadyRW.dig as structural Verilog
module DispReadyRW (
  input  PHI1,
  input  PHI2,
  input  RDY,
  input  STOR,
  input  PC_DB,
  input  D98,
  input  D100,
  input  T6,
  input  T7,
  input  DORES,
  output nready,
  output NotReadyPhi1,
  output WR
);

  wire dlatch_1_q, dlatch_2_nq, dlatch_3_q, dlatch_4_nq, nor_1_out, nor_2_out;

  nor nor_1 (nor_1_out, STOR, PC_DB, D98, D100, T6, T7);
  DLATCH dlatch_1 (.C(PHI2), .D(nor_1_out), .Q(dlatch_1_q));  // open: nQ
  nor nor_2 (nor_2_out, RDY, dlatch_3_q);
  nor nor_3 (WR, nready, dlatch_1_q, DORES);
  DLATCH dlatch_2 (.C(PHI2), .D(nor_2_out), .nQ(dlatch_2_nq));  // open: Q
  DLATCH dlatch_3 (.C(PHI1), .D(WR), .Q(dlatch_3_q));  // open: nQ
  not not_1 (nready, dlatch_2_nq);
  DLATCH dlatch_4 (.C(PHI1), .D(nready), .nQ(dlatch_4_nq));  // open: Q
  DLATCH dlatch_5 (.C(PHI2), .D(dlatch_4_nq), .nQ(NotReadyPhi1));  // open: Q
endmodule
