// Digital circuit DispShortCycle.dig as structural Verilog
module DispShortCycle (
  input  PHI1,
  input  PHI2,
  input  nready,
  input  RESP,
  input  BRA,
  input  ENDS,
  input  nTWOCYCLE,
  input  nTRESX,
  output T1,
  output nT0,
  output T0,
  output nT1X
);

  wire and_1_out, dlatch_1_q, dlatch_2_q, dlatch_3_q, dlatch_4_q, dlatch_5_q, dlatch_6_q, dlatch_8_q,
       dlatch_9_q, nor_1_out, nor_2_out, nor_4_out, nor_5_out, nor_6_out, nor_7_out, nor_8_out, not_1_out,
       not_2_out;

  not not_1 (not_1_out, nready);
  DLATCH dlatch_1 (.C(PHI1), .D(not_2_out), .Q(dlatch_1_q));  // open: nQ
  DLATCH dlatch_2 (.C(PHI1), .D(nTWOCYCLE), .Q(dlatch_2_q));  // open: nQ
  DLATCH dlatch_3 (.C(PHI1), .D(nTRESX), .Q(dlatch_3_q));  // open: nQ
  DLATCH dlatch_4 (.C(PHI1), .D(not_1_out), .Q(dlatch_4_q));  // open: nQ
  and and_1 (and_1_out, dlatch_2_q, dlatch_3_q);
  nor nor_1 (nor_1_out, dlatch_1_q, and_1_out);
  nor nor_2 (nor_2_out, dlatch_8_q, dlatch_9_q);
  nor nor_3 (nT0, nor_1_out, nor_2_out);
  nor nor_4 (nor_4_out, dlatch_8_q, nready);
  nor nor_5 (nor_5_out, RESP, dlatch_4_q, dlatch_6_q);
  nor nor_6 (nor_6_out, dlatch_5_q, BRA);
  nor nor_7 (nor_7_out, nor_6_out, nready);
  nor nor_8 (nor_8_out, nor_7_out, ENDS);
  DLATCH dlatch_5 (.C(PHI2), .D(nor_5_out), .Q(dlatch_5_q));  // open: nQ
  DLATCH dlatch_6 (.C(PHI1), .D(nor_6_out), .Q(dlatch_6_q));  // open: nQ
  DLATCH dlatch_7 (.C(PHI1), .D(nor_8_out), .nQ(T1));  // open: Q
  DLATCH dlatch_8 (.C(PHI2), .D(nT0), .Q(dlatch_8_q));  // open: nQ
  DLATCH dlatch_9 (.C(PHI1), .D(nor_4_out), .Q(dlatch_9_q), .nQ(nT1X));
  not not_2 (not_2_out, nor_8_out);
  not not_3 (T0, nT0);
endmodule
