// Digital circuit FLAGS.dig as structural Verilog
module FLAGS (
  input  P_DB,
  input  B_OUT,
  input  DB0,
  input  DB1,
  input  DB2,
  input  DB3,
  input  DB4,
  input  DB5,
  input  DB6,
  input  DB7,
  input  DB_P,
  input  DBZ_Z,
  input  DB_N,
  input  IR5_C,
  input  ACR,
  input  DB_C,
  input  ACR_C,
  input  IR5_D,
  input  PHI1,
  input  PHI2,
  input  nIR5,
  input  IR5_I,
  input  BRK6E,
  input  AVR,
  input  DB_V,
  input  D112,
  input  Z_V,
  input  SO,
  output DB_out0,
  output DB_out1,
  output DB_out2,
  output DB_out3,
  output DB_out4,
  output DB_out5,
  output DB_out6,
  output DB_out7,
  output nC_OUT,
  output nN_OUT,
  output nZ_OUT,
  output nV_OUT,
  output nI_OUT,
  output nD_OUT
);

  wire and_1_out, and_2_out, and_3_out, and_4_out, and_5_out, and_6_out, and_7_out, and_8_out, and_9_out,
       and_10_out, and_11_out, and_12_out, and_13_out, and_14_out, and_15_out, and_16_out, and_17_out,
       and_18_out, dlatch_1_q, dlatch_2_nq, dlatch_3_nq, dlatch_4_q, dlatch_6_q, dlatch_8_q, dlatch_10_q,
       dlatch_12_q, dlatch_13_nq, dlatch_14_q, dlatch_16_q, dlatch_17_q, nor_1_out, nor_2_out, nor_3_out,
       nor_4_out, nor_5_out, nor_6_out, nor_7_out, nor_8_out, nor_9_out, nor_10_out, nor_11_out, nor_12_out,
       nor_13_out, not_1_out, not_2_out, not_3_out, not_4_out, not_5_out, not_6_out, not_7_out, not_8_out,
       not_9_out, not_10_out, not_11_out, not_12_out, not_13_out, not_14_out, not_15_out, not_16_out,
       not_17_out;

  not not_1 (not_1_out, SO);
  DLATCH dlatch_1 (.C(PHI2), .D(D112), .Q(dlatch_1_q));  // open: nQ
  nor nor_1 (nor_1_out, DB0, DB1, DB2, DB3, DB4, DB5, DB6, DB7);
  not not_2 (not_2_out, DB1);
  not not_3 (not_3_out, nor_1_out);
  not not_4 (not_4_out, DB7);
  nor nor_2 (nor_2_out, IR5_D, DB_P);
  DLATCH dlatch_2 (.C(PHI1), .D(not_1_out), .nQ(dlatch_2_nq));  // open: Q
  nor nor_3 (nor_3_out, DB_P, DBZ_Z);
  nor nor_4 (nor_4_out, DB_C, IR5_C, ACR_C);
  nor nor_5 (nor_5_out, DB_P, IR5_I);
  nor nor_6 (nor_6_out, DB_V, dlatch_1_q, dlatch_17_q);
  not not_5 (not_5_out, DB_N);
  not not_6 (not_6_out, ACR);
  not not_7 (not_7_out, DB0);
  not not_8 (not_8_out, DB3);
  not not_9 (not_9_out, DB2);
  not not_10 (not_10_out, AVR);
  not not_11 (not_11_out, DB7);
  and and_1 (and_1_out, not_2_out, DB_P);
  and and_2 (and_2_out, not_3_out, DBZ_Z);
  and and_3 (and_3_out, nor_3_out, dlatch_6_q);
  and and_4 (and_4_out, not_4_out, DB_N);
  and and_5 (and_5_out, not_5_out, dlatch_8_q);
  and and_6 (and_6_out, nIR5, IR5_C);
  and and_7 (and_7_out, not_6_out, ACR_C);
  and and_8 (and_8_out, not_7_out, DB_C);
  and and_9 (and_9_out, nor_4_out, dlatch_10_q);
  and and_10 (and_10_out, IR5_D, nIR5);
  and and_11 (and_11_out, not_8_out, DB_P);
  and and_12 (and_12_out, nor_2_out, dlatch_12_q);
  and and_13 (and_13_out, nIR5, IR5_I);
  and and_14 (and_14_out, not_9_out, DB_P);
  and and_15 (and_15_out, nor_5_out, dlatch_14_q);
  and and_16 (and_16_out, not_10_out, dlatch_1_q);
  and and_17 (and_17_out, not_11_out, DB_V);
  and and_18 (and_18_out, nor_6_out, dlatch_16_q);
  DLATCH dlatch_3 (.C(PHI2), .D(dlatch_2_nq), .nQ(dlatch_3_nq));  // open: Q
  DLATCH dlatch_4 (.C(PHI1), .D(dlatch_3_nq), .Q(dlatch_4_q));  // open: nQ
  nor nor_7 (nor_7_out, and_1_out, and_2_out, and_3_out);
  nor nor_8 (nor_8_out, and_4_out, and_5_out);
  nor nor_9 (nor_9_out, and_6_out, and_7_out, and_8_out, and_9_out);
  nor nor_10 (nor_10_out, and_10_out, and_11_out, and_12_out);
  nor nor_11 (nor_11_out, and_13_out, and_14_out, and_15_out);
  nor nor_12 (nor_12_out, and_16_out, and_17_out, and_18_out, Z_V);
  nor nor_13 (nor_13_out, dlatch_4_q, dlatch_2_nq);
  DLATCH dlatch_5 (.C(PHI1), .D(nor_7_out), .nQ(nZ_OUT));  // open: Q
  DLATCH dlatch_6 (.C(PHI2), .D(nZ_OUT), .Q(dlatch_6_q));  // open: nQ
  DLATCH dlatch_7 (.C(PHI1), .D(nor_8_out), .nQ(nN_OUT));  // open: Q
  DLATCH dlatch_8 (.C(PHI2), .D(nN_OUT), .Q(dlatch_8_q));  // open: nQ
  DLATCH dlatch_9 (.C(PHI1), .D(nor_9_out), .nQ(nC_OUT));  // open: Q
  DLATCH dlatch_10 (.C(PHI2), .D(nC_OUT), .Q(dlatch_10_q));  // open: nQ
  DLATCH dlatch_11 (.C(PHI1), .D(nor_10_out), .nQ(nD_OUT));  // open: Q
  DLATCH dlatch_12 (.C(PHI2), .D(nD_OUT), .Q(dlatch_12_q));  // open: nQ
  DLATCH dlatch_13 (.C(PHI1), .D(nor_11_out), .nQ(dlatch_13_nq));  // open: Q
  DLATCH dlatch_14 (.C(PHI2), .D(nI_OUT), .Q(dlatch_14_q));  // open: nQ
  DLATCH dlatch_15 (.C(PHI1), .D(nor_12_out), .nQ(nV_OUT));  // open: Q
  DLATCH dlatch_16 (.C(PHI2), .D(nV_OUT), .Q(dlatch_16_q));  // open: nQ
  DLATCH dlatch_17 (.C(PHI2), .D(nor_13_out), .Q(dlatch_17_q));  // open: nQ
  and and_19 (nI_OUT, ~BRK6E, dlatch_13_nq);  // And
  // NotConnected on DB_out5
  not not_12 (not_12_out, nC_OUT);
  not not_13 (not_13_out, nZ_OUT);
  not not_14 (not_14_out, nI_OUT);
  not not_15 (not_15_out, nD_OUT);
  not not_16 (not_16_out, nV_OUT);
  not not_17 (not_17_out, nN_OUT);
  assign DB_out0 = P_DB ? not_12_out : 1'bz;  // Driver driver_1
  assign DB_out1 = P_DB ? not_13_out : 1'bz;  // Driver driver_2
  assign DB_out2 = P_DB ? not_14_out : 1'bz;  // Driver driver_3
  assign DB_out3 = P_DB ? not_15_out : 1'bz;  // Driver driver_4
  assign DB_out4 = P_DB ? B_OUT : 1'bz;  // Driver driver_5
  assign DB_out6 = P_DB ? not_16_out : 1'bz;  // Driver driver_6
  assign DB_out7 = P_DB ? not_17_out : 1'bz;  // Driver driver_7

  // Other names for the same wires on the sheet: DB6_t = DB7
endmodule
