// Digital circuit NMI_FF.dig as structural Verilog
module NMI_FF (
  input  nNMI,
  input  PHI2,
  output NMIP
);

  wire and_1_out, and_2_out, nor_1_out, nor_2_out, not_1_out;

  not not_1 (not_1_out, nNMI);
  and and_1 (and_1_out, not_1_out, PHI2);
  and and_2 (and_2_out, nNMI, PHI2);
  nor nor_1 (nor_1_out, and_2_out, nor_2_out);
  nor nor_2 (nor_2_out, and_1_out, nor_1_out);
  not not_2 (NMIP, nor_2_out);
endmodule
