// Digital circuit PCH.dig as structural Verilog
module PCH (
  input  ADH_PCH,
  input  PCH_PCH,
  input  PCH_ADH,
  input  PCH_DB,
  input  cin,
  input  ADH0,
  input  ADH1,
  input  ADH2,
  input  ADH3,
  input  ADH4,
  input  ADH5,
  input  ADH6,
  input  ADH7,
  input  PHI2,
  output [7:0] PCSH_Debug,
  output [7:0] PCH_Debug,
  output ADH0_out,
  output ADH1_out,
  output ADH2_out,
  output ADH3_out,
  output ADH4_out,
  output ADH5_out,
  output ADH6_out,
  output ADH7_out,
  output DB0,
  output DB1,
  output DB2,
  output DB3,
  output DB4,
  output DB5,
  output DB6,
  output DB7
);

  wire nor_1_out, not_1_out, notconnected_1_out, notconnected_2_out, notconnected_3_out, notconnected_4_out,
       notconnected_5_out, notconnected_6_out, notconnected_7_out, notconnected_8_out, notconnected_9_out,
       notconnected_10_out, notconnected_11_out, notconnected_12_out, notconnected_13_out,
       notconnected_14_out, notconnected_15_out, notconnected_16_out, notconnected_17_out,
       notconnected_18_out, notconnected_19_out, notconnected_20_out, notconnected_21_out,
       notconnected_22_out, notconnected_23_out, notconnected_24_out, pch_even_bit_1_cout,
       pch_even_bit_1_sout, pch_even_bit_2_cout, pch_even_bit_2_sout, pch_even_bit_3_cout,
       pch_even_bit_4_cout, pch_odd_bit_1_cout, pch_odd_bit_1_sout, pch_odd_bit_2_sout, pch_odd_bit_3_cout;

  not not_1 (not_1_out, cin);
  PCH_EVEN_BIT pch_even_bit_1 (
    .PHI2(PHI2), .in_14(notconnected_1_out), .cin(cin), .in_15(notconnected_2_out), .ADH_PCH(ADH_PCH),
    .PCH_PCH(PCH_PCH), .PCH_ADH(PCH_ADH), .PCH_DB(PCH_DB), .in_16(notconnected_3_out), .ADHx_in(ADH0),
    .ADHx_out(ADH0_out), .DBx(DB0), .cout(pch_even_bit_1_cout), .sout(pch_even_bit_1_sout),
    .PCH_Debug(PCH_Debug[0]), .PCHS_Debug(PCSH_Debug[0]));
  // NotConnected on notconnected_1_out
  // NotConnected on notconnected_2_out
  // NotConnected on notconnected_3_out
  PCH_ODD_BIT pch_odd_bit_1 (
    .PHI2(PHI2), .in_14(notconnected_4_out), .cin(pch_even_bit_1_cout), .in_15(notconnected_5_out),
    .ADH_PCH(ADH_PCH), .PCH_PCH(PCH_PCH), .PCH_ADH(PCH_ADH), .PCH_DB(PCH_DB), .in_16(notconnected_6_out),
    .ADHx_in(ADH1), .ADHx_out(ADH1_out), .DBx(DB1), .cout(pch_odd_bit_1_cout), .sout(pch_odd_bit_1_sout),
    .PCH_Debug(PCH_Debug[1]), .PCHS_Debug(PCSH_Debug[1]));
  // NotConnected on notconnected_4_out
  // NotConnected on notconnected_5_out
  // NotConnected on notconnected_6_out
  PCH_EVEN_BIT pch_even_bit_2 (
    .PHI2(PHI2), .in_14(notconnected_7_out), .cin(pch_odd_bit_1_cout), .in_15(notconnected_8_out),
    .ADH_PCH(ADH_PCH), .PCH_PCH(PCH_PCH), .PCH_ADH(PCH_ADH), .PCH_DB(PCH_DB), .in_16(notconnected_9_out),
    .ADHx_in(ADH2), .ADHx_out(ADH2_out), .DBx(DB2), .cout(pch_even_bit_2_cout), .sout(pch_even_bit_2_sout),
    .PCH_Debug(PCH_Debug[2]), .PCHS_Debug(PCSH_Debug[2]));
  // NotConnected on notconnected_7_out
  // NotConnected on notconnected_8_out
  // NotConnected on notconnected_9_out
  PCH_ODD_BIT pch_odd_bit_2 (
    .PHI2(PHI2), .in_14(notconnected_10_out), .cin(pch_even_bit_2_cout), .in_15(notconnected_11_out),
    .ADH_PCH(ADH_PCH), .PCH_PCH(PCH_PCH), .PCH_ADH(PCH_ADH), .PCH_DB(PCH_DB), .in_16(notconnected_12_out),
    .ADHx_in(ADH3), .ADHx_out(ADH3_out), .DBx(DB3), .sout(pch_odd_bit_2_sout), .PCH_Debug(PCH_Debug[3]),
    .PCHS_Debug(PCSH_Debug[3]));  // open: cout
  // NotConnected on notconnected_10_out
  // NotConnected on notconnected_11_out
  // NotConnected on notconnected_12_out
  PCH_EVEN_BIT pch_even_bit_3 (
    .PHI2(PHI2), .in_14(notconnected_13_out), .cin(nor_1_out), .in_15(notconnected_14_out),
    .ADH_PCH(ADH_PCH), .PCH_PCH(PCH_PCH), .PCH_ADH(PCH_ADH), .PCH_DB(PCH_DB), .in_16(notconnected_15_out),
    .ADHx_in(ADH4), .ADHx_out(ADH4_out), .DBx(DB4), .cout(pch_even_bit_3_cout), .PCH_Debug(PCH_Debug[4]),
    .PCHS_Debug(PCSH_Debug[4]));  // open: sout
  // NotConnected on notconnected_13_out
  // NotConnected on notconnected_14_out
  // NotConnected on notconnected_15_out
  PCH_ODD_BIT pch_odd_bit_3 (
    .PHI2(PHI2), .in_14(notconnected_16_out), .cin(pch_even_bit_3_cout), .in_15(notconnected_17_out),
    .ADH_PCH(ADH_PCH), .PCH_PCH(PCH_PCH), .PCH_ADH(PCH_ADH), .PCH_DB(PCH_DB), .in_16(notconnected_18_out),
    .ADHx_in(ADH5), .ADHx_out(ADH5_out), .DBx(DB5), .cout(pch_odd_bit_3_cout), .PCH_Debug(PCH_Debug[5]),
    .PCHS_Debug(PCSH_Debug[5]));  // open: sout
  // NotConnected on notconnected_16_out
  // NotConnected on notconnected_17_out
  // NotConnected on notconnected_18_out
  PCH_EVEN_BIT pch_even_bit_4 (
    .PHI2(PHI2), .in_14(notconnected_19_out), .cin(pch_odd_bit_3_cout), .in_15(notconnected_20_out),
    .ADH_PCH(ADH_PCH), .PCH_PCH(PCH_PCH), .PCH_ADH(PCH_ADH), .PCH_DB(PCH_DB), .in_16(notconnected_21_out),
    .ADHx_in(ADH6), .ADHx_out(ADH6_out), .DBx(DB6), .cout(pch_even_bit_4_cout), .PCH_Debug(PCH_Debug[6]),
    .PCHS_Debug(PCSH_Debug[6]));  // open: sout
  // NotConnected on notconnected_19_out
  // NotConnected on notconnected_20_out
  // NotConnected on notconnected_21_out
  PCH_ODD_BIT pch_odd_bit_4 (
    .PHI2(PHI2), .in_14(notconnected_22_out), .cin(pch_even_bit_4_cout), .in_15(notconnected_23_out),
    .ADH_PCH(ADH_PCH), .PCH_PCH(PCH_PCH), .PCH_ADH(PCH_ADH), .PCH_DB(PCH_DB), .in_16(notconnected_24_out),
    .ADHx_in(ADH7), .ADHx_out(ADH7_out), .DBx(DB7), .PCH_Debug(PCH_Debug[7]), .PCHS_Debug(PCSH_Debug[7]));  // open: cout, sout
  // NotConnected on notconnected_22_out
  // NotConnected on notconnected_23_out
  // NotConnected on notconnected_24_out
  nor nor_1 (nor_1_out, not_1_out, pch_even_bit_1_sout, pch_odd_bit_1_sout, pch_even_bit_2_sout, pch_odd_bit_2_sout);
endmodule
