// Digital circuit PC_SETUP.dig as structural Verilog
module PC_SETUP (
  input  PHI1,
  input  PHI2,
  input  D77,
  input  D78,
  input  D83,
  input  D84,
  input  D94,
  input  D95,
  input  D96,
  input  D129,
  input  nready,
  input  BR3,
  input  BR2,
  input  T0,
  input  T1,
  input  BR0,
  input  D56,
  output nPCH_PCH,
  output PCH_PCH,
  output ADH_PCH,
  output DL_PCH,
  output nADL_PCL,
  output ADL_PCL,
  output PCL_PCL,
  output PCH_ADH,
  output PCL_ADL,
  output PCH_DB,
  output PCL_DB,
  output PC_DB
);

  wire and_1_out, and_2_out, dlatch_1_q, dlatch_2_q, dlatch_3_nq, dlatch_4_nq, dlatch_5_nq, dlatch_6_nq,
       dlatch_7_nq, dlatch_8_q, dlatch_9_q, dlatch_10_q, dlatch_11_q, nor_1_out, nor_2_out, nor_3_out,
       nor_4_out, nor_5_out, nor_8_out, nor_9_out, nor_10_out, nor_11_out, nor_12_out, nor_13_out,
       nor_14_out, nor_15_out, not_1_out, not_2_out, not_3_out, not_5_out;

  nor nor_1 (nor_1_out, D94, D95, D96);
  nor nor_2 (nor_2_out, D77, D78);
  and and_1 (and_1_out, D83, ~D129);  // And
  DLATCH dlatch_1 (.C(PHI2), .D(nor_2_out), .Q(dlatch_1_q));  // open: nQ
  DLATCH dlatch_2 (.C(PHI1), .D(nready), .Q(dlatch_2_q));  // open: nQ
  nor nor_3 (nor_3_out, dlatch_1_q, nready);
  nor nor_4 (nor_4_out, nor_1_out, dlatch_2_q);
  not not_1 (not_1_out, dlatch_2_q);
  not not_2 (not_2_out, T0);
  nor nor_5 (nor_5_out, nor_4_out, not_2_out);
  nor nor_6 (DL_PCH, not_2_out, nor_1_out);
  and and_2 (and_2_out, not_1_out, BR3);
  DLATCH dlatch_3 (.C(PHI1), .D(nor_3_out), .nQ(dlatch_3_nq));  // open: Q
  not not_3 (not_3_out, nor_8_out);
  nor nor_7 (nADL_PCL, not_3_out, D84, T0, and_2_out);
  nand nand_1 (PC_DB, dlatch_3_nq, nor_2_out);
  nor nor_8 (nor_8_out, T1, D56, and_1_out, nor_5_out, BR2);
  nor nor_9 (nor_9_out, D84, and_1_out, T0, T1, BR2, BR3);
  nor nor_10 (nor_10_out, nor_8_out, DL_PCH, BR0);
  not not_4 (nPCH_PCH, nor_9_out);
  nor nor_11 (nor_11_out, nor_10_out, BR3);
  not not_5 (not_5_out, nADL_PCL);
  DLATCH dlatch_4 (.C(PHI2), .D(dlatch_3_nq), .nQ(dlatch_4_nq));  // open: Q
  DLATCH dlatch_5 (.C(PHI2), .D(nor_2_out), .nQ(dlatch_5_nq));  // open: Q
  DLATCH dlatch_6 (.C(PHI2), .D(nor_8_out), .nQ(dlatch_6_nq));  // open: Q
  DLATCH dlatch_7 (.C(PHI2), .D(nor_11_out), .nQ(dlatch_7_nq));  // open: Q
  DLATCH dlatch_8 (.C(PHI2), .D(not_5_out), .Q(dlatch_8_q));  // open: nQ
  DLATCH dlatch_9 (.C(PHI2), .D(nADL_PCL), .Q(dlatch_9_q));  // open: nQ
  DLATCH dlatch_10 (.C(PHI2), .D(nor_9_out), .Q(dlatch_10_q));  // open: nQ
  DLATCH dlatch_11 (.C(PHI2), .D(nPCH_PCH), .Q(dlatch_11_q));  // open: nQ
  nor nor_12 (nor_12_out, dlatch_8_q, PHI2);
  nor nor_13 (nor_13_out, dlatch_9_q, PHI2);
  nor nor_14 (nor_14_out, dlatch_10_q, PHI2);
  nor nor_15 (nor_15_out, dlatch_11_q, PHI2);
  assign PCL_DB = 1'b1 ? dlatch_4_nq : 1'bz;  // Driver driver_1
  assign PCH_DB = 1'b1 ? dlatch_5_nq : 1'bz;  // Driver driver_2
  assign PCL_ADL = 1'b1 ? dlatch_6_nq : 1'bz;  // Driver driver_3
  assign PCH_ADH = 1'b1 ? dlatch_7_nq : 1'bz;  // Driver driver_4
  assign PCL_PCL = 1'b1 ? nor_12_out : 1'bz;  // Driver driver_5
  assign ADL_PCL = 1'b1 ? nor_13_out : 1'bz;  // Driver driver_6
  assign ADH_PCH = 1'b1 ? nor_14_out : 1'bz;  // Driver driver_7
  assign PCH_PCH = 1'b1 ? nor_15_out : 1'bz;  // Driver driver_8

  // Other names for the same wires on the sheet: RTS_5 = D84
endmodule
