// Digital circuit PRECHARGE.dig as structural Verilog
module PRECHARGE (
  input  PHI2,
  input  Z_ADD,
  input  SB_ADD,
  input  [7:0] SB_In,
  input  [7:0] DB_In,
  input  [7:0] ADL_In,
  input  [7:0] ADH_In,
  output [7:0] SB_out,
  output [7:0] DB_out,
  output [7:0] ADL_out,
  output [7:0] ADH_out
);

  wire and_1_out, not_1_out;

  not not_1 (not_1_out, PHI2);
  and and_1 (and_1_out, not_1_out, Z_ADD, SB_ADD);
  Multiplexer #(.Bits(8)) multiplexer_1 (.sel(and_1_out), .in_0(SB_In), .in_1({8{1'b0}}), .out(SB_out));
  Multiplexer #(.Bits(8)) multiplexer_2 (.sel(and_1_out), .in_0(DB_In), .in_1({8{1'b0}}), .out(DB_out));
  Multiplexer #(.Bits(8)) multiplexer_3 (.sel(and_1_out), .in_0(ADL_In), .in_1({8{1'b0}}), .out(ADL_out));
  Multiplexer #(.Bits(8)) multiplexer_4 (.sel(and_1_out), .in_0(ADH_In), .in_1({8{1'b0}}), .out(ADH_out));
endmodule
