// Digital circuit REGS.dig as structural Verilog
module REGS (
  input  SB0,
  input  SB1,
  input  SB2,
  input  SB3,
  input  SB4,
  input  SB5,
  input  SB6,
  input  SB7,
  input  Y_SB,
  input  SB_Y,
  input  X_SB,
  input  SB_X,
  input  S_ADL,
  input  S_S,
  input  SB_S,
  input  S_SB,
  input  PHI2,
  output [7:0] Y_Debug,
  output [7:0] X_Debug,
  output [7:0] S_Debug,
  output SB_out0,
  output SB_out1,
  output SB_out2,
  output SB_out3,
  output SB_out4,
  output SB_out5,
  output SB_out6,
  output SB_out7,
  output ADL0,
  output ADL1,
  output ADL2,
  output ADL3,
  output ADL4,
  output ADL5,
  output ADL6,
  output ADL7
);

  wire notconnected_1_out, notconnected_2_out, notconnected_3_out, notconnected_4_out, notconnected_5_out,
       notconnected_6_out, notconnected_7_out, notconnected_8_out, notconnected_9_out, notconnected_10_out,
       notconnected_11_out, notconnected_12_out, notconnected_13_out, notconnected_14_out,
       notconnected_15_out, notconnected_16_out, notconnected_17_out, notconnected_18_out,
       notconnected_19_out, notconnected_20_out, notconnected_21_out, notconnected_22_out,
       notconnected_23_out, notconnected_24_out, notconnected_25_out, notconnected_26_out,
       notconnected_27_out, notconnected_28_out, notconnected_29_out, notconnected_30_out,
       notconnected_31_out, notconnected_32_out;

  REGS_BIT regs_bit_1 (
    .PHI2(PHI2), .in_16(notconnected_1_out), .Y_SB(Y_SB), .SB_Y(SB_Y), .in_17(notconnected_2_out),
    .X_SB(X_SB), .SB_X(SB_X), .in_18(notconnected_3_out), .S_ADL(S_ADL), .S_S(S_S), .SB_S(SB_S), .S_SB(S_SB),
    .in_19(notconnected_4_out), .SBx_in(SB0), .SBx_out(SB_out0), .ADLx(ADL0), .Y(Y_Debug[0]), .X(X_Debug[0]),
    .S(S_Debug[3]));
  // NotConnected on notconnected_1_out
  // NotConnected on notconnected_2_out
  // NotConnected on notconnected_3_out
  // NotConnected on notconnected_4_out
  REGS_BIT regs_bit_2 (
    .PHI2(PHI2), .in_16(notconnected_5_out), .Y_SB(Y_SB), .SB_Y(SB_Y), .in_17(notconnected_6_out),
    .X_SB(X_SB), .SB_X(SB_X), .in_18(notconnected_7_out), .S_ADL(S_ADL), .S_S(S_S), .SB_S(SB_S), .S_SB(S_SB),
    .in_19(notconnected_8_out), .SBx_in(SB4), .SBx_out(SB_out4), .ADLx(ADL4), .Y(Y_Debug[4]), .X(X_Debug[4]),
    .S(S_Debug[4]));
  // NotConnected on notconnected_5_out
  // NotConnected on notconnected_6_out
  // NotConnected on notconnected_7_out
  // NotConnected on notconnected_8_out
  REGS_BIT regs_bit_3 (
    .PHI2(PHI2), .in_16(notconnected_9_out), .Y_SB(Y_SB), .SB_Y(SB_Y), .in_17(notconnected_10_out),
    .X_SB(X_SB), .SB_X(SB_X), .in_18(notconnected_11_out), .S_ADL(S_ADL), .S_S(S_S), .SB_S(SB_S),
    .S_SB(S_SB), .in_19(notconnected_12_out), .SBx_in(SB1), .SBx_out(SB_out1), .ADLx(ADL1), .Y(Y_Debug[1]),
    .X(X_Debug[1]), .S(S_Debug[2]));
  // NotConnected on notconnected_9_out
  // NotConnected on notconnected_10_out
  // NotConnected on notconnected_11_out
  // NotConnected on notconnected_12_out
  REGS_BIT regs_bit_4 (
    .PHI2(PHI2), .in_16(notconnected_13_out), .Y_SB(Y_SB), .SB_Y(SB_Y), .in_17(notconnected_14_out),
    .X_SB(X_SB), .SB_X(SB_X), .in_18(notconnected_15_out), .S_ADL(S_ADL), .S_S(S_S), .SB_S(SB_S),
    .S_SB(S_SB), .in_19(notconnected_16_out), .SBx_in(SB5), .SBx_out(SB_out5), .ADLx(ADL5), .Y(Y_Debug[5]),
    .X(X_Debug[5]), .S(S_Debug[5]));
  // NotConnected on notconnected_13_out
  // NotConnected on notconnected_14_out
  // NotConnected on notconnected_15_out
  // NotConnected on notconnected_16_out
  REGS_BIT regs_bit_5 (
    .PHI2(PHI2), .in_16(notconnected_17_out), .Y_SB(Y_SB), .SB_Y(SB_Y), .in_17(notconnected_18_out),
    .X_SB(X_SB), .SB_X(SB_X), .in_18(notconnected_19_out), .S_ADL(S_ADL), .S_S(S_S), .SB_S(SB_S),
    .S_SB(S_SB), .in_19(notconnected_20_out), .SBx_in(SB2), .SBx_out(SB_out2), .ADLx(ADL2), .Y(Y_Debug[2]),
    .X(X_Debug[2]), .S(S_Debug[1]));
  // NotConnected on notconnected_17_out
  // NotConnected on notconnected_18_out
  // NotConnected on notconnected_19_out
  // NotConnected on notconnected_20_out
  REGS_BIT regs_bit_6 (
    .PHI2(PHI2), .in_16(notconnected_21_out), .Y_SB(Y_SB), .SB_Y(SB_Y), .in_17(notconnected_22_out),
    .X_SB(X_SB), .SB_X(SB_X), .in_18(notconnected_23_out), .S_ADL(S_ADL), .S_S(S_S), .SB_S(SB_S),
    .S_SB(S_SB), .in_19(notconnected_24_out), .SBx_in(SB6), .SBx_out(SB_out6), .ADLx(ADL6), .Y(Y_Debug[6]),
    .X(X_Debug[6]), .S(S_Debug[6]));
  // NotConnected on notconnected_21_out
  // NotConnected on notconnected_22_out
  // NotConnected on notconnected_23_out
  // NotConnected on notconnected_24_out
  REGS_BIT regs_bit_7 (
    .PHI2(PHI2), .in_16(notconnected_25_out), .Y_SB(Y_SB), .SB_Y(SB_Y), .in_17(notconnected_26_out),
    .X_SB(X_SB), .SB_X(SB_X), .in_18(notconnected_27_out), .S_ADL(S_ADL), .S_S(S_S), .SB_S(SB_S),
    .S_SB(S_SB), .in_19(notconnected_28_out), .SBx_in(SB3), .SBx_out(ADL3), .ADLx(SB_out3), .Y(Y_Debug[3]),
    .X(X_Debug[3]), .S(S_Debug[0]));
  // NotConnected on notconnected_25_out
  // NotConnected on notconnected_26_out
  // NotConnected on notconnected_27_out
  // NotConnected on notconnected_28_out
  REGS_BIT regs_bit_8 (
    .PHI2(PHI2), .in_16(notconnected_29_out), .Y_SB(Y_SB), .SB_Y(SB_Y), .in_17(notconnected_30_out),
    .X_SB(X_SB), .SB_X(SB_X), .in_18(notconnected_31_out), .S_ADL(S_ADL), .S_S(S_S), .SB_S(SB_S),
    .S_SB(S_SB), .in_19(notconnected_32_out), .SBx_in(SB7), .SBx_out(SB_out7), .ADLx(ADL7), .Y(Y_Debug[7]),
    .X(X_Debug[7]), .S(S_Debug[7]));
  // NotConnected on notconnected_29_out
  // NotConnected on notconnected_30_out
  // NotConnected on notconnected_31_out
  // NotConnected on notconnected_32_out
endmodule
