// Digital circuit ABL.dig as structural Verilog
module ABL (
  input  PHI1,
  input  PHI2,
  input  ADL_ABL,
  input  ADL0,
  input  ADL1,
  input  ADL2,
  input  ADL3,
  input  ADL4,
  input  ADL5,
  input  ADL6,
  input  ADL7,
  output A0,
  output A1,
  output A2,
  output A3,
  output A4,
  output A5,
  output A6,
  output A7
);

  wire notconnected_1_out, notconnected_2_out, notconnected_3_out, notconnected_4_out, notconnected_5_out,
       notconnected_6_out, notconnected_7_out, notconnected_8_out;

  ABL_BIT abl_bit_1 (.PHI1(PHI1), .PHI2(PHI2), .in_6(notconnected_1_out), .ADL_ABL(ADL_ABL), .ADLx(ADL0), .Ax(A0));
  // NotConnected on notconnected_1_out
  ABL_BIT abl_bit_2 (.PHI1(PHI1), .PHI2(PHI2), .in_6(notconnected_2_out), .ADL_ABL(ADL_ABL), .ADLx(ADL1), .Ax(A1));
  // NotConnected on notconnected_2_out
  ABL_BIT abl_bit_3 (.PHI1(PHI1), .PHI2(PHI2), .in_6(notconnected_3_out), .ADL_ABL(ADL_ABL), .ADLx(ADL2), .Ax(A2));
  // NotConnected on notconnected_3_out
  ABL_BIT abl_bit_4 (.PHI1(PHI1), .PHI2(PHI2), .in_6(notconnected_4_out), .ADL_ABL(ADL_ABL), .ADLx(ADL3), .Ax(A3));
  // NotConnected on notconnected_4_out
  ABL_BIT abl_bit_5 (.PHI1(PHI1), .PHI2(PHI2), .in_6(notconnected_5_out), .ADL_ABL(ADL_ABL), .ADLx(ADL4), .Ax(A4));
  // NotConnected on notconnected_5_out
  ABL_BIT abl_bit_6 (.PHI1(PHI1), .PHI2(PHI2), .in_6(notconnected_6_out), .ADL_ABL(ADL_ABL), .ADLx(ADL5), .Ax(A5));
  // NotConnected on notconnected_6_out
  ABL_BIT abl_bit_7 (.PHI1(PHI1), .PHI2(PHI2), .in_6(notconnected_7_out), .ADL_ABL(ADL_ABL), .ADLx(ADL6), .Ax(A6));
  // NotConnected on notconnected_7_out
  ABL_BIT abl_bit_8 (.PHI1(PHI1), .PHI2(PHI2), .in_6(notconnected_8_out), .ADL_ABL(ADL_ABL), .ADLx(ADL7), .Ax(A7));
  // NotConnected on notconnected_8_out

  // Notes on the sheet:
  //   0
  //   1
  //   2
  //   3
  //   4
  //   5
  //   6
  //   7
endmodule
