// Digital circuit ABL_BIT.dig as structural Verilog
module ABL_BIT (
  input  PHI1,
  input  PHI2,
  input  ADL_ABL,
  input  ADLx,
  input  in_6,
  output Ax
);

  wire and_1_out, not_1_out;

  and and_1 (and_1_out, PHI1, ADL_ABL);
  not not_1 (not_1_out, ADLx);
  DFF_Level dff_level_1 (.nQ(Ax), .EN(and_1_out), .D(not_1_out));  // open: Q

  // Notes on the sheet:
  //   not used
endmodule
