// Digital circuit ADD_SB7_Logic.dig as structural Verilog
module ADD_SB7_Logic (
  input  PHI1,
  input  PHI2,
  input  nC_OUT,
  input  nready,
  input  SR,
  input  nROR,
  output nADD_SB7
);

  wire dlatch_1_nq, dlatch_2_nq, dlatch_3_q, dlatch_4_nq, dlatch_5_q, dlatch_6_nq, dlatch_7_q,
       multiplexer_1_out, nor_1_out, not_1_out, not_2_out, not_3_out;

  not not_1 (not_1_out, nC_OUT);
  DLATCH dlatch_1 (.C(PHI2), .D(not_1_out), .nQ(dlatch_1_nq));  // open: Q
  DLATCH dlatch_2 (.C(PHI1), .D(nready), .nQ(dlatch_2_nq));  // open: Q
  not not_2 (not_2_out, SR);
  nor nor_1 (nor_1_out, dlatch_2_nq, not_2_out);
  DLATCH dlatch_3 (.C(PHI2), .D(nor_1_out), .Q(dlatch_3_q));  // open: nQ
  DLATCH dlatch_4 (.C(PHI2), .D(SR), .nQ(dlatch_4_nq));  // open: Q
  DLATCH dlatch_5 (.C(PHI2), .D(dlatch_6_nq), .Q(dlatch_5_q));  // open: nQ
  Multiplexer multiplexer_1 (.sel(dlatch_3_q), .in_0(dlatch_5_q), .in_1(dlatch_1_nq), .out(multiplexer_1_out));
  not not_3 (not_3_out, multiplexer_1_out);
  DLATCH dlatch_6 (.C(PHI1), .D(not_3_out), .nQ(dlatch_6_nq));  // open: Q
  DLATCH dlatch_7 (.C(PHI1), .D(dlatch_4_nq), .Q(dlatch_7_q));  // open: nQ
  nor nor_2 (nADD_SB7, dlatch_6_nq, dlatch_7_q, nROR);
endmodule
