// Digital circuit ALU_ADD.dig as structural Verilog
module ALU_ADD (
  input  [7:0] nres,
  input  ADD_ADL,
  input  ADD_SB7,
  input  ADD_SB06,
  input  PHI2,
  output SB0,
  output SB1,
  output SB2,
  output SB3,
  output SB4,
  output SB5,
  output SB6,
  output SB7,
  output ADL0,
  output ADL1,
  output ADL2,
  output ADL3,
  output ADL4,
  output ADL5,
  output ADL6,
  output ADL7,
  output [7:0] nADDx,
  output [7:0] ADD_Debug
);

  DLATCH dlatch_1 (.C(PHI2), .D(nres[0]), .Q(nADDx[0]), .nQ(ADD_Debug[0]));
  DLATCH dlatch_2 (.C(PHI2), .D(nres[1]), .Q(nADDx[1]), .nQ(ADD_Debug[1]));
  DLATCH dlatch_3 (.C(PHI2), .D(nres[2]), .Q(nADDx[2]), .nQ(ADD_Debug[2]));
  DLATCH dlatch_4 (.C(PHI2), .D(nres[3]), .Q(nADDx[3]), .nQ(ADD_Debug[3]));
  DLATCH dlatch_5 (.C(PHI2), .D(nres[4]), .Q(nADDx[4]), .nQ(ADD_Debug[4]));
  DLATCH dlatch_6 (.C(PHI2), .D(nres[5]), .Q(nADDx[5]), .nQ(ADD_Debug[5]));
  DLATCH dlatch_7 (.C(PHI2), .D(nres[6]), .Q(nADDx[6]), .nQ(ADD_Debug[6]));
  DLATCH dlatch_8 (.C(PHI2), .D(nres[7]), .Q(nADDx[7]), .nQ(ADD_Debug[7]));
  assign SB0 = ADD_SB06 ? ADD_Debug[0] : 1'bz;  // Driver driver_1
  assign SB1 = ADD_SB06 ? ADD_Debug[1] : 1'bz;  // Driver driver_2
  assign SB2 = ADD_SB06 ? ADD_Debug[2] : 1'bz;  // Driver driver_3
  assign SB3 = ADD_SB06 ? ADD_Debug[3] : 1'bz;  // Driver driver_4
  assign SB4 = ADD_SB06 ? ADD_Debug[4] : 1'bz;  // Driver driver_5
  assign SB5 = ADD_SB06 ? ADD_Debug[5] : 1'bz;  // Driver driver_6
  assign SB6 = ADD_SB06 ? ADD_Debug[6] : 1'bz;  // Driver driver_7
  assign SB7 = ADD_SB7 ? ADD_Debug[7] : 1'bz;  // Driver driver_8
  assign ADL0 = ADD_ADL ? ADD_Debug[0] : 1'bz;  // Driver driver_9
  assign ADL1 = ADD_ADL ? ADD_Debug[1] : 1'bz;  // Driver driver_10
  assign ADL2 = ADD_ADL ? ADD_Debug[2] : 1'bz;  // Driver driver_11
  assign ADL3 = ADD_ADL ? ADD_Debug[3] : 1'bz;  // Driver driver_12
  assign ADL4 = ADD_ADL ? ADD_Debug[4] : 1'bz;  // Driver driver_13
  assign ADL5 = ADD_ADL ? ADD_Debug[5] : 1'bz;  // Driver driver_14
  assign ADL6 = ADD_ADL ? ADD_Debug[6] : 1'bz;  // Driver driver_15
  assign ADL7 = ADD_ADL ? ADD_Debug[7] : 1'bz;  // Driver driver_16
endmodule
