// Digital circuit ALU_SETUP.dig as structural Verilog
module ALU_SETUP (
  input  PHI1,
  input  PHI2,
  input  BR3,
  input  BRK6E,
  input  STKOP,
  input  T0,
  input  T1,
  input  T6,
  input  T7,
  input  nC_OUT,
  input  nD_OUT,
  input  nready,
  input  BRFW,
  input  PGX,
  input  D26,
  input  D27,
  input  D29,
  input  D30,
  input  D31,
  input  D32,
  input  D33,
  input  D34,
  input  D35,
  input  D36,
  input  D37,
  input  D38,
  input  D39,
  input  D40,
  input  D41,
  input  D42,
  input  D43,
  input  D44,
  input  D45,
  input  D47,
  input  D48,
  input  D49,
  input  D50,
  input  D51,
  input  D52,
  input  D53,
  input  D54,
  input  D56,
  input  D69,
  input  D70,
  input  D75,
  input  D76,
  input  D84,
  input  D85,
  input  D86,
  input  D87,
  input  D88,
  input  D89,
  output AND,
  output INC_SB,
  output SR,
  output NDB_ADD,
  output DB_ADD,
  output Z_ADD,
  output SB_ADD,
  output ADL_ADD,
  output ANDS,
  output EORS,
  output ORS,
  output nACIN,
  output SUMS,
  output nDAA,
  output ADD_SB7,
  output ADD_SB06,
  output ADD_ADL,
  output nDSA,
  output SRS
);

  wire acin_latch1_q, acin_latch2_q, acin_latch3_q, acin_latch4_q, acin_latch5_nq, add_sb7_logic_1_nadd_sb7,
       addadl_latch_2_nq, addadl_latch_q, addsb06_latch_nq, addsb7_latch_q, and_1_out, and_2_out, and_3_out,
       ands_latch1_nq, ands_latch2_nq, daa_latch1_nq, daa_latch2_nq, dbadd_latch_q, dsa_latch1_nq,
       eors_latch1_nq, eors_latch2_nq, nand_1_out, nand_2_out, nand_3_out, nand_4_out, nand_5_out,
       nand_6_out, ndbadd_latch_q, nor_1_out, nor_2_out, nor_3_out, nor_4_out, nor_5_out, nor_6_out,
       nor_7_out, nor_8_out, nor_9_out, nor_10_out, nor_11_out, nor_12_out, nor_13_out, nor_14_out,
       nor_15_out, nor_16_out, nor_17_out, nor_18_out, nor_19_out, nor_20_out, nor_21_out, nor_22_out,
       nor_23_out, not_1_out, not_2_out, not_4_out, not_5_out, not_6_out, not_9_out, not_10_out, not_11_out,
       not_12_out, not_13_out, not_14_out, not_15_out, or_1_out, or_2_out, ors_latch1_nq, ors_latch2_nq,
       sbadd_latch_q, srs_latch1_nq, srs_latch2_nq, sums_latch1_nq, sums_latch2_nq, zadd_latch_q;

  not not_1 (not_1_out, D34);
  nor nor_1 (nor_1_out, D69, D70);
  not not_2 (not_2_out, nD_OUT);
  and and_1 (and_1_out, D33, not_1_out);
  and and_2 (and_2_out, T6, D44);
  or or_1 (or_1_out, D52, D53);
  and and_3 (and_3_out, D76, T6);
  nor nor_2 (nor_2_out, D84, D85, D86, D87, D88, D89, D26);
  nor nor_3 (nor_3_out, D32, nready);
  not not_3 (AND, nor_1_out);
  nor nor_4 (nor_4_out, D75, and_3_out);
  not not_4 (not_4_out, D27);
  not not_5 (not_5_out, nor_3_out);
  nor nor_5 (nor_5_out, and_1_out, D35, D36, D37, D38, D39, nready);
  nor nor_6 (nor_6_out, D39, D40, D41, D42, D43, and_2_out);
  not not_6 (not_6_out, BR3);
  nor nor_7 (nor_7_out, T0, T6);
  not not_7 (SR, nor_4_out);
  not not_8 (INC_SB, nor_6_out);
  nor nor_8 (nor_8_out, not_6_out, BRFW);
  nor nor_9 (nor_9_out, D49, D50, nor_8_out);
  nor nor_10 (nor_10_out, nC_OUT, nor_7_out);
  nor nor_11 (nor_11_out, STKOP, D30, D31, D45, D48, INC_SB, D47, BRK6E, nready);
  not not_9 (not_9_out, D47);
  not not_10 (not_10_out, nor_9_out);
  nor nor_12 (nor_12_out, nor_5_out, not_9_out);
  nand nand_1 (nand_1_out, nor_10_out, or_1_out);
  not not_11 (not_11_out, D54);
  nand nand_2 (nand_2_out, nand_1_out, not_11_out);
  nand nand_3 (nand_3_out, D52, not_2_out);
  or or_2 (or_2_out, not_10_out, D56, D51);
  nor nor_13 (nor_13_out, nor_2_out, PGX);
  nor nor_14 (nor_14_out, nand_3_out, D51);
  nand nand_4 (nand_4_out, D51, not_2_out);
  DLATCH acin_latch1 (.C(PHI2), .D(nor_12_out), .Q(acin_latch1_q));  // open: nQ
  DLATCH acin_latch2 (.C(PHI2), .D(INC_SB), .Q(acin_latch2_q));  // open: nQ
  DLATCH acin_latch3 (.C(PHI2), .D(not_10_out), .Q(acin_latch3_q));  // open: nQ
  DLATCH acin_latch4 (.C(PHI2), .D(nand_2_out), .Q(acin_latch4_q));  // open: nQ
  not not_12 (not_12_out, nor_13_out);
  not not_13 (not_13_out, nor_14_out);
  not not_14 (not_14_out, nready);
  nor nor_15 (nor_15_out, acin_latch1_q, acin_latch2_q, acin_latch3_q, acin_latch4_q);
  nand nand_5 (nand_5_out, or_2_out, not_14_out);
  ADD_SB7_Logic add_sb7_logic_1 (
    .PHI1(PHI1), .PHI2(PHI2), .nC_OUT(nC_OUT), .nready(nready), .SR(SR), .nROR(not_4_out),
    .nADD_SB7(add_sb7_logic_1_nadd_sb7));
  nor nor_16 (nor_16_out, T7, STKOP, D56, T1, PGX);
  nand nand_6 (nand_6_out, nand_5_out, nor_5_out);
  nor nor_17 (nor_17_out, AND, D29, not_5_out, SR);
  nor nor_18 (nor_18_out, nor_16_out, add_sb7_logic_1_nadd_sb7);
  not not_15 (not_15_out, nor_11_out);
  DLATCH ndbadd_latch (.C(PHI2), .D(nand_5_out), .Q(ndbadd_latch_q));  // open: nQ
  DLATCH dbadd_latch (.C(PHI2), .D(nand_6_out), .Q(dbadd_latch_q));  // open: nQ
  DLATCH zadd_latch (.C(PHI2), .D(nor_11_out), .Q(zadd_latch_q));  // open: nQ
  DLATCH sbadd_latch (.C(PHI2), .D(not_15_out), .Q(sbadd_latch_q));  // open: nQ
  DLATCH addadl_latch (.C(PHI2), .D(nor_5_out), .Q(addadl_latch_q));  // open: nQ
  DLATCH ands_latch1 (.C(PHI2), .D(AND), .nQ(ands_latch1_nq));  // open: Q
  DLATCH eors_latch1 (.C(PHI2), .D(D29), .nQ(eors_latch1_nq));  // open: Q
  DLATCH ors_latch1 (.C(PHI2), .D(not_5_out), .nQ(ors_latch1_nq));  // open: Q
  DLATCH srs_latch1 (.C(PHI2), .D(SR), .nQ(srs_latch1_nq));  // open: Q
  DLATCH sums_latch1 (.C(PHI2), .D(nor_17_out), .nQ(sums_latch1_nq));  // open: Q
  DLATCH daa_latch1 (.C(PHI2), .D(not_13_out), .nQ(daa_latch1_nq));  // open: Q
  DLATCH addsb7_latch (.C(PHI2), .D(nor_18_out), .Q(addsb7_latch_q));  // open: nQ
  DLATCH addsb06_latch (.C(PHI2), .D(nor_16_out), .nQ(addsb06_latch_nq));  // open: Q
  DLATCH addadl_latch_2 (.C(PHI2), .D(not_12_out), .nQ(addadl_latch_2_nq));  // open: Q
  DLATCH dsa_latch1 (.C(PHI2), .D(nand_4_out), .nQ(dsa_latch1_nq));  // open: Q
  DLATCH ands_latch2 (.C(PHI1), .D(ands_latch1_nq), .nQ(ands_latch2_nq));  // open: Q
  DLATCH eors_latch2 (.C(PHI1), .D(eors_latch1_nq), .nQ(eors_latch2_nq));  // open: Q
  DLATCH ors_latch2 (.C(PHI1), .D(ors_latch1_nq), .nQ(ors_latch2_nq));  // open: Q
  DLATCH acin_latch5 (.C(PHI1), .D(nor_15_out), .nQ(acin_latch5_nq));  // open: Q
  DLATCH srs_latch2 (.C(PHI1), .D(srs_latch1_nq), .nQ(srs_latch2_nq));  // open: Q
  DLATCH sums_latch2 (.C(PHI1), .D(sums_latch1_nq), .nQ(sums_latch2_nq));  // open: Q
  DLATCH daa_latch2 (.C(PHI1), .D(daa_latch1_nq), .nQ(daa_latch2_nq));  // open: Q
  DLATCH dsa_latch2 (.C(PHI1), .D(dsa_latch1_nq), .nQ(nDSA));  // open: Q
  nor nor_19 (nor_19_out, ndbadd_latch_q, PHI2);
  nor nor_20 (nor_20_out, dbadd_latch_q, PHI2);
  nor nor_21 (nor_21_out, zadd_latch_q, PHI2);
  nor nor_22 (nor_22_out, sbadd_latch_q, PHI2);
  nor nor_23 (nor_23_out, addadl_latch_q, PHI2);
  assign ANDS = 1'b1 ? ands_latch2_nq : 1'bz;  // Driver driver_1
  assign EORS = 1'b1 ? eors_latch2_nq : 1'bz;  // Driver driver_2
  assign ORS = 1'b1 ? ors_latch2_nq : 1'bz;  // Driver driver_3
  assign nACIN = 1'b1 ? acin_latch5_nq : 1'bz;  // Driver driver_4
  not not_16 (SRS, srs_latch2_nq);
  assign SUMS = 1'b1 ? sums_latch2_nq : 1'bz;  // Driver driver_5
  assign nDAA = 1'b1 ? daa_latch2_nq : 1'bz;  // Driver driver_6
  assign ADD_SB7 = 1'b1 ? addsb7_latch_q : 1'bz;  // Driver driver_7
  assign ADD_SB06 = 1'b1 ? addsb06_latch_nq : 1'bz;  // Driver driver_8
  assign ADD_ADL = 1'b1 ? addadl_latch_2_nq : 1'bz;  // Driver driver_9
  assign NDB_ADD = 1'b1 ? nor_19_out : 1'bz;  // Driver driver_10
  assign DB_ADD = 1'b1 ? nor_20_out : 1'bz;  // Driver driver_11
  assign Z_ADD = 1'b1 ? nor_21_out : 1'bz;  // Driver driver_12
  assign SB_ADD = 1'b1 ? nor_22_out : 1'bz;  // Driver driver_13
  assign ADL_ADD = 1'b1 ? nor_23_out : 1'bz;  // Driver driver_14

  // Other names for the same wires on the sheet: JSR_5 = D56; RTI_5 = D26; RTS_5 = D84; SBC0 = D51
endmodule
