// Digital circuit BUS_MUX_HACK.dig as structural Verilog
module BUS_MUX_HACK (
  input  Y_SB,
  input  X_SB,
  input  S_SB,
  input  AC_DB,
  input  AC_SB,
  input  ADD_SB06,
  input  ADD_SB7,
  input  PCL_DB,
  input  PCH_DB,
  input  PCH_ADH,
  input  DL_ADH,
  input  DL_DB,
  output SB_Dirty,
  output DB_Dirty,
  output ADH_Dirty,
  output SBDB_Clutch
);

  wire or_1_out, or_2_out, or_3_out;

  or or_1 (or_1_out, ADD_SB06, ADD_SB7);
  or or_2 (or_2_out, Y_SB, X_SB, S_SB, AC_SB, or_1_out);
  or or_3 (or_3_out, AC_DB, PCL_DB, PCH_DB, DL_DB);
  or or_4 (ADH_Dirty, PCH_ADH, DL_ADH);
  and and_1 (SBDB_Clutch, or_2_out, or_3_out);
  Multiplexer multiplexer_1 (.sel(SBDB_Clutch), .in_0(or_2_out), .in_1(1'b0), .out(SB_Dirty));
  Multiplexer multiplexer_2 (.sel(SBDB_Clutch), .in_0(or_3_out), .in_1(1'b0), .out(DB_Dirty));
endmodule
