// Digital circuit CONST_GEN.dig as structural Verilog
module CONST_GEN (
  input  Z_ADL0,
  input  Z_ADL1,
  input  Z_ADL2,
  input  Z_ADH0,
  input  Z_ADH17,
  input  [7:0] ADL_In,
  input  [7:0] ADH_In,
  output [7:0] ADL_out,
  output [7:0] ADL_out_2
);

  and and_1 (ADL_out[0], ADL_In[0], ~Z_ADL0);  // And
  and and_2 (ADL_out[1], ADL_In[1], ~Z_ADL1);  // And
  and and_3 (ADL_out[2], ADL_In[2], ~Z_ADL2);  // And
  and and_4 (ADL_out_2[0], ADH_In[0], ~Z_ADH0);  // And
  and and_5 (ADL_out_2[1], ADH_In[1], ~Z_ADH17);  // And
  and and_6 (ADL_out_2[2], ADH_In[2], ~Z_ADH17);  // And
  and and_7 (ADL_out_2[3], ADH_In[3], ~Z_ADH17);  // And
  and and_8 (ADL_out_2[4], ADH_In[4], ~Z_ADH17);  // And
  and and_9 (ADL_out_2[5], ADH_In[5], ~Z_ADH17);  // And
  and and_10 (ADL_out_2[6], ADH_In[6], ~Z_ADH17);  // And
  and and_11 (ADL_out_2[7], ADH_In[7], ~Z_ADH17);  // And

  assign ADL_out[7:3] = ADL_In[7:3];
endmodule
