// Digital circuit DISPATCH.dig as structural Verilog
module DISPATCH (
  input  PHI1,
  input  PHI2,
  input  BRK6E,
  input  BR2,
  input  RESP,
  input  ACR,
  input  DORES,
  input  PC_DB,
  input  D91,
  input  D92,
  input  BR3,
  input  D96,
  input  D97,
  input  D98,
  input  D100,
  input  D101,
  input  D102,
  input  D103,
  input  D104,
  input  D105,
  input  D106,
  input  D107,
  input  D111,
  input  D122,
  input  D123,
  input  D124,
  input  D125,
  input  RDY,
  input  B_OUT,
  input  BRFW,
  input  nBRTAKEN,
  input  nTWOCYCLE,
  input  nADL_PCL,
  input  nIMPLIED,
  output T7,
  output T6,
  output ACRL2,
  output TRES2,
  output T0,
  output nT1X,
  output nIPC,
  output nT0,
  output T1,
  output WR,
  output nready,
  output Z_IR,
  output FETCH,
  output STOR
);

  wire and_1_out, and_2_out, and_3_out, and_4_out, and_5_out, and_6_out, dlatch_1_nq, dlatch_2_nq,
       dlatch_4_q, dlatch_5_q, dlatch_6_q, dlatch_7_q, dlatch_8_q, dlatch_9_nq, dlatch_11_q, dlatch_12_q,
       dlatch_13_q, dlatch_14_q, dlatch_15_q, dlatch_16_nq, dlatch_17_nq, dlatch_18_nq, dlatch_19_nq,
       dlatch_20_q, dlatch_21_q, dlatch_22_q, dlatch_24_q, dlatch_25_q, dlatch_26_q, dlatch_27_q,
       dlatch_28_q, dlatch_29_q, dlatch_31_nq, multiplexer_1_out, nand_1_out, nand_2_out, nMemOP, nor_1_out,
       nor_3_out, nor_4_out, nor_6_out, nor_7_out, nor_8_out, nor_9_out, nor_10_out, nor_11_out, nor_12_out,
       nor_13_out, nor_14_out, nor_15_out, nor_16_out, nor_17_out, nor_18_out, nor_19_out, nor_20_out,
       nor_21_out, nor_23_out, nor_24_out, nor_25_out, nor_26_out, nor_28_out, nor_29_out, nor_30_out,
       nor_31_out, not_1_out, not_2_out, not_3_out, not_4_out, not_5_out, not_6_out, not_7_out, not_8_out,
       not_9_out, not_10_out, not_11_out, not_12_out, not_13_out, NotReadyPhi1, nSHIFT, nTRESX, or_1_out,
       xor_1_out;

  nor nor_1 (nor_1_out, D91, D92);
  not not_1 (not_1_out, D97);
  nor nor_2 (nMemOP, D111, D122, D123, D124, D125);
  nor nor_3 (nor_3_out, BR2, BR3);
  nor nor_4 (nor_4_out, D100, D101, D102, D103, D104, D105);
  nor nor_5 (nSHIFT, D106, D107);
  not not_2 (not_2_out, nor_3_out);
  not not_3 (not_3_out, nIMPLIED);
  not not_4 (not_4_out, NotReadyPhi1);
  not not_5 (not_5_out, nor_4_out);
  nor nor_6 (nor_6_out, nADL_PCL, not_2_out);
  not not_6 (not_6_out, ACR);
  nor nor_7 (nor_7_out, not_4_out, ACRL2);
  and and_1 (and_1_out, nBRTAKEN, BR2);
  and and_2 (and_2_out, nBRTAKEN, BR2);
  and and_3 (and_3_out, not_6_out, not_4_out);
  nor nor_8 (nor_8_out, STOR, PC_DB, D98, D100, T7, T6);
  not not_7 (not_7_out, BR3);
  nor nor_9 (nor_9_out, and_3_out, nor_7_out);
  nor nor_10 (nor_10_out, T0, and_1_out);
  not not_8 (not_8_out, T1);
  DLATCH dlatch_1 (.C(PHI1), .D(nready), .nQ(dlatch_1_nq));  // open: Q
  nor nor_11 (nor_11_out, and_2_out, nor_6_out);
  Multiplexer multiplexer_1 (.sel(nready), .in_0(nor_10_out), .in_1(not_8_out), .out(multiplexer_1_out));
  nor nor_12 (nor_12_out, not_7_out, NotReadyPhi1);
  not not_9 (not_9_out, nready);
  not not_10 (not_10_out, ACR);
  DLATCH dlatch_2 (.C(PHI1), .D(nor_9_out), .nQ(dlatch_2_nq));  // open: Q
  DLATCH dlatch_3 (.C(PHI2), .D(dlatch_2_nq), .nQ(ACRL2));  // open: Q
  DLATCH dlatch_4 (.C(PHI2), .D(nor_1_out), .Q(dlatch_4_q));  // open: nQ
  not not_11 (not_11_out, nSHIFT);
  DLATCH dlatch_5 (.C(PHI2), .D(nor_8_out), .Q(dlatch_5_q));  // open: nQ
  DLATCH dlatch_6 (.C(PHI2), .D(multiplexer_1_out), .Q(dlatch_6_q));  // open: nQ
  DLATCH dlatch_7 (.C(PHI2), .D(RESP), .Q(dlatch_7_q));  // open: nQ
  DLATCH dlatch_8 (.C(PHI1), .D(not_9_out), .Q(dlatch_8_q));  // open: nQ
  DLATCH dlatch_9 (.C(PHI2), .D(nor_12_out), .nQ(dlatch_9_nq));  // open: Q
  xor xor_1 (xor_1_out, BRFW, not_10_out);
  DLATCH dlatch_10 (.C(PHI2), .D(dlatch_1_nq), .nQ(NotReadyPhi1));  // open: Q
  DLATCH dlatch_11 (.C(PHI1), .D(not_13_out), .Q(dlatch_11_q));  // open: nQ
  DLATCH dlatch_12 (.C(PHI1), .D(nTWOCYCLE), .Q(dlatch_12_q));  // open: nQ
  DLATCH dlatch_13 (.C(PHI1), .D(nTRESX), .Q(dlatch_13_q));  // open: nQ
  DLATCH dlatch_14 (.C(PHI2), .D(nor_11_out), .Q(dlatch_14_q));  // open: nQ
  nor nor_13 (nor_13_out, D96, not_11_out, nMemOP);
  nand nand_1 (nand_1_out, nSHIFT, not_1_out);
  and and_4 (and_4_out, dlatch_12_q, dlatch_13_q);
  nor nor_14 (nor_14_out, nor_13_out, T7, not_5_out, BR3);
  nor nor_15 (nor_15_out, dlatch_6_q, dlatch_7_q);
  and and_5 (and_5_out, ~dlatch_9_nq, xor_1_out);  // And
  nor nor_16 (nor_16_out, nSHIFT, nMemOP, nready);
  nor nor_17 (nor_17_out, nor_9_out, dlatch_4_q, nready, nand_1_out);
  nor nor_18 (nor_18_out, dlatch_11_q, and_4_out);
  nor nor_19 (nor_19_out, dlatch_24_q, dlatch_25_q);
  not not_12 (not_12_out, nready);
  DLATCH dlatch_15 (.C(PHI2), .D(nor_16_out), .Q(dlatch_15_q));  // open: nQ
  nand nand_2 (nand_2_out, T6, not_12_out);
  nor nor_20 (nor_20_out, nready, nor_14_out);
  nor nor_21 (nor_21_out, RDY, dlatch_20_q);
  nor nor_22 (WR, nready, dlatch_5_q, DORES);
  nor nor_23 (nor_23_out, dlatch_8_q, RESP, dlatch_22_q);
  nor nor_24 (nor_24_out, dlatch_21_q, and_5_out);
  nor nor_25 (nor_25_out, nor_24_out, nready);
  nor nor_26 (nor_26_out, nor_25_out, nor_15_out);
  nor nor_27 (nT0, nor_18_out, nor_19_out);
  nor nor_28 (nor_28_out, dlatch_24_q, nready);
  nor nor_29 (nor_29_out, nready, dlatch_14_q, not_3_out);
  and and_6 (and_6_out, dlatch_29_q, nready);
  nor nor_30 (nor_30_out, RESP, nor_15_out, nor_20_out);
  DLATCH dlatch_16 (.C(PHI2), .D(nand_2_out), .nQ(dlatch_16_nq));  // open: Q
  nor nor_31 (nor_31_out, and_6_out, dlatch_15_q);
  nor nor_32 (nTRESX, nor_17_out, BRK6E, dlatch_17_nq);
  DLATCH dlatch_17 (.C(PHI2), .D(nor_30_out), .nQ(dlatch_17_nq));  // open: Q
  DLATCH dlatch_18 (.C(PHI2), .D(T1), .nQ(dlatch_18_nq));  // open: Q
  DLATCH dlatch_19 (.C(PHI2), .D(nor_21_out), .nQ(dlatch_19_nq));  // open: Q
  DLATCH dlatch_20 (.C(PHI1), .D(WR), .Q(dlatch_20_q));  // open: nQ
  DLATCH dlatch_21 (.C(PHI2), .D(nor_23_out), .Q(dlatch_21_q));  // open: nQ
  DLATCH dlatch_22 (.C(PHI1), .D(nor_24_out), .Q(dlatch_22_q));  // open: nQ
  DLATCH dlatch_23 (.C(PHI1), .D(nor_26_out), .nQ(T1));  // open: Q
  not not_13 (not_13_out, nor_26_out);
  DLATCH dlatch_24 (.C(PHI2), .D(nT0), .Q(dlatch_24_q));  // open: nQ
  DLATCH dlatch_25 (.C(PHI1), .D(nor_28_out), .Q(dlatch_25_q), .nQ(nT1X));
  DLATCH dlatch_26 (.C(PHI1), .D(B_OUT), .Q(dlatch_26_q));  // open: nQ
  DLATCH dlatch_27 (.C(PHI1), .D(and_5_out), .Q(dlatch_27_q));  // open: nQ
  DLATCH dlatch_28 (.C(PHI1), .D(nor_29_out), .Q(dlatch_28_q));  // open: nQ
  nor nor_33 (STOR, nMemOP, not_1_out);
  not not_14 (nready, dlatch_19_nq);
  DLATCH dlatch_29 (.C(PHI2), .D(T6), .Q(dlatch_29_q));  // open: nQ
  DLATCH dlatch_30 (.C(PHI1), .D(nor_31_out), .nQ(T6));  // open: Q
  DLATCH dlatch_31 (.C(PHI1), .D(dlatch_16_nq), .nQ(dlatch_31_nq));  // open: Q
  DLATCH dlatch_32 (.C(PHI1), .D(nTRESX), .nQ(TRES2));  // open: Q
  nor nor_34 (FETCH, dlatch_18_nq, nready);
  not not_15 (T0, nT0);
  or or_1 (or_1_out, dlatch_27_q, dlatch_28_q);
  not not_16 (T7, dlatch_31_nq);
  nand nand_3 (Z_IR, B_OUT, FETCH);
  nand nand_4 (nIPC, dlatch_26_q, or_1_out);
endmodule
