// Digital circuit DispACRLatch.dig as structural Verilog
module DispACRLatch (
  input  PHI1,
  input  PHI2,
  input  ACR,
  input  NotReadyPhi1,
  output ACRL1,
  output ACRL2
);

  wire and_1_out, dlatch_1_nq, nor_1_out, not_1_out, not_2_out;

  not not_1 (not_1_out, NotReadyPhi1);
  not not_2 (not_2_out, ACR);
  nor nor_1 (nor_1_out, not_1_out, ACRL2);
  and and_1 (and_1_out, not_2_out, not_1_out);
  nor nor_2 (ACRL1, and_1_out, nor_1_out);
  DLATCH dlatch_1 (.C(PHI1), .D(ACRL1), .nQ(dlatch_1_nq));  // open: Q
  DLATCH dlatch_2 (.C(PHI2), .D(dlatch_1_nq), .nQ(ACRL2));  // open: Q
endmodule
