// Digital circuit DispFetch.dig as structural Verilog
module DispFetch (
  input  B_OUT,
  input  PHI2,
  input  T1,
  input  nready,
  output Z_IR,
  output FETCH
);

  wire dlatch_1_nq;

  DLATCH dlatch_1 (.C(PHI2), .D(T1), .nQ(dlatch_1_nq));  // open: Q
  nor nor_1 (FETCH, dlatch_1_nq, nready);
  nand nand_1 (Z_IR, B_OUT, FETCH);
endmodule
