// Digital circuit DispRMWCycle.dig as structural Verilog
module DispRMWCycle (
  input  PHI1,
  input  PHI2,
  input  nready,
  input  nSHIFT,
  input  nMemOP,
  output T6,
  output T7
);

  wire and_1_out, dlatch_1_q, dlatch_2_q, dlatch_4_nq, dlatch_5_nq, nand_1_out, nor_1_out, nor_2_out,
       not_1_out;

  nor nor_1 (nor_1_out, nSHIFT, nMemOP, nready);
  DLATCH dlatch_1 (.C(PHI2), .D(nor_1_out), .Q(dlatch_1_q));  // open: nQ
  and and_1 (and_1_out, dlatch_2_q, nready);
  nor nor_2 (nor_2_out, and_1_out, dlatch_1_q);
  DLATCH dlatch_2 (.C(PHI2), .D(T6), .Q(dlatch_2_q));  // open: nQ
  DLATCH dlatch_3 (.C(PHI1), .D(nor_2_out), .nQ(T6));  // open: Q
  not not_1 (not_1_out, nready);
  nand nand_1 (nand_1_out, T6, not_1_out);
  DLATCH dlatch_4 (.C(PHI2), .D(nand_1_out), .nQ(dlatch_4_nq));  // open: Q
  DLATCH dlatch_5 (.C(PHI1), .D(dlatch_4_nq), .nQ(dlatch_5_nq));  // open: Q
  not not_2 (T7, dlatch_5_nq);
endmodule
