// Digital circuit DispatchUnit.dig as structural Verilog
module DispatchUnit (
  input  PHI1,
  input  PHI2,
  input  RDY,
  input  DORES,
  input  RESP,
  input  BRFW,
  input  nBRTAKEN,
  input  ACR,
  input  nIMPLIED,
  input  nTWOCYCLE,
  input  B_OUT,
  input  nADL_PCL,
  input  BRK6E,
  input  PC_DB,
  input  [63:0] dec2,
  output nready,
  output WR,
  output T0,
  output T1,
  output nT0,
  output nT1X,
  output T6,
  output T7,
  output ACRL2,
  output TRES2,
  output nIPC,
  output STOR,
  output Z_IR,
  output FETCH
);

  wire acrl_acrl1, comp_ends, comp_ntresx, dispincrementpc_1_bra, nMemOP, not_1_out, nSHIFT,
       ready_rw_notreadyphi1, REST;

  nor nor_1 (nSHIFT, dec2[42], dec2[43]);
  nor nor_2 (nMemOP, dec2[47], dec2[58], dec2[59], dec2[60], dec2[61]);
  not not_1 (not_1_out, dec2[33]);
  nand nand_1 (REST, nSHIFT, not_1_out);
  nor nor_3 (STOR, not_1_out, nMemOP);
  DispReadyRW ready_rw (
    .PHI1(PHI1), .PHI2(PHI2), .RDY(RDY), .STOR(STOR), .PC_DB(PC_DB), .D98(dec2[34]), .D100(dec2[36]),
    .T6(T6), .T7(T7), .DORES(DORES), .nready(nready), .NotReadyPhi1(ready_rw_notreadyphi1), .WR(WR));
  DispACRLatch acrl (
    .PHI1(PHI1), .PHI2(PHI2), .ACR(ACR), .NotReadyPhi1(ready_rw_notreadyphi1), .ACRL1(acrl_acrl1),
    .ACRL2(ACRL2));
  DispRMWCycle disprmwcycle_1 (
    .PHI1(PHI1), .PHI2(PHI2), .nready(nready), .nSHIFT(nSHIFT), .nMemOP(nMemOP), .T6(T6), .T7(T7));
  DispShortCycle dispshortcycle_1 (
    .PHI1(PHI1), .PHI2(PHI2), .nready(nready), .RESP(RESP), .BRA(dispincrementpc_1_bra), .ENDS(comp_ends),
    .nTWOCYCLE(nTWOCYCLE), .nTRESX(comp_ntresx), .T1(T1), .nT0(nT0), .T0(T0), .nT1X(nT1X));
  DispCompletionUnit comp (
    .PHI1(PHI1), .PHI2(PHI2), .nready(nready), .ACRL1(acrl_acrl1), .D91(dec2[27]), .D92(dec2[28]),
    .REST(REST), .BRK6E(BRK6E), .RESP(RESP), .nSHIFT(nSHIFT), .nMemOP(nMemOP), .T7(T7), .D96(dec2[32]),
    .D100(dec2[36]), .D101(dec2[37]), .D102(dec2[38]), .D103(dec2[39]), .D104(dec2[40]), .D105(dec2[41]),
    .T0(T0), .nBRTAKEN(nBRTAKEN), .T1(T1), .BR2(dec2[16]), .BR3(dec2[29]), .TRES2(TRES2),
    .nTRESX(comp_ntresx), .ENDS(comp_ends));
  DispIncrementPC dispincrementpc_1 (
    .PHI1(PHI1), .PHI2(PHI2), .B_OUT(B_OUT), .NotReadyPhi1(ready_rw_notreadyphi1), .BRFW(BRFW), .ACR(ACR),
    .nready(nready), .nBRTAKEN(nBRTAKEN), .nADL_PCL(nADL_PCL), .nIMPLIED(nIMPLIED), .BR2(dec2[16]),
    .BR3(dec2[29]), .BRA(dispincrementpc_1_bra), .nIPC(nIPC));
  DispFetch dispfetch_1 (.B_OUT(B_OUT), .PHI2(PHI2), .T1(T1), .nready(nready), .Z_IR(Z_IR), .FETCH(FETCH));

  // Other names for the same wires on the sheet: BR2 = dec2[16]; BR3 = dec2[29]
endmodule
