// Digital circuit EXTENDED_CYCLE_COUNTER.dig as structural Verilog
module EXTENDED_CYCLE_COUNTER (
  input  PHI1,
  input  PHI2,
  input  TRES2,
  input  nready,
  input  T1,
  output nT2,
  output nT3,
  output nT4,
  output nT5
);

  wire dlatch_1_nq, dlatch_2_nq, dlatch_3_q, dlatch_4_nq, dlatch_5_q, dlatch_6_nq, dlatch_7_q, dlatch_8_nq,
       dlatch_9_q, multiplexer_1_out, multiplexer_2_out, multiplexer_3_out, multiplexer_4_out, nor_1_out,
       nor_2_out, nor_3_out, nor_4_out;

  DLATCH dlatch_1 (.C(PHI2), .D(T1), .nQ(dlatch_1_nq));  // open: Q
  Multiplexer multiplexer_1 (.sel(nready), .in_0(dlatch_1_nq), .in_1(dlatch_2_nq), .out(multiplexer_1_out));
  Multiplexer multiplexer_2 (.sel(nready), .in_0(dlatch_2_nq), .in_1(dlatch_4_nq), .out(multiplexer_2_out));
  Multiplexer multiplexer_3 (.sel(nready), .in_0(dlatch_4_nq), .in_1(dlatch_6_nq), .out(multiplexer_3_out));
  Multiplexer multiplexer_4 (.sel(nready), .in_0(dlatch_6_nq), .in_1(dlatch_8_nq), .out(multiplexer_4_out));
  nor nor_1 (nor_1_out, TRES2, dlatch_3_q);
  nor nor_2 (nor_2_out, TRES2, dlatch_5_q);
  nor nor_3 (nor_3_out, TRES2, dlatch_7_q);
  nor nor_4 (nor_4_out, TRES2, dlatch_9_q);
  DLATCH dlatch_2 (.C(PHI2), .D(nor_1_out), .nQ(dlatch_2_nq));  // open: Q
  DLATCH dlatch_3 (.C(PHI1), .D(multiplexer_1_out), .Q(dlatch_3_q));  // open: nQ
  DLATCH dlatch_4 (.C(PHI2), .D(nor_2_out), .nQ(dlatch_4_nq));  // open: Q
  DLATCH dlatch_5 (.C(PHI1), .D(multiplexer_2_out), .Q(dlatch_5_q));  // open: nQ
  DLATCH dlatch_6 (.C(PHI2), .D(nor_3_out), .nQ(dlatch_6_nq));  // open: Q
  DLATCH dlatch_7 (.C(PHI1), .D(multiplexer_3_out), .Q(dlatch_7_q));  // open: nQ
  DLATCH dlatch_8 (.C(PHI2), .D(nor_4_out), .nQ(dlatch_8_nq));  // open: Q
  DLATCH dlatch_9 (.C(PHI1), .D(multiplexer_4_out), .Q(dlatch_9_q));  // open: nQ
  not not_1 (nT2, nor_1_out);
  not not_2 (nT3, nor_2_out);
  not not_3 (nT4, nor_3_out);
  not not_4 (nT5, nor_4_out);
endmodule
