// Digital circuit FLAGS_CONTROL.dig as structural Verilog
module FLAGS_CONTROL (
  input  PHI2,
  input  D98,
  input  D99,
  input  D108,
  input  D110,
  input  D120,
  input  D127,
  input  D107,
  input  T7,
  input  D112,
  input  D116,
  input  D117,
  input  D118,
  input  D119,
  input  ZTST,
  input  D109,
  input  nready,
  input  SR,
  input  D114,
  input  D115,
  input  D113,
  output P_DB,
  output IR5_I,
  output IR5_C,
  output IR5_D,
  output Z_V,
  output ARC_C,
  output DBZ_Z,
  output DB_N,
  output DB_P,
  output DB_C,
  output DB_V
);

  wire and_1_out, and_2_out, dlatch_7_q, dlatch_8_q, dlatch_10_q, dlatch_11_q, nor_1_out, nor_2_out,
       nor_3_out, nor_4_out, nor_5_out, not_1_out, not_2_out, not_3_out, not_4_out, not_5_out;

  nor nor_1 (nor_1_out, D98, D99);
  and and_1 (and_1_out, D107, T7);
  nor nor_2 (nor_2_out, D114, D115);
  not not_1 (not_1_out, D108);
  not not_2 (not_2_out, D110);
  not not_3 (not_3_out, D120);
  not not_4 (not_4_out, D127);
  not not_5 (not_5_out, D113);
  nor nor_3 (nor_3_out, and_1_out, D112, D116, D117, D118, D119);
  nor nor_4 (nor_4_out, ARC_C, ZTST, D109);
  nor nor_5 (nor_5_out, SR, DB_P);
  DLATCH dlatch_1 (.C(PHI2), .D(nor_1_out), .Q(P_DB));  // open: nQ
  DLATCH dlatch_2 (.C(PHI2), .D(not_1_out), .Q(IR5_I));  // open: nQ
  DLATCH dlatch_3 (.C(PHI2), .D(not_2_out), .Q(IR5_C));  // open: nQ
  DLATCH dlatch_4 (.C(PHI2), .D(not_3_out), .Q(IR5_D));  // open: nQ
  DLATCH dlatch_5 (.C(PHI2), .D(not_4_out), .Q(Z_V));  // open: nQ
  DLATCH dlatch_6 (.C(PHI2), .D(nor_3_out), .nQ(ARC_C));  // open: Q
  DLATCH dlatch_7 (.C(PHI2), .D(nor_4_out), .Q(dlatch_7_q), .nQ(DBZ_Z));
  DLATCH dlatch_8 (.C(PHI2), .D(D109), .Q(dlatch_8_q));  // open: nQ
  DLATCH dlatch_9 (.C(PHI2), .D(nor_5_out), .nQ(DB_C));  // open: Q
  DLATCH dlatch_10 (.C(PHI2), .D(nor_2_out), .Q(dlatch_10_q));  // open: nQ
  DLATCH dlatch_11 (.C(PHI2), .D(not_5_out), .Q(dlatch_11_q));  // open: nQ
  and and_2 (and_2_out, dlatch_7_q, dlatch_10_q);
  nor nor_6 (DB_P, dlatch_10_q, nready);
  nand nand_1 (DB_V, dlatch_10_q, dlatch_11_q);
  nor nor_7 (DB_N, and_2_out, dlatch_8_q);
endmodule
