// Digital circuit INT_FF.dig as structural Verilog
module INT_FF (
  input  phi2,
  input  d,
  output q,
  output nq
);

  wire and_1_out, and_2_out, not_1_out;

  not not_1 (not_1_out, d);
  and and_1 (and_1_out, phi2, not_1_out);
  and and_2 (and_2_out, phi2, d);
  nor nor_1 (q, and_1_out, nq);
  nor nor_2 (nq, and_2_out, q);
endmodule
