// Digital circuit INT_RESET_CONTROL.dig as structural Verilog
module INT_RESET_CONTROL (
  input  PHI1,
  input  PHI2,
  input  BRK5,
  input  nready,
  input  RESP,
  input  nNMIP,
  input  BR2,
  input  T0,
  input  nIRQP,
  input  nI_OUT,
  output B_OUT,
  output nDONMI,
  output DORES,
  output BRK5_RDY,
  output BRK7,
  output BRK6E
);

  wire and_2_out, and_3_out, dlatch_1_q, dlatch_2_q, dlatch_3_q, dlatch_4_nq, dlatch_5_q, dlatch_6_nq,
       dlatch_7_q, dlatch_8_q, dlatch_9_q, dlatch_10_q, dlatch_11_q, dlatch_12_nq, dlatch_13_q, dlatch_14_nq,
       dlatch_15_q, nand_1_out, nand_2_out, nand_3_out, nor_1_out, nor_2_out, nor_3_out, nor_4_out,
       nor_5_out, nor_6_out, nor_9_out, not_1_out, not_2_out, not_3_out, not_4_out, or_1_out, or_2_out;

  and and_1 (BRK5_RDY, BRK5, not_1_out);
  not not_1 (not_1_out, nready);
  DLATCH dlatch_1 (.C(PHI2), .D(BRK5_RDY), .Q(dlatch_1_q));  // open: nQ
  DLATCH dlatch_2 (.C(PHI2), .D(RESP), .Q(dlatch_2_q));  // open: nQ
  DLATCH dlatch_3 (.C(PHI1), .D(nor_4_out), .Q(dlatch_3_q));  // open: nQ
  DLATCH dlatch_4 (.C(PHI2), .D(BRK7), .nQ(dlatch_4_nq));  // open: Q
  DLATCH dlatch_5 (.C(PHI1), .D(nNMIP), .Q(dlatch_5_q));  // open: nQ
  DLATCH dlatch_6 (.C(PHI2), .D(nDONMI), .nQ(dlatch_6_nq));  // open: Q
  DLATCH dlatch_7 (.C(PHI2), .D(nDONMI), .Q(dlatch_7_q));  // open: nQ
  DLATCH dlatch_8 (.C(PHI1), .D(BRK6E), .Q(dlatch_8_q));  // open: nQ
  not not_2 (not_2_out, nI_OUT);
  DLATCH dlatch_9 (.C(PHI1), .D(nor_9_out), .Q(dlatch_9_q));  // open: nQ
  not not_3 (not_3_out, dlatch_1_q);
  nand nand_1 (nand_1_out, nready, dlatch_12_nq);
  or or_1 (or_1_out, nIRQP, not_2_out);
  and and_2 (and_2_out, nand_3_out, not_4_out);
  not not_4 (not_4_out, dlatch_9_q);
  and and_3 (and_3_out, not_3_out, nand_1_out);
  nor nor_1 (nor_1_out, dlatch_2_q, dlatch_3_q);
  nor nor_2 (nor_2_out, dlatch_5_q, nor_6_out);
  DLATCH dlatch_10 (.C(PHI2), .D(nor_2_out), .Q(dlatch_10_q));  // open: nQ
  DLATCH dlatch_11 (.C(PHI1), .D(dlatch_6_nq), .Q(dlatch_11_q));  // open: nQ
  nor nor_3 (nor_3_out, dlatch_7_q, dlatch_8_q);
  nand nand_2 (nand_2_out, or_1_out, nDONMI);
  DLATCH dlatch_12 (.C(PHI1), .D(and_3_out), .nQ(dlatch_12_nq));  // open: Q
  nor nor_4 (nor_4_out, nor_1_out, BRK6E);
  nor nor_5 (nor_5_out, dlatch_4_nq, nNMIP, nor_2_out);
  nor nor_6 (nor_6_out, dlatch_10_q, dlatch_11_q);
  nor nor_7 (nDONMI, dlatch_15_q, nor_3_out);
  or or_2 (or_2_out, BR2, T0);
  DLATCH dlatch_13 (.C(PHI2), .D(and_2_out), .Q(dlatch_13_q));  // open: nQ
  not not_5 (DORES, nor_1_out);
  nand nand_3 (nand_3_out, or_2_out, nand_2_out);
  DLATCH dlatch_14 (.C(PHI2), .D(dlatch_12_nq), .nQ(dlatch_14_nq));  // open: Q
  nor nor_8 (BRK7, dlatch_12_nq, BRK5_RDY);
  nor nor_9 (nor_9_out, dlatch_13_q, BRK6E);
  DLATCH dlatch_15 (.C(PHI1), .D(nor_5_out), .Q(dlatch_15_q));  // open: nQ
  nor nor_10 (BRK6E, dlatch_14_nq, nready);
  nor nor_11 (B_OUT, DORES, nor_9_out);
endmodule
