// Digital circuit INT_VECTR_Logic.dig as structural Verilog
module INT_VECTR_Logic (
  input  PHI2,
  input  BRK5_RDY,
  input  BRK7,
  input  DORES,
  input  nDONMI,
  output Z_ADL0,
  output Z_ADL1,
  output Z_ADL2
);

  wire dlatch_3_nq, nor_1_out, nor_2_out, not_1_out, not_2_out, not_3_out;

  not not_1 (not_1_out, DORES);
  not not_2 (not_2_out, BRK5_RDY);
  nor nor_1 (nor_1_out, BRK7, not_1_out);
  nor nor_2 (nor_2_out, BRK7, DORES, nDONMI);
  not not_3 (not_3_out, nor_1_out);
  DLATCH dlatch_1 (.C(PHI2), .D(not_2_out), .nQ(Z_ADL0));  // open: Q
  DLATCH dlatch_2 (.C(PHI2), .D(not_3_out), .nQ(Z_ADL1));  // open: Q
  DLATCH dlatch_3 (.C(PHI2), .D(nor_2_out), .nQ(dlatch_3_nq));  // open: Q
  not not_4 (Z_ADL2, dlatch_3_nq);
endmodule
