// Digital circuit IR.dig as structural Verilog
module IR (
  input  nin0,
  input  PHI1,
  input  FETCH,
  input  nin1,
  input  nin2,
  input  nin3,
  input  nin4,
  input  nin5,
  input  nin6,
  input  nin7,
  output IR0,
  output IR1,
  output IR2,
  output IR3,
  output IR4,
  output IR5,
  output IR6,
  output IR7
);

  wire and_1_out;

  and and_1 (and_1_out, FETCH, PHI1);
  DLATCH dlatch_1 (.C(and_1_out), .D(nin0), .nQ(IR0));  // open: Q
  DLATCH dlatch_2 (.C(and_1_out), .D(nin1), .nQ(IR1));  // open: Q
  DLATCH dlatch_3 (.C(and_1_out), .D(nin2), .nQ(IR2));  // open: Q
  DLATCH dlatch_4 (.C(and_1_out), .D(nin3), .nQ(IR3));  // open: Q
  DLATCH dlatch_5 (.C(and_1_out), .D(nin4), .nQ(IR4));  // open: Q
  DLATCH dlatch_6 (.C(and_1_out), .D(nin5), .nQ(IR5));  // open: Q
  DLATCH dlatch_7 (.C(and_1_out), .D(nin6), .nQ(IR6));  // open: Q
  DLATCH dlatch_8 (.C(and_1_out), .D(nin7), .nQ(IR7));  // open: Q
endmodule
