// Digital circuit PCH_EVEN_BIT.dig as structural Verilog
module PCH_EVEN_BIT (
  input  PHI2,
  input  cin,
  input  ADH_PCH,
  input  PCH_PCH,
  input  PCH_ADH,
  input  PCH_DB,
  input  ADHx_in,
  input  in_14,
  input  in_15,
  input  in_16,
  output DBx,
  output ADHx_out,
  output sout,
  output cout,
  output PCH_Debug,
  output PCHS_Debug
);

  wire and_1_out, dff_posedge_1_nq, driver_1_out, nand_1_out, not_1_out;

  nor nor_1 (cout, cin, sout);
  nand nand_1 (nand_1_out, cin, sout);
  not not_1 (not_1_out, cout);
  assign driver_1_out = PCH_PCH ? PCH_Debug : 1'bz;  // Driver driver_1
  assign driver_1_out = ADH_PCH ? ADHx_in : 1'bz;  // Driver driver_2
  and and_1 (and_1_out, nand_1_out, not_1_out);
  DFF_Posedge dff_posedge_1 (.nQ(dff_posedge_1_nq), .EN(PHI2), .D(and_1_out));  // open: Q
  DFF_Level dff_level_1 (.Q(PCHS_Debug), .nQ(sout), .EN(1'b1), .D(driver_1_out));
  not not_2 (PCH_Debug, dff_posedge_1_nq);
  assign DBx = PCH_DB ? PCH_Debug : 1'bz;  // Driver driver_3
  assign ADHx_out = PCH_ADH ? PCH_Debug : 1'bz;  // Driver driver_4
endmodule
