// Digital circuit PCH_ODD_BIT.dig as structural Verilog
module PCH_ODD_BIT (
  input  PHI2,
  input  cin,
  input  ADH_PCH,
  input  PCH_PCH,
  input  PCH_ADH,
  input  PCH_DB,
  input  ADHx_in,
  input  in_14,
  input  in_15,
  input  in_16,
  output DBx,
  output ADHx_out,
  output sout,
  output cout,
  output PCH_Debug,
  output PCHS_Debug
);

  wire driver_1_out, nor_1_out, not_1_out, not_2_out, not_3_out, or_1_out;

  not not_1 (not_1_out, sout);
  nand nand_1 (cout, cin, not_1_out);
  not not_2 (not_2_out, sout);
  nor nor_1 (nor_1_out, cin, not_2_out);
  not not_3 (not_3_out, cout);
  assign driver_1_out = PCH_PCH ? PCH_Debug : 1'bz;  // Driver driver_1
  assign driver_1_out = ADH_PCH ? ADHx_in : 1'bz;  // Driver driver_2
  or or_1 (or_1_out, nor_1_out, not_3_out);
  DFF_Posedge dff_posedge_1 (.nQ(PCH_Debug), .EN(PHI2), .D(or_1_out));  // open: Q
  DFF_Level dff_level_1 (.Q(PCHS_Debug), .nQ(sout), .EN(1'b1), .D(driver_1_out));
  assign DBx = PCH_DB ? PCH_Debug : 1'bz;  // Driver driver_3
  assign ADHx_out = PCH_ADH ? PCH_Debug : 1'bz;  // Driver driver_4
endmodule
