// Digital circuit PCL.dig as structural Verilog
module PCL (
  input  PHI2,
  input  cin,
  input  ADL_PCL,
  input  PCL_PCL,
  input  PCL_ADL,
  input  PCL_DB,
  input  ADL0,
  input  ADL1,
  input  ADL2,
  input  ADL3,
  input  ADL4,
  input  ADL5,
  input  ADL6,
  input  ADL7,
  output ADL0_out,
  output ADL1_out,
  output ADL2_out,
  output ADL3_out,
  output ADL4_out,
  output ADL5_out,
  output ADL6_out,
  output ADL7_out,
  output DB0,
  output DB1,
  output DB2,
  output DB3,
  output DB4,
  output DB5,
  output DB6,
  output DB7,
  output PCLC,
  output [7:0] PCL_Debug,
  output [7:0] PCLS_Debug
);

  wire notconnected_1_out, notconnected_2_out, notconnected_3_out, notconnected_4_out, notconnected_5_out,
       notconnected_6_out, notconnected_7_out, notconnected_8_out, notconnected_9_out, notconnected_10_out,
       notconnected_11_out, notconnected_12_out, notconnected_13_out, notconnected_14_out,
       notconnected_15_out, notconnected_16_out, notconnected_17_out, notconnected_18_out,
       notconnected_19_out, notconnected_20_out, notconnected_21_out, notconnected_22_out,
       notconnected_23_out, notconnected_24_out, pcl_even_bit_1_cout, pcl_even_bit_1_sout,
       pcl_even_bit_2_cout, pcl_even_bit_2_sout, pcl_even_bit_3_cout, pcl_even_bit_3_sout,
       pcl_even_bit_4_cout, pcl_even_bit_4_sout, pcl_odd_bit_1_cout, pcl_odd_bit_1_sout, pcl_odd_bit_2_cout,
       pcl_odd_bit_2_sout, pcl_odd_bit_3_cout, pcl_odd_bit_3_sout, pcl_odd_bit_4_sout;

  PCL_EVEN_BIT pcl_even_bit_1 (
    .PHI2(PHI2), .in_14(notconnected_1_out), .cin(cin), .in_15(notconnected_2_out), .ADL_PCL(ADL_PCL),
    .PCL_PCL(PCL_PCL), .PCL_ADL(PCL_ADL), .PCL_DB(PCL_DB), .in_16(notconnected_3_out), .ADLx_in(ADL0),
    .ADLx(ADL0_out), .DBx(DB0), .cout(pcl_even_bit_1_cout), .sout(pcl_even_bit_1_sout),
    .PCL_Debug(PCL_Debug[0]), .PCLS_Debug(PCLS_Debug[0]));
  // NotConnected on notconnected_1_out
  // NotConnected on notconnected_2_out
  // NotConnected on notconnected_3_out
  PCL_ODD_BIT pcl_odd_bit_1 (
    .PHI2(PHI2), .in_14(notconnected_4_out), .cin(pcl_even_bit_1_cout), .in_15(notconnected_5_out),
    .ADL_PCL(ADL_PCL), .PCL_PCL(PCL_PCL), .PCL_ADL(PCL_ADL), .PCL_DB(PCL_DB), .in_16(notconnected_6_out),
    .ADLx_in(ADL1), .ADLx(ADL1_out), .DBx(DB1), .cout(pcl_odd_bit_1_cout), .sout(pcl_odd_bit_1_sout),
    .PCL_Debug(PCL_Debug[1]), .PCLS_Debug(PCLS_Debug[1]));
  // NotConnected on notconnected_4_out
  // NotConnected on notconnected_5_out
  // NotConnected on notconnected_6_out
  PCL_EVEN_BIT pcl_even_bit_2 (
    .PHI2(PHI2), .in_14(notconnected_7_out), .cin(pcl_odd_bit_1_cout), .in_15(notconnected_8_out),
    .ADL_PCL(ADL_PCL), .PCL_PCL(PCL_PCL), .PCL_ADL(PCL_ADL), .PCL_DB(PCL_DB), .in_16(notconnected_9_out),
    .ADLx_in(ADL2), .ADLx(ADL2_out), .DBx(DB2), .cout(pcl_even_bit_2_cout), .sout(pcl_even_bit_2_sout),
    .PCL_Debug(PCL_Debug[2]), .PCLS_Debug(PCLS_Debug[2]));
  // NotConnected on notconnected_7_out
  // NotConnected on notconnected_8_out
  // NotConnected on notconnected_9_out
  PCL_ODD_BIT pcl_odd_bit_2 (
    .PHI2(PHI2), .in_14(notconnected_10_out), .cin(pcl_even_bit_2_cout), .in_15(notconnected_11_out),
    .ADL_PCL(ADL_PCL), .PCL_PCL(PCL_PCL), .PCL_ADL(PCL_ADL), .PCL_DB(PCL_DB), .in_16(notconnected_12_out),
    .ADLx_in(ADL3), .ADLx(ADL3_out), .DBx(DB3), .cout(pcl_odd_bit_2_cout), .sout(pcl_odd_bit_2_sout),
    .PCL_Debug(PCL_Debug[3]), .PCLS_Debug(PCLS_Debug[3]));
  // NotConnected on notconnected_10_out
  // NotConnected on notconnected_11_out
  // NotConnected on notconnected_12_out
  PCL_EVEN_BIT pcl_even_bit_3 (
    .PHI2(PHI2), .in_14(notconnected_13_out), .cin(pcl_odd_bit_2_cout), .in_15(notconnected_14_out),
    .ADL_PCL(ADL_PCL), .PCL_PCL(PCL_PCL), .PCL_ADL(PCL_ADL), .PCL_DB(PCL_DB), .in_16(notconnected_15_out),
    .ADLx_in(ADL4), .ADLx(ADL4_out), .DBx(DB4), .cout(pcl_even_bit_3_cout), .sout(pcl_even_bit_3_sout),
    .PCL_Debug(PCL_Debug[4]), .PCLS_Debug(PCLS_Debug[4]));
  // NotConnected on notconnected_13_out
  // NotConnected on notconnected_14_out
  // NotConnected on notconnected_15_out
  PCL_ODD_BIT pcl_odd_bit_3 (
    .PHI2(PHI2), .in_14(notconnected_16_out), .cin(pcl_even_bit_3_cout), .in_15(notconnected_17_out),
    .ADL_PCL(ADL_PCL), .PCL_PCL(PCL_PCL), .PCL_ADL(PCL_ADL), .PCL_DB(PCL_DB), .in_16(notconnected_18_out),
    .ADLx_in(ADL5), .ADLx(ADL5_out), .DBx(DB5), .cout(pcl_odd_bit_3_cout), .sout(pcl_odd_bit_3_sout),
    .PCL_Debug(PCL_Debug[5]), .PCLS_Debug(PCLS_Debug[5]));
  // NotConnected on notconnected_16_out
  // NotConnected on notconnected_17_out
  // NotConnected on notconnected_18_out
  PCL_EVEN_BIT pcl_even_bit_4 (
    .PHI2(PHI2), .in_14(notconnected_19_out), .cin(pcl_odd_bit_3_cout), .in_15(notconnected_20_out),
    .ADL_PCL(ADL_PCL), .PCL_PCL(PCL_PCL), .PCL_ADL(PCL_ADL), .PCL_DB(PCL_DB), .in_16(notconnected_21_out),
    .ADLx_in(ADL6), .ADLx(ADL6_out), .DBx(DB6), .cout(pcl_even_bit_4_cout), .sout(pcl_even_bit_4_sout),
    .PCL_Debug(PCL_Debug[6]), .PCLS_Debug(PCLS_Debug[6]));
  // NotConnected on notconnected_19_out
  // NotConnected on notconnected_20_out
  // NotConnected on notconnected_21_out
  PCL_ODD_BIT pcl_odd_bit_4 (
    .PHI2(PHI2), .in_14(notconnected_22_out), .cin(pcl_even_bit_4_cout), .in_15(notconnected_23_out),
    .ADL_PCL(ADL_PCL), .PCL_PCL(PCL_PCL), .PCL_ADL(PCL_ADL), .PCL_DB(PCL_DB), .in_16(notconnected_24_out),
    .ADLx_in(ADL7), .ADLx(ADL7_out), .DBx(DB7), .sout(pcl_odd_bit_4_sout), .PCL_Debug(PCL_Debug[7]),
    .PCLS_Debug(PCLS_Debug[7]));  // open: cout
  // NotConnected on notconnected_22_out
  // NotConnected on notconnected_23_out
  // NotConnected on notconnected_24_out
  nor nor_1 (PCLC, pcl_even_bit_1_sout, pcl_odd_bit_1_sout, pcl_even_bit_2_sout, pcl_odd_bit_2_sout, cin, pcl_even_bit_3_sout, pcl_odd_bit_3_sout, pcl_even_bit_4_sout, pcl_odd_bit_4_sout);
endmodule
