// Digital circuit PCL_EVEN_BIT.dig as structural Verilog
module PCL_EVEN_BIT (
  input  PHI2,
  input  cin,
  input  ADL_PCL,
  input  PCL_PCL,
  input  PCL_ADL,
  input  PCL_DB,
  input  ADLx_in,
  input  in_14,
  input  in_15,
  input  in_16,
  output DBx,
  output ADLx,
  output sout,
  output cout,
  output PCL_Debug,
  output PCLS_Debug
);

  wire and_1_out, dff_posedge_1_nq, driver_1_out, nand_1_out, not_1_out;

  nor nor_1 (cout, cin, sout);
  nand nand_1 (nand_1_out, cin, sout);
  not not_1 (not_1_out, cout);
  assign driver_1_out = PCL_PCL ? PCL_Debug : 1'bz;  // Driver driver_1
  assign driver_1_out = ADL_PCL ? ADLx_in : 1'bz;  // Driver driver_2
  and and_1 (and_1_out, nand_1_out, not_1_out);
  DFF_Posedge dff_posedge_1 (.nQ(dff_posedge_1_nq), .EN(PHI2), .D(and_1_out));  // open: Q
  DFF_Level dff_level_1 (.Q(PCLS_Debug), .nQ(sout), .EN(1'b1), .D(driver_1_out));
  not not_2 (PCL_Debug, dff_posedge_1_nq);
  assign DBx = PCL_DB ? PCL_Debug : 1'bz;  // Driver driver_3
  assign ADLx = PCL_ADL ? PCL_Debug : 1'bz;  // Driver driver_4
endmodule
