// Digital circuit PCL_ODD_BIT.dig as structural Verilog
module PCL_ODD_BIT (
  input  PHI2,
  input  cin,
  input  ADL_PCL,
  input  PCL_PCL,
  input  PCL_ADL,
  input  PCL_DB,
  input  ADLx_in,
  input  in_14,
  input  in_15,
  input  in_16,
  output DBx,
  output ADLx,
  output sout,
  output cout,
  output PCL_Debug,
  output PCLS_Debug
);

  wire driver_1_out, nor_1_out, not_1_out, not_2_out, not_3_out, or_1_out;

  not not_1 (not_1_out, sout);
  nand nand_1 (cout, cin, not_1_out);
  not not_2 (not_2_out, sout);
  nor nor_1 (nor_1_out, cin, not_2_out);
  not not_3 (not_3_out, cout);
  assign driver_1_out = PCL_PCL ? PCL_Debug : 1'bz;  // Driver driver_1
  assign driver_1_out = ADL_PCL ? ADLx_in : 1'bz;  // Driver driver_2
  or or_1 (or_1_out, nor_1_out, not_3_out);
  DFF_Posedge dff_posedge_1 (.nQ(PCL_Debug), .EN(PHI2), .D(or_1_out));  // open: Q
  DFF_Level dff_level_1 (.Q(PCLS_Debug), .nQ(sout), .EN(1'b1), .D(driver_1_out));
  assign DBx = PCL_DB ? PCL_Debug : 1'bz;  // Driver driver_3
  assign ADLx = PCL_ADL ? PCL_Debug : 1'bz;  // Driver driver_4
endmodule
