// Digital circuit PRECODE.dig as structural Verilog
module PRECODE (
  input  PHI2,
  input  Z_IR,
  input  D0,
  input  D1,
  input  D2,
  input  D3,
  input  D4,
  input  D5,
  input  D6,
  input  D7,
  output nIMPLIED,
  output nTWOCYCLE,
  output nPD0,
  output nPD1,
  output nPD2,
  output nPD3,
  output nPD4,
  output nPD5,
  output nPD6,
  output nPD7
);

  wire and_1_out, dlatch_1_nq, dlatch_2_nq, dlatch_3_nq, dlatch_4_nq, dlatch_5_nq, dlatch_6_nq, dlatch_7_nq,
       dlatch_8_nq, dlatch_9_q, dlatch_10_q, dlatch_11_q, dlatch_12_q, dlatch_13_q, dlatch_14_q, dlatch_15_q,
       dlatch_16_q, nor_1_out, nor_2_out, nor_3_out, nor_4_out, nor_5_out, nor_6_out, nor_7_out, nor_8_out,
       nor_10_out, nor_11_out, nor_12_out, not_1_out;

  DLATCH dlatch_1 (.C(1'b1), .D(D0), .nQ(dlatch_1_nq));  // open: Q
  DLATCH dlatch_2 (.C(1'b1), .D(D1), .nQ(dlatch_2_nq));  // open: Q
  DLATCH dlatch_3 (.C(1'b1), .D(D2), .nQ(dlatch_3_nq));  // open: Q
  DLATCH dlatch_4 (.C(1'b1), .D(D3), .nQ(dlatch_4_nq));  // open: Q
  DLATCH dlatch_5 (.C(1'b1), .D(D4), .nQ(dlatch_5_nq));  // open: Q
  DLATCH dlatch_6 (.C(1'b1), .D(D5), .nQ(dlatch_6_nq));  // open: Q
  DLATCH dlatch_7 (.C(1'b1), .D(D6), .nQ(dlatch_7_nq));  // open: Q
  DLATCH dlatch_8 (.C(1'b1), .D(D7), .nQ(dlatch_8_nq));  // open: Q
  DLATCH dlatch_9 (.C(PHI2), .D(dlatch_1_nq), .Q(dlatch_9_q));  // open: nQ
  DLATCH dlatch_10 (.C(PHI2), .D(dlatch_2_nq), .Q(dlatch_10_q));  // open: nQ
  DLATCH dlatch_11 (.C(PHI2), .D(dlatch_3_nq), .Q(dlatch_11_q));  // open: nQ
  DLATCH dlatch_12 (.C(PHI2), .D(dlatch_4_nq), .Q(dlatch_12_q));  // open: nQ
  DLATCH dlatch_13 (.C(PHI2), .D(dlatch_5_nq), .Q(dlatch_13_q));  // open: nQ
  DLATCH dlatch_14 (.C(PHI2), .D(dlatch_6_nq), .Q(dlatch_14_q));  // open: nQ
  DLATCH dlatch_15 (.C(PHI2), .D(dlatch_7_nq), .Q(dlatch_15_q));  // open: nQ
  DLATCH dlatch_16 (.C(PHI2), .D(dlatch_8_nq), .Q(dlatch_16_q));  // open: nQ
  nor nor_1 (nor_1_out, dlatch_9_q, Z_IR);
  nor nor_2 (nor_2_out, dlatch_10_q, Z_IR);
  nor nor_3 (nor_3_out, dlatch_11_q, Z_IR);
  nor nor_4 (nor_4_out, dlatch_12_q, Z_IR);
  nor nor_5 (nor_5_out, dlatch_13_q, Z_IR);
  nor nor_6 (nor_6_out, dlatch_14_q, Z_IR);
  nor nor_7 (nor_7_out, dlatch_15_q, Z_IR);
  nor nor_8 (nor_8_out, dlatch_16_q, Z_IR);
  nor nor_9 (nIMPLIED, nor_1_out, nor_3_out, nPD3);
  nor nor_10 (nor_10_out, nor_2_out, nor_5_out, nor_8_out);
  not not_1 (not_1_out, nor_10_out);
  nor nor_11 (nor_11_out, nPD0, nor_3_out, nPD3, nor_5_out);
  nor nor_12 (nor_12_out, nor_1_out, nor_3_out, nor_4_out, nor_5_out, nPD7);
  not not_2 (nPD0, nor_1_out);
  not not_3 (nPD1, nor_2_out);
  not not_4 (nPD2, nor_3_out);
  not not_5 (nPD3, nor_4_out);
  not not_6 (nPD4, nor_5_out);
  not not_7 (nPD5, nor_6_out);
  not not_8 (nPD6, nor_7_out);
  not not_9 (nPD7, nor_8_out);
  and and_1 (and_1_out, nIMPLIED, not_1_out);
  nor nor_13 (nTWOCYCLE, and_1_out, nor_11_out, nor_12_out);
endmodule
