// Digital circuit RANDOM_LOGIC.dig as structural Verilog
module RANDOM_LOGIC (
  input  X0,
  input  X1,
  input  X2,
  input  X3,
  input  X4,
  input  X5,
  input  X6,
  input  X7,
  input  X8,
  input  X9,
  input  X10,
  input  X11,
  input  X12,
  input  X13,
  input  X14,
  input  X15,
  input  X16,
  input  X17,
  input  X18,
  input  X19,
  input  X20,
  input  X21,
  input  X22,
  input  X23,
  input  X24,
  input  X25,
  input  X26,
  input  X27,
  input  X28,
  input  X29,
  input  X30,
  input  X31,
  input  X32,
  input  X33,
  input  X34,
  input  X35,
  input  X36,
  input  X37,
  input  X38,
  input  X39,
  input  X40,
  input  X41,
  input  X42,
  input  X43,
  input  X44,
  input  X45,
  input  X46,
  input  X47,
  input  X48,
  input  X49,
  input  X50,
  input  X51,
  input  X52,
  input  X53,
  input  X54,
  input  X55,
  input  X56,
  input  X57,
  input  X58,
  input  X59,
  input  X60,
  input  X61,
  input  X62,
  input  X63,
  input  X64,
  input  X65,
  input  X66,
  input  X67,
  input  X68,
  input  X69,
  input  X70,
  input  X71,
  input  X72,
  input  X73,
  input  X74,
  input  X75,
  input  X76,
  input  X77,
  input  X78,
  input  X79,
  input  X80,
  input  X81,
  input  X82,
  input  X83,
  input  X84,
  input  X85,
  input  X86,
  input  X87,
  input  X88,
  input  X89,
  input  X90,
  input  X91,
  input  X92,
  input  X93,
  input  X94,
  input  X95,
  input  X96,
  input  X97,
  input  X98,
  input  X99,
  input  X100,
  input  X101,
  input  X102,
  input  X103,
  input  X104,
  input  X105,
  input  X106,
  input  X107,
  input  X108,
  input  X109,
  input  X110,
  input  X111,
  input  X112,
  input  X113,
  input  X114,
  input  X115,
  input  X116,
  input  X117,
  input  X118,
  input  X119,
  input  X120,
  input  X121,
  input  X122,
  input  X123,
  input  X124,
  input  X125,
  input  X126,
  input  X127,
  input  X128,
  input  X129
);

  wire undriven, undriven_2, undriven_3, undriven_4, undriven_5, undriven_6, undriven_7, undriven_8,
       undriven_9, undriven_10, undriven_11, undriven_12, undriven_13, undriven_14, undriven_15, undriven_16,
       undriven_17, undriven_18, undriven_19, undriven_20, undriven_21, undriven_22, undriven_23,
       undriven_24, undriven_25, undriven_26, undriven_27, undriven_28;

  REGS_CONTROL regs_control_1 (
    .D0(X0), .D1(X1), .D2(X2), .D3(X3), .D4(X4), .D5(X5), .D6(X6), .D7(X7), .D8(X8), .D9(X9), .D10(X10),
    .D11(X11), .D12(X12), .D13(X13), .D14(X14), .D15(X15), .D16(X16), .D17(X17), .D18(X18), .D19(X19),
    .D20(X20), .D21(X21), .D22(X22), .D23(X23), .D24(X24), .D25(X25), .D26(X26), .D35(X35), .D48(X48));  // open: PHI1, PHI2, STOR, nready, Y_SB, STXY, X_SB, S_SB, SB_X, nSBXY, SB_Y, SB_S, S_S, STKOP, S_ADL
  ALU_SETUP alu_setup_1 (
    .D26(undriven), .D27(undriven_2), .D29(undriven_3), .D30(undriven_4), .D31(undriven_5), .D32(undriven_6),
    .D33(undriven_7), .D34(undriven_8), .D35(undriven_9), .D36(undriven_10), .D37(undriven_11),
    .D38(undriven_12), .D39(undriven_13), .D40(undriven_14), .D41(undriven_15), .D42(undriven_16),
    .D43(undriven_17), .D44(undriven_18), .D45(undriven_19), .D47(undriven_20), .D48(undriven_21),
    .D49(undriven_22), .D50(undriven_23), .D51(undriven_24), .D52(undriven_25), .D53(undriven_26),
    .D54(undriven_27), .D56(undriven_28), .D69(X69), .D70(X70), .D75(X75), .D76(X76), .D84(X84), .D85(X85),
    .D86(X86), .D87(X87), .D88(X88), .D89(X89));  // open: PHI1, PHI2, BR3, BRK6E, STKOP, T0, T1, T6, T7, nC_OUT, nD_OUT, nready, BRFW, PGX, AND, INC_SB, SR, NDB_ADD, DB_ADD, Z_ADD, SB_ADD, ADL_ADD, ANDS, EORS, ORS, nACIN, SUMS, nDAA, ADD_SB7, ADD_SB06, ADD_ADL, nDSA, SRS
  // BUS_CONTROL bus_control_1: pin names not known; wires that end beside it: X45, X47, X48, X49, X55, X56, X57, X58, X59, X60, X61
  DispatchUnit dispatchunit_1 ();  // open: PHI1, PHI2, RDY, DORES, RESP, BRFW, nBRTAKEN, ACR, nIMPLIED, nTWOCYCLE, B_OUT, nADL_PCL, BRK6E, PC_DB, dec2, nready, WR, T0, T1, nT0, nT1X, T6, T7, ACRL2, TRES2, nIPC, STOR, Z_IR, FETCH
endmodule
