// Digital circuit REGS_BIT.dig as structural Verilog
module REGS_BIT (
  input  PHI2,
  input  Y_SB,
  input  SB_Y,
  input  X_SB,
  input  SB_X,
  input  S_ADL,
  input  S_S,
  input  SB_S,
  input  S_SB,
  input  SBx_in,
  input  in_16,
  input  in_17,
  input  in_18,
  input  in_19,
  output SBx_out,
  output ADLx,
  output Y,
  output X,
  output S
);

  wire and_1_out, and_2_out, dlatch_1_nq, multiplexer_1_out, not_1_out, not_2_out, not_3_out;

  not not_1 (not_1_out, PHI2);
  not not_2 (not_2_out, PHI2);
  not not_3 (not_3_out, PHI2);
  and and_1 (and_1_out, not_1_out, SB_Y);
  and and_2 (and_2_out, not_2_out, SB_X);
  Multiplexer multiplexer_1 (.sel(SB_S), .in_0(S), .in_1(SBx_in), .out(multiplexer_1_out));
  DFF_Level dff_level_1 (.Q(Y), .EN(and_1_out), .D(SBx_in));  // open: nQ
  DFF_Level dff_level_2 (.Q(X), .EN(and_2_out), .D(SBx_in));  // open: nQ
  DLATCH dlatch_1 (.C(not_3_out), .D(multiplexer_1_out), .nQ(dlatch_1_nq));  // open: Q
  DLATCH dlatch_2 (.C(PHI2), .D(dlatch_1_nq), .nQ(S));  // open: Q
  assign SBx_out = Y_SB ? Y : 1'bz;  // Driver driver_1
  assign SBx_out = X_SB ? X : 1'bz;  // Driver driver_2
  assign SBx_out = S_SB ? S : 1'bz;  // Driver driver_3
  assign ADLx = S_ADL ? S : 1'bz;  // Driver driver_4

  // Notes on the sheet:
  //   unused
endmodule
