// Digital circuit REGS_CONTROL.dig as structural Verilog
module REGS_CONTROL (
  input  PHI1,
  input  PHI2,
  input  STOR,
  input  nready,
  input  D0,
  input  D1,
  input  D2,
  input  D3,
  input  D4,
  input  D5,
  input  D6,
  input  D7,
  input  D8,
  input  D9,
  input  D10,
  input  D11,
  input  D12,
  input  D13,
  input  D14,
  input  D15,
  input  D16,
  input  D17,
  input  D18,
  input  D19,
  input  D20,
  input  D21,
  input  D22,
  input  D23,
  input  D24,
  input  D25,
  input  D26,
  input  D35,
  input  D48,
  output Y_SB,
  output STXY,
  output X_SB,
  output S_SB,
  output SB_X,
  output nSBXY,
  output SB_Y,
  output SB_S,
  output S_S,
  output STKOP,
  output S_ADL
);

  wire and_1_out, and_2_out, and_3_out, and_4_out, and_5_out, and_6_out, and_7_out, dlatch_1_nq, dlatch_1_q,
       dlatch_2_q, dlatch_3_nq, dlatch_3_q, dlatch_4_nq, dlatch_5_q, dlatch_6_q, dlatch_7_q, dlatch_8_q,
       dlatch_9_nq, nor_1_out, nor_2_out, nor_3_out, nor_4_out, nor_5_out, nor_6_out, nor_8_out, nor_9_out,
       nor_11_out, nor_12_out, nor_13_out, nor_14_out, nor_15_out, nor_16_out, not_1_out, not_2_out,
       not_3_out, not_4_out;

  nor nor_1 (nor_1_out, D14, D15, D16);
  not not_1 (not_1_out, D17);
  nor nor_2 (nor_2_out, D18, D19, D20);
  not not_2 (not_2_out, D7);
  nor nor_3 (nor_3_out, D21, D22, D23, D24, D25, D26);
  not not_3 (not_3_out, D48);
  and and_1 (and_1_out, D6, D7);
  and and_2 (and_2_out, D6, not_2_out);
  DLATCH dlatch_1 (.C(PHI1), .D(nready), .Q(dlatch_1_q), .nQ(dlatch_1_nq));
  nor nor_4 (nor_4_out, not_3_out, nready);
  and and_3 (and_3_out, STOR, D0);
  and and_4 (and_4_out, STOR, D12);
  nor nor_5 (nor_5_out, D1, D2, D3, D4, D5, and_1_out, and_3_out);
  nor nor_6 (nor_6_out, and_4_out, and_2_out, D8, D9, D10, D11, D13);
  and and_5 (and_5_out, D21, dlatch_1_nq);
  nor nor_7 (STKOP, nor_3_out, dlatch_1_q);
  nor nor_8 (nor_8_out, D13, nor_4_out, STKOP);
  nor nor_9 (nor_9_out, and_5_out, D35);
  and and_6 (and_6_out, STOR, D0);
  and and_7 (and_7_out, STOR, D12);
  nand nand_1 (nSBXY, nor_1_out, nor_2_out);
  not not_4 (not_4_out, nor_8_out);
  DLATCH dlatch_2 (.C(PHI2), .D(nor_5_out), .Q(dlatch_2_q));  // open: nQ
  nor nor_10 (STXY, and_6_out, and_7_out);
  DLATCH dlatch_3 (.C(PHI2), .D(nor_6_out), .Q(dlatch_3_q), .nQ(dlatch_3_nq));
  DLATCH dlatch_4 (.C(PHI2), .D(not_1_out), .nQ(dlatch_4_nq));  // open: Q
  DLATCH dlatch_5 (.C(PHI2), .D(nor_1_out), .Q(dlatch_5_q));  // open: nQ
  DLATCH dlatch_6 (.C(PHI2), .D(nor_2_out), .Q(dlatch_6_q));  // open: nQ
  DLATCH dlatch_7 (.C(PHI2), .D(nor_8_out), .Q(dlatch_7_q));  // open: nQ
  DLATCH dlatch_8 (.C(PHI2), .D(not_4_out), .Q(dlatch_8_q));  // open: nQ
  DLATCH dlatch_9 (.C(PHI2), .D(nor_9_out), .nQ(dlatch_9_nq));  // open: Q
  nor nor_11 (nor_11_out, dlatch_2_q, PHI2);
  nor nor_12 (nor_12_out, dlatch_3_q, dlatch_3_nq);
  nor nor_13 (nor_13_out, dlatch_5_q, PHI2);
  nor nor_14 (nor_14_out, dlatch_6_q, PHI2);
  nor nor_15 (nor_15_out, dlatch_7_q, PHI2);
  nor nor_16 (nor_16_out, dlatch_8_q, PHI2);
  assign S_SB = 1'b1 ? dlatch_4_nq : 1'bz;  // Driver driver_1
  assign Y_SB = 1'b1 ? nor_11_out : 1'bz;  // Driver driver_2
  assign X_SB = 1'b1 ? nor_12_out : 1'bz;  // Driver driver_3
  assign SB_X = 1'b1 ? nor_13_out : 1'bz;  // Driver driver_4
  assign SB_Y = 1'b1 ? nor_14_out : 1'bz;  // Driver driver_5
  assign SB_S = 1'b1 ? nor_15_out : 1'bz;  // Driver driver_6
  assign S_S = 1'b1 ? nor_16_out : 1'bz;  // Driver driver_7
  assign S_ADL = 1'b1 ? dlatch_9_nq : 1'bz;  // Driver driver_8
endmodule
